// Logisim project 多级中断.circ as structural Verilog: 31 circuits, main circuit ◇单周期MIPS
module \单周期MIPS  (
);

  wire and_1_out, and_2_out, and_3_out, and_4_out, and_5_out, and_6_out, and_7_out, CLK, d_ff_1_q, EQ, Go,
       Halt, JAL, mips_alu_1_equal, not_1_out, not_2_out, RST, SignedExt, Syscall, \无条件分支 , \条件分支 ,
       \硬布线控制器_1_alu_src , \硬布线控制器_1_beq , \硬布线控制器_1_bne , \硬布线控制器_1_jr , \硬布线控制器_1_memtoreg ,
       \硬布线控制器_1_memwrite , \硬布线控制器_1_regdst , \硬布线控制器_1_regwrite ;
  wire [3:0] \硬布线控制器_1_alu_op ;
  wire [4:0] multiplexer_3_out, multiplexer_4_out, multiplexer_6_out, multiplexer_7_out;
  wire [15:0] \总周期数 , \无条件分支数 , \条件分支成功数 ;
  wire [31:0] adder_1_out, adder_2_out, bit_extender_1_out, bit_extender_2_out, LedData, mips_alu_1_result,
       mips_regifile_1_r1, multiplexer_1_out, multiplexer_2_out, multiplexer_5_out, multiplexer_8_out,
       multiplexer_9_out, PC_q, ram_1_data, rom_1_data, v0;

  Button \u_总复位  (.out(RST));
  Button \u_继续运行  (.out(Go));
  Clock clock_1 (.out(CLK));
  Multiplexer #(.width(32), .enable("false")) multiplexer_1 (
    .in0(bit_extender_1_out), .in1(mips_regifile_1_r1), .out(multiplexer_1_out), .sel(\硬布线控制器_1_jr ));
  Hex_Digit_Display hex_digit_display_1 (.value(LedData[27:24]));  // open: dp
  Hex_Digit_Display hex_digit_display_2 (.value(LedData[31:28]));  // open: dp
  or or_1 (\条件分支 , and_7_out, and_6_out);
  Multiplexer #(.select(2), .width(32), .enable("false")) multiplexer_2 (
    .in0(adder_1_out), .in1(adder_2_out), .in2(multiplexer_1_out), .out(multiplexer_2_out),
    .sel({\无条件分支 , \条件分支 }));  // open: in3
  Hex_Digit_Display hex_digit_display_3 (.value(LedData[19:16]));  // open: dp
  Hex_Digit_Display hex_digit_display_4 (.value(LedData[23:20]));  // open: dp
  and and_1 (and_1_out, Halt, \无条件分支 );
  Register #(.width(32)) PC (.D(multiplexer_2_out), .en(Halt), .Q(PC_q), .clk(CLK), .clr(RST));
  Hex_Digit_Display hex_digit_display_5 (.value(LedData[15:12]));  // open: dp
  Hex_Digit_Display hex_digit_display_6 (.value(LedData[11:8]));  // open: dp
  Counter #(.width(16), .max('hffff)) counter_1 (
    .count(Halt), .Q(\总周期数 ), .clk(CLK), .clr(RST));  // open: load, D, carry
  Counter #(.width(16), .max('hffff)) counter_2 (
    .count(and_1_out), .Q(\无条件分支数 ), .clk(CLK), .clr(RST));  // open: load, D, carry
  Adder #(.width(32)) adder_1 (.a(PC_q), .b(32'h1), .out(adder_1_out));  // open: cin, cout
  Hex_Digit_Display hex_digit_display_7 (.value(LedData[7:4]));  // open: dp
  Hex_Digit_Display hex_digit_display_8 (.value(LedData[3:0]));  // open: dp
  assign bit_extender_1_out = {{6{rom_1_data[25]}}, rom_1_data[25:0]};  // Bit_Extender bit_extender_1
  // Probe on bit_extender_1_out
  and and_2 (and_2_out, Halt, \条件分支 );
  ROM #(.addrWidth(10), .dataWidth(32)) rom_1 (.addr(PC_q[9:0]), .data(rom_1_data));  // open: sel
  Counter #(.width(16), .max('hffff)) counter_3 (
    .count(and_2_out), .Q(\条件分支成功数 ), .clk(CLK), .clr(RST));  // open: load, D, carry
  \硬布线控制器  \u_硬布线控制器_1  (
    .Func(rom_1_data[5:0]), .OP(rom_1_data[31:26]), .ALU_OP(\硬布线控制器_1_alu_op ),
    .MemToReg(\硬布线控制器_1_memtoreg ), .MemWrite(\硬布线控制器_1_memwrite ), .ALU_SRC(\硬布线控制器_1_alu_src ),
    .RegWrite(\硬布线控制器_1_regwrite ), .SysCALL(Syscall), .SignedExt(SignedExt), .RegDst(\硬布线控制器_1_regdst ),
    .JR(\硬布线控制器_1_jr ), .JMP(\无条件分支 ), .Beq(\硬布线控制器_1_beq ), .JAL(JAL), .Bne(\硬布线控制器_1_bne ));  // open: LUI, LH, BLTZ
  Multiplexer #(.width(5), .enable("false")) multiplexer_3 (
    .in0(rom_1_data[20:16]), .in1(rom_1_data[15:11]), .out(multiplexer_3_out), .sel(\硬布线控制器_1_regdst ));
  and and_3 (and_3_out, rom_1_data[15], SignedExt);
  assign bit_extender_2_out = {{16{and_3_out}}, rom_1_data[15:0]};  // Bit_Extender bit_extender_2
  // Probe on \总周期数 
  // Probe on \无条件分支数 
  // Probe on \条件分支成功数 
  Register #(.width(32)) register_1 (.D(v0), .en(and_4_out), .Q(LedData), .clk(CLK));  // open: clr
  and and_4 (and_4_out, EQ, Syscall);
  Multiplexer #(.width(5), .enable("false")) multiplexer_4 (
    .in0(multiplexer_3_out), .in1({5{1'b1}}), .out(multiplexer_4_out), .sel(JAL));
  Multiplexer #(.width(32), .enable("false")) multiplexer_5 (
    .in0(multiplexer_9_out), .in1(adder_1_out), .out(multiplexer_5_out), .sel(JAL));
  Multiplexer #(.width(5), .enable("false")) multiplexer_6 (
    .in0(rom_1_data[25:21]), .in1(5'b00010), .out(multiplexer_6_out), .sel(Syscall));
  Multiplexer #(.width(5), .enable("false")) multiplexer_7 (
    .in0(rom_1_data[20:16]), .in1(5'b00100), .out(multiplexer_7_out), .sel(Syscall));
  MIPS_Regifile mips_regifile_1 (
    .Din(multiplexer_5_out), .Clk(CLK), .R1(mips_regifile_1_r1), .R2(v0), .WE(\硬布线控制器_1_regwrite ),
    .W_num(multiplexer_4_out), .R1_num(multiplexer_6_out), .R2_num(multiplexer_7_out));
  Comparator #(.width(32), .mode("unsigned")) comparator_1 (
    .a(32'h22), .b(mips_regifile_1_r1), .eq(EQ));  // open: gt, lt
  not not_1 (not_1_out, EQ);
  and and_5 (and_5_out, not_1_out, Syscall);
  Multiplexer #(.width(32), .enable("false")) multiplexer_8 (
    .in0(v0), .in1(bit_extender_2_out), .out(multiplexer_8_out), .sel(\硬布线控制器_1_alu_src ));
  Adder #(.width(32)) adder_2 (.a(bit_extender_2_out), .b(adder_1_out), .out(adder_2_out));  // open: cin, cout
  D_Flip_Flop #(.trigger("high")) d_ff_1 (
    .clk(CLK), .D(and_5_out), .Q(d_ff_1_q), .en(Syscall), .reset(Go));  // open: Qn, preset
  and and_6 (and_6_out, mips_alu_1_equal, \硬布线控制器_1_beq );
  not not_2 (not_2_out, mips_alu_1_equal);
  and and_7 (and_7_out, not_2_out, \硬布线控制器_1_bne );
  MIPS_ALU mips_alu_1 (
    .X(mips_regifile_1_r1), .Y(multiplexer_8_out), .AluOP(\硬布线控制器_1_alu_op ), .Equal(mips_alu_1_equal),
    .Result(mips_alu_1_result), .shamt(rom_1_data[10:6]));  // open: Result_2
  not not_3 (Halt, d_ff_1_q);
  RAM #(.addrWidth(10), .dataWidth(32), .bus("separate")) ram_1 (
    .addr(mips_alu_1_result[11:2]), .din(v0), .data(ram_1_data), .str(\硬布线控制器_1_memwrite ), .clk(CLK),
    .ld(\硬布线控制器_1_memtoreg ), .clr(RST));  // open: sel
  Multiplexer #(.width(32), .enable("false")) multiplexer_9 (
    .in0(mips_alu_1_result), .in1(ram_1_data), .out(multiplexer_9_out), .sel(\硬布线控制器_1_memtoreg ));

  // Notes on the sheet:
  //   数码管输出应该用寄存器锁存，否则显示数据只能一闪而过
  //   可以通过项目增加Logisim库的方式将前几次实验完成的电路作为子电路引入到本电路中使用
  //   数码管输出
  //   指令存储器
  //   contents of rom_1 (hex, n*v repeats v):
  //   20110005 8100006 20110001 20120002 20130003 20140004 810000b 20110001 20120002 20130003 20140004
  //   8100010 20110001 20120002 20130003 20140004 8100015 20110001 20120002 20130003 20140004 810001a
  //   20110001 20120002 20130003 20140004 810001f 20110001 20120002 20130003 20140004 8100029 20110001
  //   20120002 20130003 20140004 8100029 20110001 20120002 20130003 20140004 2231ffff 1620ffe0 20100001
  //   201200ff 20110001 20130003 12120005 12100004 20110001 20120002 20130003 20140004 16310004 16320003
  //   20110001 20120002 20130003 c10003d 2002000a c 20100000 22100001 102020 20020022 c 3e00008
  //   JMP
  //   JR
  //   Op
  //   Func
  //   rs
  //   rt
  //   rd
  //   总复位信号应将除ROM以外所有存储组件全部清零
  //   Beq
  //   Bne
  //   MemToReg
  //   MemWrite
  //   AluOP
  //   AluSrcB
  //   RegWrite
  //   JAL
  //   RegDst
  //   v0
  //   a0
endmodule

// 单周期硬布线控制器
module \硬布线控制器  (
  input  [5:0] OP,
  input  [5:0] Func,
  output [3:0] ALU_OP,
  output MemToReg,
  output MemWrite,
  output ALU_SRC,
  output RegWrite,
  output SysCALL,
  output SignedExt,
  output RegDst,
  output Beq,
  output Bne,
  output JR,
  output JMP,
  output JAL,
  output LUI,
  output LH,
  output BLTZ
);

  // Probe on OP
  \运算控制器  \u_运算控制器_1  (
    .OP0(OP[0]), .OP1(OP[1]), .OP2(OP[2]), .OP3(OP[3]), .OP4(OP[4]), .OP5(OP[5]), .F0(Func[0]), .F1(Func[1]),
    .F2(Func[2]), .F3(Func[3]), .F4(Func[4]), .F5(Func[5]), .S0(ALU_OP[0]), .S1(ALU_OP[1]), .S2(ALU_OP[2]),
    .S3(ALU_OP[3]));
  \控制信号生成  \u_控制信号生成_1  (
    .OP0(OP[0]), .OP1(OP[1]), .OP2(OP[2]), .OP3(OP[3]), .OP4(OP[4]), .OP5(OP[5]), .F0(Func[0]), .F1(Func[1]),
    .F2(Func[2]), .F3(Func[3]), .F4(Func[4]), .F5(Func[5]), .MemToReg(MemToReg), .MemWrite(MemWrite),
    .ALU_SRC(ALU_SRC), .RegWrite(RegWrite), .SysCALL(SysCALL), .SignedExt(SignedExt), .RegDst(RegDst),
    .BEQ(Beq), .BNE(Bne), .JR(JR), .JMP(JMP), .JAL(JAL));
  \拓展指令信号  \u_拓展指令信号_1  (
    .OP0(OP[0]), .OP1(OP[1]), .OP2(OP[2]), .OP3(OP[3]), .OP4(OP[4]), .OP5(OP[5]), .F0(Func[0]), .F1(Func[1]),
    .F2(Func[2]), .F3(Func[3]), .F4(Func[4]), .F5(Func[5]), .LUI(LUI), .LH(LH), .BLTZ(BLTZ));
  // Probe on Func
  // Probe on ALU_OP

  // Other names for the same wires on the sheet: OP_CODE[5:0] = OP

  // Notes on the sheet:
  //   运算器控制器，根据指令生成运算器功能选择信号
  //   控制信号生成，产生数据通路需要的其他控制信号
endmodule

// 运算器控制器
module \运算控制器  (
  input  OP0,
  input  OP1,
  input  OP2,
  input  OP3,
  input  OP4,
  input  OP5,
  input  F0,
  input  F1,
  input  F2,
  input  F3,
  input  F4,
  input  F5,
  output S0,
  output S1,
  output S2,
  output S3
);

  wire and_1_out, and_2_out, and_3_out, and_4_out, and_5_out, and_6_out, and_7_out, and_8_out, and_9_out,
       and_10_out, and_11_out, and_12_out, and_13_out, and_14_out, and_15_out, and_16_out, and_17_out,
       and_18_out, and_19_out, and_20_out, and_21_out, and_22_out, and_23_out, and_24_out, and_25_out,
       and_26_out, and_27_out, and_28_out, and_29_out, and_30_out, and_31_out, and_32_out, and_33_out,
       and_34_out, and_35_out, and_36_out, and_37_out, and_38_out, and_39_out, and_40_out, and_41_out,
       not_1_out, not_2_out, not_3_out, not_4_out, not_5_out, not_6_out, not_7_out, not_8_out, not_9_out,
       not_10_out, not_11_out, not_12_out, not_13_out, not_14_out, not_15_out, not_16_out, not_17_out,
       not_18_out, not_19_out, not_20_out, not_21_out, not_22_out, not_23_out, not_24_out, not_25_out,
       not_26_out, not_27_out, not_28_out, not_29_out, not_30_out, not_31_out, not_32_out, not_33_out,
       not_34_out, not_35_out, not_36_out, not_37_out, not_38_out, not_39_out, not_40_out, not_41_out,
       not_42_out, not_43_out, not_44_out, not_45_out, not_46_out, not_47_out, not_48_out, not_49_out,
       not_50_out, not_51_out, not_52_out, not_53_out, not_54_out, not_55_out, not_56_out, not_57_out,
       not_58_out, not_59_out, not_60_out, not_61_out, not_62_out, not_63_out, not_64_out, not_65_out,
       not_66_out, not_67_out, not_68_out, not_69_out, not_70_out, not_71_out, not_72_out, not_73_out,
       not_74_out, not_75_out, not_76_out, not_77_out, not_78_out, not_79_out, not_80_out, not_81_out,
       not_82_out, not_83_out, not_84_out, not_85_out, not_86_out, not_87_out, not_88_out, not_89_out,
       not_90_out, not_91_out, not_92_out, not_93_out, not_94_out, not_95_out, not_96_out, not_97_out,
       not_98_out, not_99_out, not_100_out, not_101_out, not_102_out, not_103_out, not_104_out, not_105_out,
       not_106_out, not_107_out, not_108_out, not_109_out, not_110_out, not_111_out, not_112_out,
       not_113_out, not_114_out, not_115_out, not_116_out, not_117_out, not_118_out, not_119_out,
       not_120_out, not_121_out, not_122_out, not_123_out, not_124_out, not_125_out, not_126_out,
       not_127_out, not_128_out, not_129_out, not_130_out, not_131_out, not_132_out, not_133_out,
       not_134_out, not_135_out, not_136_out, not_137_out, not_138_out, not_139_out, not_140_out,
       not_141_out, not_142_out, not_143_out, not_144_out, not_145_out, not_146_out, not_147_out,
       not_148_out, not_149_out, not_150_out, not_151_out, not_152_out, not_153_out, not_154_out,
       not_155_out, not_156_out, not_157_out, not_158_out, not_159_out, not_160_out, not_161_out,
       not_162_out, not_163_out, not_164_out, not_165_out, not_166_out, not_167_out, not_168_out,
       not_169_out, not_170_out, not_171_out, not_172_out, not_173_out, not_174_out, not_175_out,
       not_176_out, not_177_out, not_178_out, not_179_out, not_180_out, not_181_out, not_182_out,
       not_183_out, not_184_out, not_185_out, not_186_out, not_187_out, not_188_out, not_189_out,
       not_190_out, not_191_out, not_192_out, not_193_out, not_194_out, not_195_out, not_196_out,
       not_197_out, not_198_out, not_199_out, not_200_out, not_201_out, not_202_out, not_203_out,
       not_204_out, not_205_out, not_206_out, not_207_out, not_208_out, not_209_out, not_210_out,
       not_211_out, not_212_out, not_213_out, not_214_out, not_215_out, not_216_out, not_217_out,
       not_218_out, not_219_out, not_220_out, not_221_out, not_222_out, not_223_out, not_224_out,
       not_225_out, not_226_out, not_227_out, not_228_out, not_229_out, not_230_out, not_231_out,
       not_232_out, not_233_out, not_234_out, not_235_out, not_236_out, not_237_out, not_238_out,
       not_239_out, not_240_out, not_241_out, not_242_out, not_243_out, not_244_out, not_245_out,
       not_246_out, not_247_out, not_248_out, not_249_out, not_250_out, not_251_out, not_252_out,
       not_253_out, not_254_out, not_255_out, not_256_out, not_257_out, not_258_out, not_259_out,
       not_260_out, not_261_out, not_262_out, not_263_out, not_264_out, not_265_out, not_266_out,
       not_267_out, not_268_out, not_269_out, not_270_out, not_271_out, not_272_out, not_273_out,
       not_274_out, not_275_out, not_276_out, not_277_out;

  not not_1 (not_1_out, OP5);
  not not_2 (not_2_out, OP4);
  not not_3 (not_3_out, OP3);
  not not_4 (not_4_out, OP2);
  not not_5 (not_5_out, OP1);
  not not_6 (not_6_out, OP0);
  not not_7 (not_7_out, F5);
  not not_8 (not_8_out, F4);
  not not_9 (not_9_out, F3);
  not not_10 (not_10_out, F2);
  not not_11 (not_11_out, OP5);
  not not_12 (not_12_out, OP4);
  not not_13 (not_13_out, OP3);
  not not_14 (not_14_out, OP2);
  not not_15 (not_15_out, OP1);
  not not_16 (not_16_out, OP0);
  not not_17 (not_17_out, F4);
  not not_18 (not_18_out, F3);
  not not_19 (not_19_out, F2);
  not not_20 (not_20_out, F1);
  not not_21 (not_21_out, F0);
  not not_22 (not_22_out, OP5);
  not not_23 (not_23_out, OP4);
  not not_24 (not_24_out, OP3);
  not not_25 (not_25_out, OP2);
  not not_26 (not_26_out, OP1);
  not not_27 (not_27_out, OP0);
  not not_28 (not_28_out, F4);
  not not_29 (not_29_out, F3);
  not not_30 (not_30_out, F2);
  not not_31 (not_31_out, F1);
  not not_32 (not_32_out, OP5);
  not not_33 (not_33_out, OP4);
  not not_34 (not_34_out, OP3);
  not not_35 (not_35_out, OP2);
  not not_36 (not_36_out, OP1);
  not not_37 (not_37_out, OP0);
  not not_38 (not_38_out, F4);
  not not_39 (not_39_out, F3);
  not not_40 (not_40_out, F1);
  not not_41 (not_41_out, F0);
  not not_42 (not_42_out, OP5);
  not not_43 (not_43_out, OP4);
  not not_44 (not_44_out, OP3);
  not not_45 (not_45_out, OP2);
  not not_46 (not_46_out, OP1);
  not not_47 (not_47_out, OP0);
  not not_48 (not_48_out, F4);
  not not_49 (not_49_out, F2);
  not not_50 (not_50_out, F0);
  not not_51 (not_51_out, OP5);
  not not_52 (not_52_out, OP4);
  not not_53 (not_53_out, OP2);
  not not_54 (not_54_out, OP1);
  not not_55 (not_55_out, OP0);
  not not_56 (not_56_out, OP5);
  not not_57 (not_57_out, OP4);
  not not_58 (not_58_out, OP1);
  not not_59 (not_59_out, OP0);
  not not_60 (not_60_out, OP5);
  not not_61 (not_61_out, OP4);
  not not_62 (not_62_out, OP2);
  not not_63 (not_63_out, OP1);
  not not_64 (not_64_out, OP5);
  not not_65 (not_65_out, OP4);
  not not_66 (not_66_out, OP2);
  not not_67 (not_67_out, OP0);
  not not_68 (not_68_out, OP4);
  not not_69 (not_69_out, OP3);
  not not_70 (not_70_out, OP2);
  not not_71 (not_71_out, OP4);
  not not_72 (not_72_out, OP2);
  not not_73 (not_73_out, OP5);
  not not_74 (not_74_out, OP4);
  not not_75 (not_75_out, OP3);
  not not_76 (not_76_out, OP2);
  not not_77 (not_77_out, OP1);
  not not_78 (not_78_out, OP0);
  not not_79 (not_79_out, F4);
  not not_80 (not_80_out, F3);
  not not_81 (not_81_out, F0);
  not not_82 (not_82_out, OP4);
  not not_83 (not_83_out, OP3);
  not not_84 (not_84_out, OP2);
  not not_85 (not_85_out, OP1);
  not not_86 (not_86_out, OP5);
  not not_87 (not_87_out, OP4);
  not not_88 (not_88_out, OP3);
  not not_89 (not_89_out, OP2);
  not not_90 (not_90_out, OP1);
  not not_91 (not_91_out, OP5);
  not not_92 (not_92_out, OP4);
  not not_93 (not_93_out, OP3);
  not not_94 (not_94_out, OP2);
  not not_95 (not_95_out, OP1);
  not not_96 (not_96_out, OP0);
  not not_97 (not_97_out, F5);
  not not_98 (not_98_out, F4);
  not not_99 (not_99_out, F3);
  not not_100 (not_100_out, F2);
  not not_101 (not_101_out, F0);
  not not_102 (not_102_out, OP5);
  not not_103 (not_103_out, OP4);
  not not_104 (not_104_out, OP3);
  not not_105 (not_105_out, OP2);
  not not_106 (not_106_out, OP1);
  not not_107 (not_107_out, OP0);
  not not_108 (not_108_out, F4);
  not not_109 (not_109_out, F3);
  not not_110 (not_110_out, F2);
  not not_111 (not_111_out, F0);
  not not_112 (not_112_out, OP5);
  not not_113 (not_113_out, OP4);
  not not_114 (not_114_out, OP3);
  not not_115 (not_115_out, OP2);
  not not_116 (not_116_out, OP1);
  not not_117 (not_117_out, OP0);
  not not_118 (not_118_out, F4);
  not not_119 (not_119_out, F3);
  not not_120 (not_120_out, F1);
  not not_121 (not_121_out, F0);
  not not_122 (not_122_out, OP5);
  not not_123 (not_123_out, OP4);
  not not_124 (not_124_out, OP3);
  not not_125 (not_125_out, OP2);
  not not_126 (not_126_out, OP1);
  not not_127 (not_127_out, OP0);
  not not_128 (not_128_out, F4);
  not not_129 (not_129_out, F3);
  not not_130 (not_130_out, OP5);
  not not_131 (not_131_out, OP4);
  not not_132 (not_132_out, OP3);
  not not_133 (not_133_out, OP2);
  not not_134 (not_134_out, OP1);
  not not_135 (not_135_out, OP0);
  not not_136 (not_136_out, F4);
  not not_137 (not_137_out, F2);
  not not_138 (not_138_out, F0);
  not not_139 (not_139_out, OP5);
  not not_140 (not_140_out, OP4);
  not not_141 (not_141_out, OP1);
  not not_142 (not_142_out, OP0);
  not not_143 (not_143_out, OP5);
  not not_144 (not_144_out, OP4);
  not not_145 (not_145_out, OP2);
  not not_146 (not_146_out, OP0);
  not not_147 (not_147_out, OP5);
  not not_148 (not_148_out, OP4);
  not not_149 (not_149_out, OP3);
  not not_150 (not_150_out, OP2);
  not not_151 (not_151_out, OP1);
  not not_152 (not_152_out, OP5);
  not not_153 (not_153_out, OP4);
  not not_154 (not_154_out, OP3);
  not not_155 (not_155_out, OP2);
  not not_156 (not_156_out, OP1);
  not not_157 (not_157_out, OP0);
  not not_158 (not_158_out, F4);
  not not_159 (not_159_out, F3);
  not not_160 (not_160_out, F2);
  not not_161 (not_161_out, F1);
  not not_162 (not_162_out, F0);
  not not_163 (not_163_out, OP5);
  not not_164 (not_164_out, OP4);
  not not_165 (not_165_out, OP3);
  not not_166 (not_166_out, OP2);
  not not_167 (not_167_out, OP1);
  not not_168 (not_168_out, OP0);
  not not_169 (not_169_out, F4);
  not not_170 (not_170_out, F3);
  not not_171 (not_171_out, F2);
  not not_172 (not_172_out, F1);
  not not_173 (not_173_out, OP5);
  not not_174 (not_174_out, OP4);
  not not_175 (not_175_out, OP3);
  not not_176 (not_176_out, OP2);
  not not_177 (not_177_out, OP1);
  not not_178 (not_178_out, OP0);
  not not_179 (not_179_out, F4);
  not not_180 (not_180_out, F3);
  not not_181 (not_181_out, F2);
  not not_182 (not_182_out, F0);
  not not_183 (not_183_out, OP5);
  not not_184 (not_184_out, OP4);
  not not_185 (not_185_out, OP3);
  not not_186 (not_186_out, OP2);
  not not_187 (not_187_out, OP1);
  not not_188 (not_188_out, OP0);
  not not_189 (not_189_out, F4);
  not not_190 (not_190_out, F3);
  not not_191 (not_191_out, F1);
  not not_192 (not_192_out, F0);
  not not_193 (not_193_out, OP5);
  not not_194 (not_194_out, OP4);
  not not_195 (not_195_out, OP3);
  not not_196 (not_196_out, OP2);
  not not_197 (not_197_out, OP1);
  not not_198 (not_198_out, OP0);
  not not_199 (not_199_out, F4);
  not not_200 (not_200_out, F2);
  not not_201 (not_201_out, OP5);
  not not_202 (not_202_out, OP4);
  not not_203 (not_203_out, OP2);
  not not_204 (not_204_out, OP1);
  not not_205 (not_205_out, OP0);
  not not_206 (not_206_out, OP5);
  not not_207 (not_207_out, OP4);
  not not_208 (not_208_out, OP1);
  not not_209 (not_209_out, OP0);
  not not_210 (not_210_out, OP5);
  not not_211 (not_211_out, OP4);
  not not_212 (not_212_out, OP2);
  not not_213 (not_213_out, OP1);
  not not_214 (not_214_out, OP4);
  not not_215 (not_215_out, OP3);
  not not_216 (not_216_out, OP2);
  not not_217 (not_217_out, OP4);
  not not_218 (not_218_out, OP2);
  not not_219 (not_219_out, OP4);
  not not_220 (not_220_out, OP3);
  not not_221 (not_221_out, OP2);
  not not_222 (not_222_out, OP1);
  not not_223 (not_223_out, OP5);
  not not_224 (not_224_out, OP4);
  not not_225 (not_225_out, OP3);
  not not_226 (not_226_out, OP2);
  not not_227 (not_227_out, OP1);
  not not_228 (not_228_out, OP0);
  not not_229 (not_229_out, F4);
  not not_230 (not_230_out, F3);
  not not_231 (not_231_out, F1);
  not not_232 (not_232_out, OP5);
  not not_233 (not_233_out, OP4);
  not not_234 (not_234_out, OP3);
  not not_235 (not_235_out, OP2);
  not not_236 (not_236_out, OP1);
  not not_237 (not_237_out, OP0);
  not not_238 (not_238_out, F4);
  not not_239 (not_239_out, F3);
  not not_240 (not_240_out, OP5);
  not not_241 (not_241_out, OP4);
  not not_242 (not_242_out, OP3);
  not not_243 (not_243_out, OP2);
  not not_244 (not_244_out, OP1);
  not not_245 (not_245_out, OP0);
  not not_246 (not_246_out, F4);
  not not_247 (not_247_out, F2);
  not not_248 (not_248_out, F0);
  not not_249 (not_249_out, OP5);
  not not_250 (not_250_out, OP4);
  not not_251 (not_251_out, OP3);
  not not_252 (not_252_out, OP2);
  not not_253 (not_253_out, OP1);
  not not_254 (not_254_out, OP0);
  not not_255 (not_255_out, F4);
  not not_256 (not_256_out, F2);
  not not_257 (not_257_out, OP5);
  not not_258 (not_258_out, OP4);
  not not_259 (not_259_out, OP2);
  not not_260 (not_260_out, OP0);
  not not_261 (not_261_out, OP5);
  not not_262 (not_262_out, OP4);
  not not_263 (not_263_out, OP1);
  not not_264 (not_264_out, OP5);
  not not_265 (not_265_out, OP4);
  not not_266 (not_266_out, OP3);
  not not_267 (not_267_out, OP2);
  not not_268 (not_268_out, OP1);
  not not_269 (not_269_out, OP0);
  not not_270 (not_270_out, F4);
  not not_271 (not_271_out, F3);
  not not_272 (not_272_out, F0);
  not not_273 (not_273_out, OP5);
  not not_274 (not_274_out, OP4);
  not not_275 (not_275_out, OP3);
  not not_276 (not_276_out, OP2);
  not not_277 (not_277_out, OP1);
  and and_1 (and_1_out, not_1_out, not_2_out, not_3_out, not_4_out, not_5_out, not_6_out, not_7_out, not_8_out, not_9_out, not_10_out, F1, F0);
  and and_2 (and_2_out, not_11_out, not_12_out, not_13_out, not_14_out, not_15_out, not_16_out, F5, not_17_out, not_18_out, not_19_out, not_20_out, not_21_out);
  and and_3 (and_3_out, not_22_out, not_23_out, not_24_out, not_25_out, not_26_out, not_27_out, F5, not_28_out, not_29_out, not_30_out, not_31_out, F0);
  and and_4 (and_4_out, not_32_out, not_33_out, not_34_out, not_35_out, not_36_out, not_37_out, F5, not_38_out, not_39_out, F2, not_40_out, not_41_out);
  and and_5 (and_5_out, not_42_out, not_43_out, not_44_out, not_45_out, not_46_out, not_47_out, F5, not_48_out, F3, not_49_out, F1, not_50_out);
  and and_6 (and_6_out, not_51_out, not_52_out, OP3, not_53_out, not_54_out, not_55_out);
  and and_7 (and_7_out, not_56_out, not_57_out, OP3, OP2, not_58_out, not_59_out);
  and and_8 (and_8_out, not_60_out, not_61_out, OP3, not_62_out, not_63_out, OP0);
  and and_9 (and_9_out, not_64_out, not_65_out, OP3, not_66_out, OP1, not_67_out);
  and and_10 (and_10_out, OP5, not_68_out, not_69_out, not_70_out, OP1, OP0);
  and and_11 (and_11_out, OP5, not_71_out, OP3, not_72_out, OP1, OP0);
  and and_12 (and_12_out, not_73_out, not_74_out, not_75_out, not_76_out, not_77_out, not_78_out, F5, not_79_out, not_80_out, F2, F1, not_81_out);
  and and_13 (and_13_out, OP5, not_82_out, not_83_out, not_84_out, not_85_out, OP0);
  and and_14 (and_14_out, not_86_out, not_87_out, not_88_out, not_89_out, not_90_out, OP0);
  and and_15 (and_15_out, not_91_out, not_92_out, not_93_out, not_94_out, not_95_out, not_96_out, not_97_out, not_98_out, not_99_out, not_100_out, F1, not_101_out);
  and and_16 (and_16_out, not_102_out, not_103_out, not_104_out, not_105_out, not_106_out, not_107_out, F5, not_108_out, not_109_out, not_110_out, F1, not_111_out);
  and and_17 (and_17_out, not_112_out, not_113_out, not_114_out, not_115_out, not_116_out, not_117_out, F5, not_118_out, not_119_out, F2, not_120_out, not_121_out);
  and and_18 (and_18_out, not_122_out, not_123_out, not_124_out, not_125_out, not_126_out, not_127_out, F5, not_128_out, not_129_out, F2, F1, F0);
  and and_19 (and_19_out, not_130_out, not_131_out, not_132_out, not_133_out, not_134_out, not_135_out, F5, not_136_out, F3, not_137_out, F1, not_138_out);
  and and_20 (and_20_out, not_139_out, not_140_out, OP3, OP2, not_141_out, not_142_out);
  and and_21 (and_21_out, not_143_out, not_144_out, OP3, not_145_out, OP1, not_146_out);
  and and_22 (and_22_out, not_147_out, not_148_out, not_149_out, not_150_out, not_151_out, OP0);
  and and_23 (and_23_out, not_152_out, not_153_out, not_154_out, not_155_out, not_156_out, not_157_out, F5, not_158_out, not_159_out, not_160_out, not_161_out, not_162_out);
  and and_24 (and_24_out, not_163_out, not_164_out, not_165_out, not_166_out, not_167_out, not_168_out, F5, not_169_out, not_170_out, not_171_out, not_172_out, F0);
  and and_25 (and_25_out, not_173_out, not_174_out, not_175_out, not_176_out, not_177_out, not_178_out, F5, not_179_out, not_180_out, not_181_out, F1, not_182_out);
  and and_26 (and_26_out, not_183_out, not_184_out, not_185_out, not_186_out, not_187_out, not_188_out, F5, not_189_out, not_190_out, F2, not_191_out, not_192_out);
  and and_27 (and_27_out, not_193_out, not_194_out, not_195_out, not_196_out, not_197_out, not_198_out, F5, not_199_out, F3, not_200_out, F1, F0);
  and and_28 (and_28_out, not_201_out, not_202_out, OP3, not_203_out, not_204_out, not_205_out);
  and and_29 (and_29_out, not_206_out, not_207_out, OP3, OP2, not_208_out, not_209_out);
  and and_30 (and_30_out, not_210_out, not_211_out, OP3, not_212_out, not_213_out, OP0);
  and and_31 (and_31_out, OP5, not_214_out, not_215_out, not_216_out, OP1, OP0);
  and and_32 (and_32_out, OP5, not_217_out, OP3, not_218_out, OP1, OP0);
  and and_33 (and_33_out, OP5, not_219_out, not_220_out, not_221_out, not_222_out, OP0);
  and and_34 (and_34_out, not_223_out, not_224_out, not_225_out, not_226_out, not_227_out, not_228_out, F5, not_229_out, not_230_out, F2, not_231_out, F0);
  and and_35 (and_35_out, not_232_out, not_233_out, not_234_out, not_235_out, not_236_out, not_237_out, F5, not_238_out, not_239_out, F2, F1, F0);
  and and_36 (and_36_out, not_240_out, not_241_out, not_242_out, not_243_out, not_244_out, not_245_out, F5, not_246_out, F3, not_247_out, F1, not_248_out);
  and and_37 (and_37_out, not_249_out, not_250_out, not_251_out, not_252_out, not_253_out, not_254_out, F5, not_255_out, F3, not_256_out, F1, F0);
  and and_38 (and_38_out, not_257_out, not_258_out, OP3, not_259_out, OP1, not_260_out);
  and and_39 (and_39_out, not_261_out, not_262_out, OP3, OP2, not_263_out, OP0);
  and and_40 (and_40_out, not_264_out, not_265_out, not_266_out, not_267_out, not_268_out, not_269_out, F5, not_270_out, not_271_out, F2, F1, not_272_out);
  and and_41 (and_41_out, not_273_out, not_274_out, not_275_out, not_276_out, not_277_out, OP0);
  or or_1 (S1, and_15_out, and_16_out, and_17_out, and_18_out, and_19_out, and_20_out, and_21_out, and_22_out);
  or or_2 (S2, and_23_out, and_24_out, and_25_out, and_26_out, and_27_out, and_28_out, and_29_out, and_30_out, and_31_out, and_32_out, and_33_out);
  or or_3 (S3, and_34_out, and_35_out, and_36_out, and_37_out, and_38_out, and_39_out, and_40_out, and_41_out);
  or or_4 (S0, and_1_out, and_2_out, and_3_out, and_4_out, and_5_out, and_6_out, and_7_out, and_8_out, and_9_out, and_10_out, and_11_out, and_12_out, and_13_out, and_14_out);
endmodule

// 控制信号生成
module \控制信号生成  (
  input  OP0,
  input  OP1,
  input  OP2,
  input  OP3,
  input  OP4,
  input  OP5,
  input  F0,
  input  F1,
  input  F2,
  input  F3,
  input  F4,
  input  F5,
  output MemToReg,
  output MemWrite,
  output ALU_SRC,
  output RegWrite,
  output SysCALL,
  output SignedExt,
  output RegDst,
  output BEQ,
  output BNE,
  output JR,
  output JMP,
  output JAL
);

  wire and_1_out, and_2_out, and_4_out, and_5_out, and_6_out, and_7_out, and_8_out, and_9_out, and_10_out,
       and_11_out, and_12_out, and_13_out, and_14_out, and_15_out, and_16_out, and_17_out, and_18_out,
       and_19_out, and_20_out, and_21_out, and_22_out, and_23_out, and_24_out, and_25_out, and_26_out,
       and_27_out, and_28_out, and_29_out, and_30_out, and_31_out, and_32_out, and_33_out, and_35_out,
       and_36_out, and_37_out, and_38_out, and_39_out, and_40_out, and_41_out, and_42_out, and_43_out,
       and_44_out, and_45_out, and_46_out, and_47_out, and_48_out, and_49_out, and_53_out, and_54_out,
       and_55_out, not_1_out, not_2_out, not_3_out, not_4_out, not_5_out, not_6_out, not_7_out, not_8_out,
       not_9_out, not_10_out, not_11_out, not_12_out, not_13_out, not_14_out, not_15_out, not_16_out,
       not_17_out, not_18_out, not_19_out, not_20_out, not_21_out, not_22_out, not_23_out, not_24_out,
       not_25_out, not_26_out, not_27_out, not_28_out, not_29_out, not_30_out, not_31_out, not_32_out,
       not_33_out, not_34_out, not_35_out, not_36_out, not_37_out, not_38_out, not_39_out, not_40_out,
       not_41_out, not_42_out, not_43_out, not_44_out, not_45_out, not_46_out, not_47_out, not_48_out,
       not_49_out, not_50_out, not_51_out, not_52_out, not_53_out, not_54_out, not_55_out, not_56_out,
       not_57_out, not_58_out, not_59_out, not_60_out, not_61_out, not_62_out, not_63_out, not_64_out,
       not_65_out, not_66_out, not_67_out, not_68_out, not_69_out, not_70_out, not_71_out, not_72_out,
       not_73_out, not_74_out, not_75_out, not_76_out, not_77_out, not_78_out, not_79_out, not_80_out,
       not_81_out, not_82_out, not_83_out, not_84_out, not_85_out, not_86_out, not_87_out, not_88_out,
       not_89_out, not_90_out, not_91_out, not_92_out, not_93_out, not_94_out, not_95_out, not_96_out,
       not_97_out, not_98_out, not_99_out, not_100_out, not_101_out, not_102_out, not_103_out, not_104_out,
       not_105_out, not_106_out, not_107_out, not_108_out, not_109_out, not_110_out, not_111_out,
       not_112_out, not_113_out, not_114_out, not_115_out, not_116_out, not_117_out, not_118_out,
       not_119_out, not_120_out, not_121_out, not_122_out, not_123_out, not_124_out, not_125_out,
       not_126_out, not_127_out, not_128_out, not_129_out, not_130_out, not_131_out, not_132_out,
       not_133_out, not_134_out, not_135_out, not_136_out, not_137_out, not_138_out, not_139_out,
       not_140_out, not_141_out, not_142_out, not_143_out, not_144_out, not_145_out, not_146_out,
       not_147_out, not_148_out, not_149_out, not_150_out, not_151_out, not_152_out, not_153_out,
       not_154_out, not_155_out, not_156_out, not_157_out, not_158_out, not_159_out, not_160_out,
       not_161_out, not_162_out, not_163_out, not_164_out, not_165_out, not_166_out, not_167_out,
       not_168_out, not_169_out, not_170_out, not_171_out, not_172_out, not_173_out, not_174_out,
       not_175_out, not_176_out, not_177_out, not_178_out, not_179_out, not_180_out, not_181_out,
       not_182_out, not_183_out, not_184_out, not_185_out, not_186_out, not_187_out, not_188_out,
       not_189_out, not_190_out, not_191_out, not_192_out, not_193_out, not_194_out, not_195_out,
       not_196_out, not_197_out, not_198_out, not_199_out, not_200_out, not_201_out, not_202_out,
       not_203_out, not_204_out, not_205_out, not_206_out, not_207_out, not_208_out, not_209_out,
       not_210_out, not_211_out, not_212_out, not_213_out, not_214_out, not_215_out, not_216_out,
       not_217_out, not_218_out, not_219_out, not_220_out, not_221_out, not_222_out, not_223_out,
       not_224_out, not_225_out, not_226_out, not_227_out, not_228_out, not_229_out, not_230_out,
       not_231_out, not_232_out, not_233_out, not_234_out, not_235_out, not_236_out, not_237_out,
       not_238_out, not_239_out, not_240_out, not_241_out, not_242_out, not_243_out, not_244_out,
       not_245_out, not_246_out, not_247_out, not_248_out, not_249_out, not_250_out, not_251_out,
       not_252_out, not_253_out, not_254_out, not_255_out, not_256_out, not_257_out, not_258_out,
       not_259_out, not_260_out, not_261_out, not_262_out, not_263_out, not_264_out, not_265_out,
       not_266_out, not_267_out, not_268_out, not_269_out, not_270_out, not_271_out, not_272_out,
       not_273_out, not_274_out, not_275_out, not_276_out, not_277_out, not_278_out, not_279_out,
       not_280_out, not_281_out, not_282_out, not_283_out, not_284_out, not_285_out, not_286_out,
       not_287_out, not_288_out, not_289_out, not_290_out, not_291_out, not_292_out, not_293_out,
       not_294_out, not_295_out, not_296_out, not_297_out, not_298_out, not_299_out, not_300_out,
       not_301_out, not_302_out, not_303_out, not_304_out, not_305_out, not_306_out, not_307_out,
       not_308_out, not_309_out, not_310_out, not_311_out, not_312_out, not_313_out, not_314_out,
       not_315_out, not_316_out, not_317_out, not_318_out, not_319_out, not_320_out, not_321_out,
       not_322_out, not_323_out, not_324_out, not_325_out, not_326_out, not_327_out, not_328_out,
       not_329_out, not_330_out, not_331_out, not_332_out, not_333_out, not_334_out, not_335_out,
       not_336_out, not_337_out, not_338_out, not_339_out, not_340_out, not_341_out, not_342_out,
       not_343_out, not_344_out, not_345_out, not_346_out, not_347_out, not_348_out, not_349_out,
       not_350_out, not_351_out, not_352_out, not_353_out, not_354_out, not_355_out, not_356_out,
       not_357_out, not_358_out, not_359_out, not_360_out, not_361_out, not_362_out, not_363_out,
       not_364_out, not_365_out, not_366_out, not_367_out, not_368_out, not_369_out, not_370_out,
       not_371_out, not_372_out, not_373_out, not_374_out, not_375_out, not_376_out, not_377_out,
       not_378_out, not_379_out, not_380_out, not_381_out, not_382_out, not_383_out, not_384_out,
       not_385_out, not_386_out, not_387_out, not_388_out, not_389_out, not_390_out;

  not not_1 (not_1_out, OP4);
  not not_2 (not_2_out, OP3);
  not not_3 (not_3_out, OP2);
  not not_4 (not_4_out, OP4);
  not not_5 (not_5_out, OP3);
  not not_6 (not_6_out, OP2);
  not not_7 (not_7_out, OP1);
  not not_8 (not_8_out, OP4);
  not not_9 (not_9_out, OP2);
  not not_10 (not_10_out, OP5);
  not not_11 (not_11_out, OP4);
  not not_12 (not_12_out, OP2);
  not not_13 (not_13_out, OP1);
  not not_14 (not_14_out, OP0);
  not not_15 (not_15_out, OP5);
  not not_16 (not_16_out, OP4);
  not not_17 (not_17_out, OP1);
  not not_18 (not_18_out, OP0);
  not not_19 (not_19_out, OP5);
  not not_20 (not_20_out, OP4);
  not not_21 (not_21_out, OP2);
  not not_22 (not_22_out, OP1);
  not not_23 (not_23_out, OP5);
  not not_24 (not_24_out, OP4);
  not not_25 (not_25_out, OP2);
  not not_26 (not_26_out, OP0);
  not not_27 (not_27_out, OP5);
  not not_28 (not_28_out, OP4);
  not not_29 (not_29_out, OP1);
  not not_30 (not_30_out, OP4);
  not not_31 (not_31_out, OP3);
  not not_32 (not_32_out, OP2);
  not not_33 (not_33_out, OP4);
  not not_34 (not_34_out, OP2);
  not not_35 (not_35_out, OP4);
  not not_36 (not_36_out, OP3);
  not not_37 (not_37_out, OP2);
  not not_38 (not_38_out, OP1);
  not not_39 (not_39_out, OP5);
  not not_40 (not_40_out, OP4);
  not not_41 (not_41_out, OP3);
  not not_42 (not_42_out, OP2);
  not not_43 (not_43_out, OP1);
  not not_44 (not_44_out, OP0);
  not not_45 (not_45_out, F5);
  not not_46 (not_46_out, F4);
  not not_47 (not_47_out, F3);
  not not_48 (not_48_out, F2);
  not not_49 (not_49_out, F1);
  not not_50 (not_50_out, F0);
  not not_51 (not_51_out, OP5);
  not not_52 (not_52_out, OP4);
  not not_53 (not_53_out, OP3);
  not not_54 (not_54_out, OP2);
  not not_55 (not_55_out, OP1);
  not not_56 (not_56_out, OP0);
  not not_57 (not_57_out, F5);
  not not_58 (not_58_out, F4);
  not not_59 (not_59_out, F3);
  not not_60 (not_60_out, F2);
  not not_61 (not_61_out, OP5);
  not not_62 (not_62_out, OP4);
  not not_63 (not_63_out, OP3);
  not not_64 (not_64_out, OP2);
  not not_65 (not_65_out, OP1);
  not not_66 (not_66_out, OP0);
  not not_67 (not_67_out, F5);
  not not_68 (not_68_out, F4);
  not not_69 (not_69_out, F3);
  not not_70 (not_70_out, F2);
  not not_71 (not_71_out, F0);
  not not_72 (not_72_out, OP5);
  not not_73 (not_73_out, OP4);
  not not_74 (not_74_out, OP3);
  not not_75 (not_75_out, OP2);
  not not_76 (not_76_out, OP1);
  not not_77 (not_77_out, OP0);
  not not_78 (not_78_out, F4);
  not not_79 (not_79_out, F3);
  not not_80 (not_80_out, F2);
  not not_81 (not_81_out, F1);
  not not_82 (not_82_out, F0);
  not not_83 (not_83_out, OP5);
  not not_84 (not_84_out, OP4);
  not not_85 (not_85_out, OP3);
  not not_86 (not_86_out, OP2);
  not not_87 (not_87_out, OP1);
  not not_88 (not_88_out, OP0);
  not not_89 (not_89_out, F4);
  not not_90 (not_90_out, F3);
  not not_91 (not_91_out, F2);
  not not_92 (not_92_out, F1);
  not not_93 (not_93_out, OP5);
  not not_94 (not_94_out, OP4);
  not not_95 (not_95_out, OP3);
  not not_96 (not_96_out, OP2);
  not not_97 (not_97_out, OP1);
  not not_98 (not_98_out, OP0);
  not not_99 (not_99_out, F4);
  not not_100 (not_100_out, F3);
  not not_101 (not_101_out, F2);
  not not_102 (not_102_out, F0);
  not not_103 (not_103_out, OP5);
  not not_104 (not_104_out, OP4);
  not not_105 (not_105_out, OP3);
  not not_106 (not_106_out, OP2);
  not not_107 (not_107_out, OP1);
  not not_108 (not_108_out, OP0);
  not not_109 (not_109_out, F4);
  not not_110 (not_110_out, F3);
  not not_111 (not_111_out, F1);
  not not_112 (not_112_out, F0);
  not not_113 (not_113_out, OP5);
  not not_114 (not_114_out, OP4);
  not not_115 (not_115_out, OP3);
  not not_116 (not_116_out, OP2);
  not not_117 (not_117_out, OP1);
  not not_118 (not_118_out, OP0);
  not not_119 (not_119_out, F4);
  not not_120 (not_120_out, F3);
  not not_121 (not_121_out, F1);
  not not_122 (not_122_out, OP5);
  not not_123 (not_123_out, OP4);
  not not_124 (not_124_out, OP3);
  not not_125 (not_125_out, OP2);
  not not_126 (not_126_out, OP1);
  not not_127 (not_127_out, OP0);
  not not_128 (not_128_out, F4);
  not not_129 (not_129_out, F3);
  not not_130 (not_130_out, OP5);
  not not_131 (not_131_out, OP4);
  not not_132 (not_132_out, OP3);
  not not_133 (not_133_out, OP2);
  not not_134 (not_134_out, OP1);
  not not_135 (not_135_out, OP0);
  not not_136 (not_136_out, F4);
  not not_137 (not_137_out, F2);
  not not_138 (not_138_out, F0);
  not not_139 (not_139_out, OP5);
  not not_140 (not_140_out, OP4);
  not not_141 (not_141_out, OP3);
  not not_142 (not_142_out, OP2);
  not not_143 (not_143_out, OP1);
  not not_144 (not_144_out, OP0);
  not not_145 (not_145_out, F4);
  not not_146 (not_146_out, F2);
  not not_147 (not_147_out, OP5);
  not not_148 (not_148_out, OP4);
  not not_149 (not_149_out, OP3);
  not not_150 (not_150_out, OP2);
  not not_151 (not_151_out, OP1);
  not not_152 (not_152_out, OP0);
  not not_153 (not_153_out, F5);
  not not_154 (not_154_out, F4);
  not not_155 (not_155_out, F2);
  not not_156 (not_156_out, F1);
  not not_157 (not_157_out, F0);
  not not_158 (not_158_out, OP5);
  not not_159 (not_159_out, OP4);
  not not_160 (not_160_out, OP3);
  not not_161 (not_161_out, OP2);
  not not_162 (not_162_out, OP5);
  not not_163 (not_163_out, OP4);
  not not_164 (not_164_out, OP2);
  not not_165 (not_165_out, OP1);
  not not_166 (not_166_out, OP0);
  not not_167 (not_167_out, OP5);
  not not_168 (not_168_out, OP4);
  not not_169 (not_169_out, OP1);
  not not_170 (not_170_out, OP0);
  not not_171 (not_171_out, OP5);
  not not_172 (not_172_out, OP4);
  not not_173 (not_173_out, OP2);
  not not_174 (not_174_out, OP1);
  not not_175 (not_175_out, OP5);
  not not_176 (not_176_out, OP4);
  not not_177 (not_177_out, OP2);
  not not_178 (not_178_out, OP0);
  not not_179 (not_179_out, OP5);
  not not_180 (not_180_out, OP4);
  not not_181 (not_181_out, OP1);
  not not_182 (not_182_out, OP4);
  not not_183 (not_183_out, OP3);
  not not_184 (not_184_out, OP2);
  not not_185 (not_185_out, OP5);
  not not_186 (not_186_out, OP4);
  not not_187 (not_187_out, OP3);
  not not_188 (not_188_out, OP2);
  not not_189 (not_189_out, OP1);
  not not_190 (not_190_out, OP0);
  not not_191 (not_191_out, F4);
  not not_192 (not_192_out, F3);
  not not_193 (not_193_out, F0);
  not not_194 (not_194_out, OP5);
  not not_195 (not_195_out, OP4);
  not not_196 (not_196_out, OP4);
  not not_197 (not_197_out, OP3);
  not not_198 (not_198_out, OP2);
  not not_199 (not_199_out, OP1);
  not not_200 (not_200_out, OP5);
  not not_201 (not_201_out, OP4);
  not not_202 (not_202_out, OP3);
  not not_203 (not_203_out, OP2);
  not not_204 (not_204_out, OP1);
  not not_205 (not_205_out, OP0);
  not not_206 (not_206_out, F5);
  not not_207 (not_207_out, F4);
  not not_208 (not_208_out, F1);
  not not_209 (not_209_out, F0);
  not not_210 (not_210_out, OP5);
  not not_211 (not_211_out, OP4);
  not not_212 (not_212_out, OP2);
  not not_213 (not_213_out, OP1);
  not not_214 (not_214_out, OP0);
  not not_215 (not_215_out, OP5);
  not not_216 (not_216_out, OP4);
  not not_217 (not_217_out, OP2);
  not not_218 (not_218_out, OP0);
  not not_219 (not_219_out, OP5);
  not not_220 (not_220_out, OP4);
  not not_221 (not_221_out, OP3);
  not not_222 (not_222_out, OP2);
  not not_223 (not_223_out, OP1);
  not not_224 (not_224_out, OP0);
  not not_225 (not_225_out, F5);
  not not_226 (not_226_out, F4);
  not not_227 (not_227_out, F3);
  not not_228 (not_228_out, F2);
  not not_229 (not_229_out, F1);
  not not_230 (not_230_out, F0);
  not not_231 (not_231_out, OP5);
  not not_232 (not_232_out, OP4);
  not not_233 (not_233_out, OP3);
  not not_234 (not_234_out, OP2);
  not not_235 (not_235_out, OP1);
  not not_236 (not_236_out, OP0);
  not not_237 (not_237_out, F5);
  not not_238 (not_238_out, F4);
  not not_239 (not_239_out, F3);
  not not_240 (not_240_out, F2);
  not not_241 (not_241_out, OP5);
  not not_242 (not_242_out, OP4);
  not not_243 (not_243_out, OP3);
  not not_244 (not_244_out, OP2);
  not not_245 (not_245_out, OP1);
  not not_246 (not_246_out, OP0);
  not not_247 (not_247_out, F5);
  not not_248 (not_248_out, F4);
  not not_249 (not_249_out, F3);
  not not_250 (not_250_out, F2);
  not not_251 (not_251_out, F0);
  not not_252 (not_252_out, OP5);
  not not_253 (not_253_out, OP4);
  not not_254 (not_254_out, OP3);
  not not_255 (not_255_out, OP2);
  not not_256 (not_256_out, OP1);
  not not_257 (not_257_out, OP0);
  not not_258 (not_258_out, F4);
  not not_259 (not_259_out, F3);
  not not_260 (not_260_out, F2);
  not not_261 (not_261_out, F1);
  not not_262 (not_262_out, F0);
  not not_263 (not_263_out, OP5);
  not not_264 (not_264_out, OP4);
  not not_265 (not_265_out, OP3);
  not not_266 (not_266_out, OP2);
  not not_267 (not_267_out, OP1);
  not not_268 (not_268_out, OP0);
  not not_269 (not_269_out, F4);
  not not_270 (not_270_out, F3);
  not not_271 (not_271_out, F2);
  not not_272 (not_272_out, F1);
  not not_273 (not_273_out, OP5);
  not not_274 (not_274_out, OP4);
  not not_275 (not_275_out, OP3);
  not not_276 (not_276_out, OP2);
  not not_277 (not_277_out, OP1);
  not not_278 (not_278_out, OP0);
  not not_279 (not_279_out, F4);
  not not_280 (not_280_out, F3);
  not not_281 (not_281_out, F2);
  not not_282 (not_282_out, F0);
  not not_283 (not_283_out, OP5);
  not not_284 (not_284_out, OP4);
  not not_285 (not_285_out, OP3);
  not not_286 (not_286_out, OP2);
  not not_287 (not_287_out, OP1);
  not not_288 (not_288_out, OP0);
  not not_289 (not_289_out, F4);
  not not_290 (not_290_out, F3);
  not not_291 (not_291_out, F1);
  not not_292 (not_292_out, F0);
  not not_293 (not_293_out, OP5);
  not not_294 (not_294_out, OP4);
  not not_295 (not_295_out, OP3);
  not not_296 (not_296_out, OP2);
  not not_297 (not_297_out, OP1);
  not not_298 (not_298_out, OP0);
  not not_299 (not_299_out, F4);
  not not_300 (not_300_out, F3);
  not not_301 (not_301_out, F1);
  not not_302 (not_302_out, OP5);
  not not_303 (not_303_out, OP4);
  not not_304 (not_304_out, OP3);
  not not_305 (not_305_out, OP2);
  not not_306 (not_306_out, OP1);
  not not_307 (not_307_out, OP0);
  not not_308 (not_308_out, F4);
  not not_309 (not_309_out, F3);
  not not_310 (not_310_out, OP5);
  not not_311 (not_311_out, OP4);
  not not_312 (not_312_out, OP3);
  not not_313 (not_313_out, OP2);
  not not_314 (not_314_out, OP1);
  not not_315 (not_315_out, OP0);
  not not_316 (not_316_out, F4);
  not not_317 (not_317_out, F2);
  not not_318 (not_318_out, F0);
  not not_319 (not_319_out, OP5);
  not not_320 (not_320_out, OP4);
  not not_321 (not_321_out, OP3);
  not not_322 (not_322_out, OP2);
  not not_323 (not_323_out, OP1);
  not not_324 (not_324_out, OP0);
  not not_325 (not_325_out, F4);
  not not_326 (not_326_out, F2);
  not not_327 (not_327_out, OP5);
  not not_328 (not_328_out, OP4);
  not not_329 (not_329_out, OP3);
  not not_330 (not_330_out, OP2);
  not not_331 (not_331_out, OP1);
  not not_332 (not_332_out, OP0);
  not not_333 (not_333_out, F5);
  not not_334 (not_334_out, F4);
  not not_335 (not_335_out, F2);
  not not_336 (not_336_out, F1);
  not not_337 (not_337_out, F0);
  not not_338 (not_338_out, OP5);
  not not_339 (not_339_out, OP4);
  not not_340 (not_340_out, OP3);
  not not_341 (not_341_out, OP2);
  not not_342 (not_342_out, OP1);
  not not_343 (not_343_out, OP0);
  not not_344 (not_344_out, F4);
  not not_345 (not_345_out, F3);
  not not_346 (not_346_out, F0);
  not not_347 (not_347_out, OP5);
  not not_348 (not_348_out, OP4);
  not not_349 (not_349_out, OP3);
  not not_350 (not_350_out, OP1);
  not not_351 (not_351_out, OP0);
  not not_352 (not_352_out, OP5);
  not not_353 (not_353_out, OP4);
  not not_354 (not_354_out, OP3);
  not not_355 (not_355_out, OP1);
  not not_356 (not_356_out, OP5);
  not not_357 (not_357_out, OP4);
  not not_358 (not_358_out, OP3);
  not not_359 (not_359_out, OP2);
  not not_360 (not_360_out, OP1);
  not not_361 (not_361_out, OP0);
  not not_362 (not_362_out, F5);
  not not_363 (not_363_out, F4);
  not not_364 (not_364_out, F2);
  not not_365 (not_365_out, F1);
  not not_366 (not_366_out, F0);
  not not_367 (not_367_out, OP5);
  not not_368 (not_368_out, OP4);
  not not_369 (not_369_out, OP3);
  not not_370 (not_370_out, OP2);
  not not_371 (not_371_out, OP1);
  not not_372 (not_372_out, OP0);
  not not_373 (not_373_out, F5);
  not not_374 (not_374_out, F4);
  not not_375 (not_375_out, F2);
  not not_376 (not_376_out, F1);
  not not_377 (not_377_out, F0);
  not not_378 (not_378_out, OP5);
  not not_379 (not_379_out, OP4);
  not not_380 (not_380_out, OP3);
  not not_381 (not_381_out, OP2);
  not not_382 (not_382_out, OP0);
  not not_383 (not_383_out, OP5);
  not not_384 (not_384_out, OP4);
  not not_385 (not_385_out, OP3);
  not not_386 (not_386_out, OP2);
  not not_387 (not_387_out, OP5);
  not not_388 (not_388_out, OP4);
  not not_389 (not_389_out, OP3);
  not not_390 (not_390_out, OP2);
  and and_1 (and_1_out, OP5, not_1_out, not_2_out, not_3_out, OP1, OP0);
  and and_2 (and_2_out, OP5, not_4_out, not_5_out, not_6_out, not_7_out, OP0);
  and and_3 (MemWrite, OP5, not_8_out, OP3, not_9_out, OP1, OP0);
  and and_4 (and_4_out, not_10_out, not_11_out, OP3, not_12_out, not_13_out, not_14_out);
  and and_5 (and_5_out, not_15_out, not_16_out, OP3, OP2, not_17_out, not_18_out);
  and and_6 (and_6_out, not_19_out, not_20_out, OP3, not_21_out, not_22_out, OP0);
  and and_7 (and_7_out, not_23_out, not_24_out, OP3, not_25_out, OP1, not_26_out);
  and and_8 (and_8_out, not_27_out, not_28_out, OP3, OP2, not_29_out, OP0);
  and and_9 (and_9_out, OP5, not_30_out, not_31_out, not_32_out, OP1, OP0);
  and and_10 (and_10_out, OP5, not_33_out, OP3, not_34_out, OP1, OP0);
  and and_11 (and_11_out, OP5, not_35_out, not_36_out, not_37_out, not_38_out, OP0);
  and and_12 (and_12_out, not_39_out, not_40_out, not_41_out, not_42_out, not_43_out, not_44_out, not_45_out, not_46_out, not_47_out, not_48_out, not_49_out, not_50_out);
  and and_13 (and_13_out, not_51_out, not_52_out, not_53_out, not_54_out, not_55_out, not_56_out, not_57_out, not_58_out, not_59_out, not_60_out, F1, F0);
  and and_14 (and_14_out, not_61_out, not_62_out, not_63_out, not_64_out, not_65_out, not_66_out, not_67_out, not_68_out, not_69_out, not_70_out, F1, not_71_out);
  and and_15 (and_15_out, not_72_out, not_73_out, not_74_out, not_75_out, not_76_out, not_77_out, F5, not_78_out, not_79_out, not_80_out, not_81_out, not_82_out);
  and and_16 (and_16_out, not_83_out, not_84_out, not_85_out, not_86_out, not_87_out, not_88_out, F5, not_89_out, not_90_out, not_91_out, not_92_out, F0);
  and and_17 (and_17_out, not_93_out, not_94_out, not_95_out, not_96_out, not_97_out, not_98_out, F5, not_99_out, not_100_out, not_101_out, F1, not_102_out);
  and and_18 (and_18_out, not_103_out, not_104_out, not_105_out, not_106_out, not_107_out, not_108_out, F5, not_109_out, not_110_out, F2, not_111_out, not_112_out);
  and and_19 (and_19_out, not_113_out, not_114_out, not_115_out, not_116_out, not_117_out, not_118_out, F5, not_119_out, not_120_out, F2, not_121_out, F0);
  and and_20 (and_20_out, not_122_out, not_123_out, not_124_out, not_125_out, not_126_out, not_127_out, F5, not_128_out, not_129_out, F2, F1, F0);
  and and_21 (and_21_out, not_130_out, not_131_out, not_132_out, not_133_out, not_134_out, not_135_out, F5, not_136_out, F3, not_137_out, F1, not_138_out);
  and and_22 (and_22_out, not_139_out, not_140_out, not_141_out, not_142_out, not_143_out, not_144_out, F5, not_145_out, F3, not_146_out, F1, F0);
  and and_23 (and_23_out, not_147_out, not_148_out, not_149_out, not_150_out, not_151_out, not_152_out, not_153_out, not_154_out, F3, not_155_out, not_156_out, not_157_out);
  and and_24 (and_24_out, not_158_out, not_159_out, not_160_out, not_161_out, OP1, OP0);
  and and_25 (and_25_out, not_162_out, not_163_out, OP3, not_164_out, not_165_out, not_166_out);
  and and_26 (and_26_out, not_167_out, not_168_out, OP3, OP2, not_169_out, not_170_out);
  and and_27 (and_27_out, not_171_out, not_172_out, OP3, not_173_out, not_174_out, OP0);
  and and_28 (and_28_out, not_175_out, not_176_out, OP3, not_177_out, OP1, not_178_out);
  and and_29 (and_29_out, not_179_out, not_180_out, OP3, OP2, not_181_out, OP0);
  and and_30 (and_30_out, OP5, not_182_out, not_183_out, not_184_out, OP1, OP0);
  and and_31 (and_31_out, not_185_out, not_186_out, not_187_out, not_188_out, not_189_out, not_190_out, F5, not_191_out, not_192_out, F2, F1, not_193_out);
  and and_32 (and_32_out, not_194_out, not_195_out, OP3, OP2, OP1, OP0);
  and and_33 (and_33_out, OP5, not_196_out, not_197_out, not_198_out, not_199_out, OP0);
  and and_34 (SysCALL, not_200_out, not_201_out, not_202_out, not_203_out, not_204_out, not_205_out, not_206_out, not_207_out, F3, F2, not_208_out, not_209_out);
  and and_35 (and_35_out, not_210_out, not_211_out, OP3, not_212_out, not_213_out, not_214_out);
  and and_36 (and_36_out, not_215_out, not_216_out, OP3, not_217_out, OP1, not_218_out);
  and and_37 (and_37_out, not_219_out, not_220_out, not_221_out, not_222_out, not_223_out, not_224_out, not_225_out, not_226_out, not_227_out, not_228_out, not_229_out, not_230_out);
  and and_38 (and_38_out, not_231_out, not_232_out, not_233_out, not_234_out, not_235_out, not_236_out, not_237_out, not_238_out, not_239_out, not_240_out, F1, F0);
  and and_39 (and_39_out, not_241_out, not_242_out, not_243_out, not_244_out, not_245_out, not_246_out, not_247_out, not_248_out, not_249_out, not_250_out, F1, not_251_out);
  and and_40 (and_40_out, not_252_out, not_253_out, not_254_out, not_255_out, not_256_out, not_257_out, F5, not_258_out, not_259_out, not_260_out, not_261_out, not_262_out);
  and and_41 (and_41_out, not_263_out, not_264_out, not_265_out, not_266_out, not_267_out, not_268_out, F5, not_269_out, not_270_out, not_271_out, not_272_out, F0);
  and and_42 (and_42_out, not_273_out, not_274_out, not_275_out, not_276_out, not_277_out, not_278_out, F5, not_279_out, not_280_out, not_281_out, F1, not_282_out);
  and and_43 (and_43_out, not_283_out, not_284_out, not_285_out, not_286_out, not_287_out, not_288_out, F5, not_289_out, not_290_out, F2, not_291_out, not_292_out);
  and and_44 (and_44_out, not_293_out, not_294_out, not_295_out, not_296_out, not_297_out, not_298_out, F5, not_299_out, not_300_out, F2, not_301_out, F0);
  and and_45 (and_45_out, not_302_out, not_303_out, not_304_out, not_305_out, not_306_out, not_307_out, F5, not_308_out, not_309_out, F2, F1, F0);
  and and_46 (and_46_out, not_310_out, not_311_out, not_312_out, not_313_out, not_314_out, not_315_out, F5, not_316_out, F3, not_317_out, F1, not_318_out);
  and and_47 (and_47_out, not_319_out, not_320_out, not_321_out, not_322_out, not_323_out, not_324_out, F5, not_325_out, F3, not_326_out, F1, F0);
  and and_48 (and_48_out, not_327_out, not_328_out, not_329_out, not_330_out, not_331_out, not_332_out, not_333_out, not_334_out, F3, not_335_out, not_336_out, not_337_out);
  and and_49 (and_49_out, not_338_out, not_339_out, not_340_out, not_341_out, not_342_out, not_343_out, F5, not_344_out, not_345_out, F2, F1, not_346_out);
  and and_50 (BEQ, not_347_out, not_348_out, not_349_out, OP2, not_350_out, not_351_out);
  and and_51 (BNE, not_352_out, not_353_out, not_354_out, OP2, not_355_out, OP0);
  and and_52 (JR, not_356_out, not_357_out, not_358_out, not_359_out, not_360_out, not_361_out, not_362_out, not_363_out, F3, not_364_out, not_365_out, not_366_out);
  and and_53 (and_53_out, not_367_out, not_368_out, not_369_out, not_370_out, not_371_out, not_372_out, not_373_out, not_374_out, F3, not_375_out, not_376_out, not_377_out);
  and and_54 (and_54_out, not_378_out, not_379_out, not_380_out, not_381_out, OP1, not_382_out);
  and and_55 (and_55_out, not_383_out, not_384_out, not_385_out, not_386_out, OP1, OP0);
  and and_56 (JAL, not_387_out, not_388_out, not_389_out, not_390_out, OP1, OP0);
  or or_1 (MemToReg, and_1_out, and_2_out);
  or or_2 (ALU_SRC, and_4_out, and_5_out, and_6_out, and_7_out, and_8_out, and_9_out, and_10_out, and_11_out);
  or or_3 (SignedExt, and_35_out, and_36_out);
  or or_4 (JMP, and_53_out, and_54_out, and_55_out);
  or or_5 (RegWrite, and_12_out, and_13_out, and_14_out, and_15_out, and_16_out, and_17_out, and_18_out, and_19_out, and_20_out, and_21_out, and_22_out, and_23_out, and_24_out, and_25_out, and_26_out, and_27_out, and_28_out, and_29_out, and_30_out, and_31_out, and_32_out, and_33_out);
  or or_6 (RegDst, and_37_out, and_38_out, and_39_out, and_40_out, and_41_out, and_42_out, and_43_out, and_44_out, and_45_out, and_46_out, and_47_out, and_48_out, and_49_out);
endmodule

// ALU
module MIPS_ALU (
  input  [4:0] shamt,
  input  [31:0] X,
  input  [31:0] Y,
  input  [3:0] AluOP,
  output Equal,
  output [31:0] Result,
  output [31:0] Result_2
);

  wire [0:0] comparator_1_lt, comparator_2_lt;
  wire [31:0] adder_1_out, AND_out, divider_1_out, divider_1_rem, multiplier_1_cout, multiplier_1_out,
       NOR_out, OR_out, shifter_1_out, shifter_2_out, shifter_3_out, subtractor_1_out, XOR_out;

  assign AND_out = X & Y;  // AND_Gate AND, 32 bits wide
  assign OR_out = X | Y;  // OR_Gate OR, 32 bits wide
  Shifter #(.width(32)) shifter_1 (.in(Y), .\dist (shamt), .out(shifter_1_out));
  Shifter #(.width(32), .shift("ar")) shifter_2 (.in(Y), .\dist (shamt), .out(shifter_2_out));
  Shifter #(.width(32), .shift("lr")) shifter_3 (.in(Y), .\dist (shamt), .out(shifter_3_out));
  Multiplier #(.width(32)) multiplier_1 (.a(X), .b(Y), .out(multiplier_1_out), .cout(multiplier_1_cout));  // open: cin
  Divider #(.width(32)) divider_1 (.a(X), .b(Y), .out(divider_1_out), .rem(divider_1_rem));  // open: upper
  Adder #(.width(32)) adder_1 (.a(X), .b(Y), .out(adder_1_out));  // open: cin, cout
  Subtractor #(.width(32)) subtractor_1 (.a(X), .b(Y), .out(subtractor_1_out));  // open: bin, bout
  assign XOR_out = X ^ Y;  // XOR_Gate XOR, 32 bits wide
  assign NOR_out = ~(X | Y);  // NOR_Gate NOR, 32 bits wide
  Comparator #(.width(32)) comparator_1 (.a(X), .b(Y), .eq(Equal), .lt(comparator_1_lt[0]));  // open: gt
  Comparator #(.width(32), .mode("unsigned")) comparator_2 (.a(X), .b(Y), .lt(comparator_2_lt[0]));  // open: gt, eq
  Multiplexer #(.select(4), .width(32), .enable("false")) multiplexer_1 (
    .in0(shifter_1_out), .in1(shifter_2_out), .in2(shifter_3_out), .in3(multiplier_1_out),
    .in4(divider_1_out), .in5(adder_1_out), .in6(subtractor_1_out), .in7(AND_out), .in8(OR_out),
    .in9(XOR_out), .in10(NOR_out), .in11({{31{1'b0}}, comparator_1_lt[0]}),
    .in12({{31{1'b0}}, comparator_2_lt[0]}), .in13({32{1'b0}}), .in14({32{1'b0}}), .in15({32{1'b0}}),
    .out(Result), .sel(AluOP));
  Multiplexer #(.select(4), .width(32), .enable("false")) multiplexer_2 (
    .in0({32{1'b0}}), .in1({32{1'b0}}), .in2({32{1'b0}}), .in3(multiplier_1_cout), .in4(divider_1_rem),
    .in5({32{1'b0}}), .in6({32{1'b0}}), .in7({32{1'b0}}), .in8({32{1'b0}}), .in9({32{1'b0}}),
    .in10({32{1'b0}}), .in11({32{1'b0}}), .in12({32{1'b0}}), .in13({32{1'b0}}), .in14({32{1'b0}}),
    .in15({32{1'b0}}), .out(Result_2), .sel(AluOP));

  // Other names for the same wires on the sheet: Result2[31:0] = Result_2; S[3:0] = AluOP

  // Notes on the sheet:
  //   不要改变此引脚区域内容，也不要改变ALU封装形式
  //   输入引脚
  //   输出引脚
endmodule

module MIPS_Regifile (
  input  [31:0] Din,
  input  Clk,
  input  WE,
  input  [4:0] R1_num,
  input  [4:0] W_num,
  input  [4:0] R2_num,
  output [31:0] R1,
  output [31:0] R2
);

  // RegisterFile registerfile_1: pin names not known; wires that end beside it: Din, Clk, WE, W_num, R1_num, R2_num, R1, R2
endmodule

module \理想流水线  (
);

  wire and_1_out, and_2_out, and_3_out, and_4_out, and_5_out, and_6_out, and_7_out, Beq, Bne, CLK, d_ff_1_q,
       EQ, Equal, \ex_mem_1_传输状态out_表明当前传输数据有效 , Go, Halt, \id_ex_1_传输状态out_表明当前传输数据有效 ,
       \if_id_1_传输状态out_表明当前传输数据有效 , IR1, IR2, IR3, JAL, JR, not_1_out, not_2_out, RegDst, RST, Syscall, W1,
       W2, W3, \无条件分支 , \条件分支 ;
  wire [4:0] \ex_mem_1_w_输出 , \id_ex_1_shamt输出 , \id_ex_1_w_输出 , \mem_wb_1_w_输出 , multiplexer_3_out,
       multiplexer_4_out, multiplexer_5_out;
  wire [5:0] Func, Op;
  wire [11:0] EX_PC, ID_PC, IF_PC, MEM_PC, WB_PC;
  wire [15:0] ControlSig, \ex_mem_1_控制信号输出 , \id_ex_1_控制信号输出 , \LoadUse次数 , \总周期数 , \插入气泡数 , \无条件分支数 ,
       \条件分支成功数 ;
  wire [15:2] \mem_wb_1_控制信号输出 ;
  wire [25:6] \if_id_1_ir输出 ;
  wire [31:0] adder_1_out, adder_2_out, bit_extender_1_out, bit_extender_2_out, \ex_mem_1_alur输出 ,
       \ex_mem_1_ir输出 , \ex_mem_1_memdin输出 , \ex_mem_1_pc输出 , \id_ex_1_imm16输出 , \id_ex_1_ir输出 ,
       \id_ex_1_pc输出 , \id_ex_1_r1输出 , \id_ex_1_r2输出 , \if_id_1_pc输出 , LedData, \mem_wb_1_alu输出 ,
       \mem_wb_1_mem输出 , mips_alu_1_result, mips_regifile_1_r1, multiplexer_1_out, multiplexer_2_out,
       multiplexer_6_out, multiplexer_7_out, multiplexer_8_out, PC_q, ram_1_data, rom_1_data, v0;

  Button \u_总复位  (.out(RST));
  Button _1 (.out(IR1));
  Button _2 (.out(IR2));
  Button _3 (.out(IR3));
  Button \u_继续运行  (.out(Go));
  LED led_1 (.in(W1));
  LED led_2 (.in(W2));
  LED led_3 (.in(W3));
  Multiplexer #(.width(32), .enable("false")) multiplexer_1 (
    .in0(bit_extender_1_out), .in1(mips_regifile_1_r1), .out(multiplexer_1_out), .sel(JR));
  Hex_Digit_Display hex_digit_display_1 (.value(LedData[31:28]));  // open: dp
  Hex_Digit_Display hex_digit_display_2 (.value(LedData[23:20]));  // open: dp
  Hex_Digit_Display hex_digit_display_3 (.value(LedData[27:24]));  // open: dp
  \硬布线控制器  \u_硬布线控制器_1  (
    .Func(Func), .OP(Op), .ALU_OP(ControlSig[15:12]), .MemToReg(ControlSig[2]), .MemWrite(ControlSig[3]),
    .ALU_SRC(ControlSig[4]), .RegWrite(ControlSig[5]), .SysCALL(ControlSig[11]), .SignedExt(ControlSig[10]),
    .RegDst(ControlSig[7]), .JR(ControlSig[9]), .JMP(ControlSig[8]), .Beq(ControlSig[0]),
    .JAL(ControlSig[6]), .Bne(ControlSig[1]));  // open: LUI, LH, BLTZ
  Register #(.width(32)) PC (.D(multiplexer_2_out), .en(Halt), .Q(PC_q), .clk(CLK), .clr(RST));
  Multiplexer #(.select(2), .width(32), .enable("false")) multiplexer_2 (
    .in0(adder_1_out), .in1(adder_2_out), .in2(multiplexer_1_out), .out(multiplexer_2_out),
    .sel({\无条件分支 , \条件分支 }));  // open: in3
  Hex_Digit_Display hex_digit_display_4 (.value(LedData[19:16]));  // open: dp
  Hex_Digit_Display hex_digit_display_5 (.value(LedData[15:12]));  // open: dp
  Hex_Digit_Display hex_digit_display_6 (.value(LedData[7:4]));  // open: dp
  Hex_Digit_Display hex_digit_display_7 (.value(LedData[11:8]));  // open: dp
  Clock clock_1 (.out(CLK));
  Adder #(.width(32)) adder_1 (.a(32'h1), .b(PC_q), .out(adder_1_out));  // open: cin, cout
  Hex_Digit_Display hex_digit_display_8 (.value(LedData[3:0]));  // open: dp
  ROM #(.addrWidth(10), .dataWidth(32)) rom_1 (.addr(PC_q[9:0]), .data(rom_1_data));  // open: sel
  IF_ID if_id_1 (
    .IR(rom_1_data), .\IR输出 ({Op, \if_id_1_ir输出 , Func}), .PC(PC_q), .\PC输出 (\if_id_1_pc输出 ),
    .\传输状态In_表明当前传输数据有效 (1'b1), .\传输状态Out_表明当前传输数据有效 (\if_id_1_传输状态out_表明当前传输数据有效 ), .CLK(CLK),
    .\同步清零_气泡_高电平有效 (RST));  // open: 使能端_低电平有效_stall_高电平有效, PcNext, PcNext输出, Hit, Hit输出
  // Probe on \总周期数 
  // Probe on \无条件分支数 
  // Probe on \条件分支成功数 
  // Probe on \插入气泡数 
  // Probe on \LoadUse次数 
  // Probe on IF_PC
  assign bit_extender_1_out = {{6{\if_id_1_ir输出 [25]}}, {\if_id_1_ir输出 , Func}};  // Bit_Extender bit_extender_1
  // Probe on ID_PC
  not not_1 (not_1_out, Equal);
  and and_1 (and_1_out, \if_id_1_ir输出 [15], ControlSig[10]);
  assign bit_extender_2_out = {{16{and_1_out}}, {\if_id_1_ir输出 [15:6], Func}};  // Bit_Extender bit_extender_2
  // Probe on MEM_PC
  // Probe on EX_PC
  and and_2 (and_2_out, Equal, Beq);
  and and_3 (and_3_out, not_1_out, Bne);
  Multiplexer #(.select(2), .width(5), .enable("false")) multiplexer_3 (
    .in0(\if_id_1_ir输出 [20:16]), .in1(\if_id_1_ir输出 [15:11]), .in2({5{1'b1}}), .in3({5{1'b1}}),
    .out(multiplexer_3_out), .sel({ControlSig[6], ControlSig[7]}));
  // Probe on WB_PC
  or or_1 (\条件分支 , and_2_out, and_3_out);
  Counter #(.width(16), .max('hffff)) counter_1 (
    .count(Halt), .Q(\总周期数 ), .clk(CLK), .clr(RST));  // open: load, D, carry
  Multiplexer #(.width(5), .enable("false")) multiplexer_4 (
    .in0(\if_id_1_ir输出 [25:21]), .in1(5'b00010), .out(multiplexer_4_out), .sel(ControlSig[11]));
  Multiplexer #(.width(5), .enable("false")) multiplexer_5 (
    .in0(\if_id_1_ir输出 [20:16]), .in1(5'b00100), .out(multiplexer_5_out), .sel(ControlSig[11]));
  Multiplexer #(.width(32), .enable("false")) multiplexer_6 (
    .in0(multiplexer_8_out), .in1(adder_1_out), .out(multiplexer_6_out), .sel(ControlSig[6]));
  and and_4 (and_4_out, Halt, \无条件分支 );
  MIPS_Regifile mips_regifile_1 (
    .Din(multiplexer_6_out), .Clk(CLK), .R1(mips_regifile_1_r1), .R2(v0), .WE(\mem_wb_1_控制信号输出 [5]),
    .W_num(\mem_wb_1_w_输出 ), .R1_num(multiplexer_4_out), .R2_num(multiplexer_5_out));
  Counter #(.width(16), .max('hffff)) counter_2 (
    .count(and_4_out), .Q(\无条件分支数 ), .clk(CLK), .clr(RST));  // open: load, D, carry
  ID_EX id_ex_1 (
    .PC(\if_id_1_pc输出 ), .\PC输出 (\id_ex_1_pc输出 ), .\传输状态In_表明当前传输数据有效 (\if_id_1_传输状态out_表明当前传输数据有效 ),
    .\传输状态Out_表明当前传输数据有效 (\id_ex_1_传输状态out_表明当前传输数据有效 ), .CLK(CLK), .\同步清零_气泡_高电平有效 (RST),
    .IR({Op, \if_id_1_ir输出 , Func}), .\IR输出 (\id_ex_1_ir输出 ), .\控制信号 (ControlSig),
    .\控制信号输出 (\id_ex_1_控制信号输出 ), .Imm16(bit_extender_2_out), .\Imm16输出 (\id_ex_1_imm16输出 ),
    .R1(mips_regifile_1_r1), .\R1输出 (\id_ex_1_r1输出 ), .\R2输出 (\id_ex_1_r2输出 ), .R2(v0),
    .shamt(\if_id_1_ir输出 [10:6]), .\shamt输出 (\id_ex_1_shamt输出 ), .W_num(multiplexer_3_out),
    .\W_输出 (\id_ex_1_w_输出 ));  // open: 使能端_低电平有效_stall_高电平有效, PcNext, PcNext输出_2, Imm26, PcNext输出, Forward, Forward输出, ExtIns, ExtIns输出, Hit, Hit输出
  Adder #(.width(32)) adder_2 (.a(adder_1_out), .b(\id_ex_1_imm16输出 ), .out(adder_2_out));  // open: cin, cout
  Multiplexer #(.width(32), .enable("false")) multiplexer_7 (
    .in0(\id_ex_1_r2输出 ), .in1(\id_ex_1_imm16输出 ), .out(multiplexer_7_out), .sel(\id_ex_1_控制信号输出 [4]));
  and and_5 (and_5_out, Halt, \条件分支 );
  Comparator #(.width(32), .mode("unsigned")) comparator_1 (.a(32'h22), .b(\id_ex_1_r1输出 ), .eq(EQ));  // open: gt, lt
  MIPS_ALU mips_alu_1 (
    .X(\id_ex_1_r1输出 ), .Y(multiplexer_7_out), .AluOP(\id_ex_1_控制信号输出 [15:12]), .Equal(Equal),
    .Result(mips_alu_1_result), .shamt(\id_ex_1_shamt输出 ));  // open: Result_2
  Counter #(.width(16), .max('hffff)) counter_3 (
    .count(and_5_out), .Q(\条件分支成功数 ), .clk(CLK), .clr(RST));  // open: load, D, carry
  EX_MEM ex_mem_1 (
    .\控制信号 (\id_ex_1_控制信号输出 ), .\控制信号输出 (\ex_mem_1_控制信号输出 ), .AluR(mips_alu_1_result),
    .\AluR输出 (\ex_mem_1_alur输出 ), .IR(\id_ex_1_ir输出 ), .\IR输出 (\ex_mem_1_ir输出 ), .PC(\id_ex_1_pc输出 ),
    .\PC输出 (\ex_mem_1_pc输出 ), .\传输状态In_表明当前传输数据有效 (\id_ex_1_传输状态out_表明当前传输数据有效 ),
    .\传输状态Out_表明当前传输数据有效 (\ex_mem_1_传输状态out_表明当前传输数据有效 ), .CLK(CLK), .\同步清零_气泡_高电平有效 (RST),
    .MemDin(\id_ex_1_r2输出 ), .\MemDin输出 (\ex_mem_1_memdin输出 ), .W_num(\id_ex_1_w_输出 ),
    .\W_输出 (\ex_mem_1_w_输出 ));  // open: 使能端_低电平有效_stall_高电平有效, PcNext, PcNext输出, EQ, EQ输出, ExtIns, ExtIns输出
  and and_6 (and_6_out, EQ, Syscall);
  Register #(.width(32)) register_1 (.D(v0), .en(and_6_out), .Q(LedData), .clk(CLK));  // open: clr
  RAM #(.addrWidth(10), .dataWidth(32), .bus("separate")) ram_1 (
    .addr(\ex_mem_1_alur输出 [11:2]), .din(\ex_mem_1_memdin输出 ), .data(ram_1_data), .str(\ex_mem_1_控制信号输出 [3]),
    .clk(CLK), .clr(RST));  // open: sel, ld
  not not_2 (not_2_out, EQ);
  and and_7 (and_7_out, not_2_out, Syscall);
  MEM_WB mem_wb_1 (
    .\控制信号 (\ex_mem_1_控制信号输出 ),
    .\控制信号输出 ({\mem_wb_1_控制信号输出 [15:12], Syscall, \mem_wb_1_控制信号输出 [10], JR, \无条件分支 , RegDst, JAL, \mem_wb_1_控制信号输出 [5:2], Bne, Beq}),
    .Mem(ram_1_data), .\Mem输出 (\mem_wb_1_mem输出 ), .Alu(\ex_mem_1_alur输出 ), .\Alu输出 (\mem_wb_1_alu输出 ),
    .IR(\ex_mem_1_ir输出 ), .PC(\ex_mem_1_pc输出 ), .\传输状态In_表明当前传输数据有效 (\ex_mem_1_传输状态out_表明当前传输数据有效 ),
    .CLK(CLK), .\同步清零_气泡_高电平有效 (RST), .W_num(\ex_mem_1_w_输出 ), .\W_输出 (\mem_wb_1_w_输出 ));  // open: IR输出, PC输出, 传输状态Out_表明当前传输数据有效, 使能端_低电平有效_stall_高电平有效, PcNext, PcNext输出, EQ, EQ_2, ExtIns, ExtIns输出, v0, v0输出
  D_Flip_Flop #(.trigger("high")) d_ff_1 (
    .clk(CLK), .D(and_7_out), .Q(d_ff_1_q), .en(Syscall), .reset(Go));  // open: Qn, preset
  Multiplexer #(.width(32), .enable("false")) multiplexer_8 (
    .in0(\mem_wb_1_alu输出 ), .in1(\mem_wb_1_mem输出 ), .out(multiplexer_8_out), .sel(\mem_wb_1_控制信号输出 [2]));
  not not_3 (Halt, d_ff_1_q);

  // Notes on the sheet:
  //   中断源
  //   中断等待指示
  //   SignedExt
  //   JMP
  //   JR
  //   Op
  //   Func
  //   Syscall
  //   数码管输出
  //   Beq
  //   Bne
  //   MemToReg
  //   MemWrite
  //   AluOP
  //   AluSrcB
  //   RegWrite
  //   JAL
  //   RegDst
  //   指令存储器
  //   contents of rom_1 (hex, n*v repeats v):
  //   20100000 20110000 20120000 20130000 36100000 36310001 36520002 36730003 ae100000 ae110004 ae120008
  //   ae13000c 2002000a 20110000 20120000 20130000 c
  //   SignedExt
  //   流水调试日志用
  //   JAL
  //   Syscall
  //   RegDst
  //   v0
  //   a0
  //   RegWrite
  //   AlcSrcB
  //   AluOp
  //   MemWrite
endmodule

// 源寄存器使用情况
module \源寄存器使用情况  (
  input  OP0,
  input  OP1,
  input  OP2,
  input  OP3,
  input  OP4,
  input  OP5,
  input  F0,
  input  F1,
  input  F2,
  input  F3,
  input  F4,
  input  F5,
  output R1_Used,
  output R2_Used
);

  wire and_1_out, and_2_out, and_3_out, and_4_out, and_5_out, and_6_out, and_7_out, and_8_out, and_9_out,
       and_10_out, and_11_out, and_12_out, and_13_out, and_14_out, and_15_out, and_16_out, and_17_out,
       and_18_out, and_19_out, and_20_out, and_21_out, and_22_out, and_23_out, and_24_out, and_25_out,
       and_26_out, and_27_out, and_28_out, and_29_out, and_30_out, and_31_out, and_32_out, and_33_out,
       and_34_out, and_35_out, and_36_out, and_37_out, and_38_out, and_39_out, not_1_out, not_2_out,
       not_3_out, not_4_out, not_5_out, not_6_out, not_7_out, not_8_out, not_9_out, not_10_out, not_11_out,
       not_12_out, not_13_out, not_14_out, not_15_out, not_16_out, not_17_out, not_18_out, not_19_out,
       not_20_out, not_21_out, not_22_out, not_23_out, not_24_out, not_25_out, not_26_out, not_27_out,
       not_28_out, not_29_out, not_30_out, not_31_out, not_32_out, not_33_out, not_34_out, not_35_out,
       not_36_out, not_37_out, not_38_out, not_39_out, not_40_out, not_41_out, not_42_out, not_43_out,
       not_44_out, not_45_out, not_46_out, not_47_out, not_48_out, not_49_out, not_50_out, not_51_out,
       not_52_out, not_53_out, not_54_out, not_55_out, not_56_out, not_57_out, not_58_out, not_59_out,
       not_60_out, not_61_out, not_62_out, not_63_out, not_64_out, not_65_out, not_66_out, not_67_out,
       not_68_out, not_69_out, not_70_out, not_71_out, not_72_out, not_73_out, not_74_out, not_75_out,
       not_76_out, not_77_out, not_78_out, not_79_out, not_80_out, not_81_out, not_82_out, not_83_out,
       not_84_out, not_85_out, not_86_out, not_87_out, not_88_out, not_89_out, not_90_out, not_91_out,
       not_92_out, not_93_out, not_94_out, not_95_out, not_96_out, not_97_out, not_98_out, not_99_out,
       not_100_out, not_101_out, not_102_out, not_103_out, not_104_out, not_105_out, not_106_out,
       not_107_out, not_108_out, not_109_out, not_110_out, not_111_out, not_112_out, not_113_out,
       not_114_out, not_115_out, not_116_out, not_117_out, not_118_out, not_119_out, not_120_out,
       not_121_out, not_122_out, not_123_out, not_124_out, not_125_out, not_126_out, not_127_out,
       not_128_out, not_129_out, not_130_out, not_131_out, not_132_out, not_133_out, not_134_out,
       not_135_out, not_136_out, not_137_out, not_138_out, not_139_out, not_140_out, not_141_out,
       not_142_out, not_143_out, not_144_out, not_145_out, not_146_out, not_147_out, not_148_out,
       not_149_out, not_150_out, not_151_out, not_152_out, not_153_out, not_154_out, not_155_out,
       not_156_out, not_157_out, not_158_out, not_159_out, not_160_out, not_161_out, not_162_out,
       not_163_out, not_164_out, not_165_out, not_166_out, not_167_out, not_168_out, not_169_out,
       not_170_out, not_171_out, not_172_out, not_173_out, not_174_out, not_175_out, not_176_out,
       not_177_out, not_178_out, not_179_out, not_180_out, not_181_out, not_182_out, not_183_out,
       not_184_out, not_185_out, not_186_out, not_187_out, not_188_out, not_189_out, not_190_out,
       not_191_out, not_192_out, not_193_out, not_194_out, not_195_out, not_196_out, not_197_out,
       not_198_out, not_199_out, not_200_out, not_201_out, not_202_out, not_203_out, not_204_out,
       not_205_out, not_206_out, not_207_out, not_208_out, not_209_out, not_210_out, not_211_out,
       not_212_out, not_213_out, not_214_out, not_215_out, not_216_out, not_217_out, not_218_out,
       not_219_out, not_220_out, not_221_out, not_222_out, not_223_out, not_224_out, not_225_out,
       not_226_out, not_227_out, not_228_out, not_229_out, not_230_out, not_231_out, not_232_out,
       not_233_out, not_234_out, not_235_out, not_236_out, not_237_out, not_238_out, not_239_out,
       not_240_out, not_241_out, not_242_out, not_243_out, not_244_out, not_245_out, not_246_out,
       not_247_out, not_248_out, not_249_out, not_250_out, not_251_out, not_252_out, not_253_out,
       not_254_out, not_255_out, not_256_out, not_257_out, not_258_out, not_259_out, not_260_out,
       not_261_out, not_262_out, not_263_out, not_264_out, not_265_out, not_266_out, not_267_out,
       not_268_out, not_269_out, not_270_out, not_271_out, not_272_out, not_273_out, not_274_out,
       not_275_out, not_276_out, not_277_out, not_278_out, not_279_out, not_280_out, not_281_out,
       not_282_out, not_283_out, not_284_out, not_285_out, not_286_out, not_287_out, not_288_out;

  not not_1 (not_1_out, OP5);
  not not_2 (not_2_out, OP4);
  not not_3 (not_3_out, OP3);
  not not_4 (not_4_out, OP2);
  not not_5 (not_5_out, OP1);
  not not_6 (not_6_out, OP0);
  not not_7 (not_7_out, F4);
  not not_8 (not_8_out, F3);
  not not_9 (not_9_out, F2);
  not not_10 (not_10_out, F1);
  not not_11 (not_11_out, F0);
  not not_12 (not_12_out, OP5);
  not not_13 (not_13_out, OP4);
  not not_14 (not_14_out, OP3);
  not not_15 (not_15_out, OP2);
  not not_16 (not_16_out, OP1);
  not not_17 (not_17_out, OP0);
  not not_18 (not_18_out, F4);
  not not_19 (not_19_out, F3);
  not not_20 (not_20_out, F2);
  not not_21 (not_21_out, F1);
  not not_22 (not_22_out, OP5);
  not not_23 (not_23_out, OP4);
  not not_24 (not_24_out, OP3);
  not not_25 (not_25_out, OP2);
  not not_26 (not_26_out, OP1);
  not not_27 (not_27_out, OP0);
  not not_28 (not_28_out, F4);
  not not_29 (not_29_out, F3);
  not not_30 (not_30_out, F2);
  not not_31 (not_31_out, F0);
  not not_32 (not_32_out, OP5);
  not not_33 (not_33_out, OP4);
  not not_34 (not_34_out, OP3);
  not not_35 (not_35_out, OP2);
  not not_36 (not_36_out, OP1);
  not not_37 (not_37_out, OP0);
  not not_38 (not_38_out, F4);
  not not_39 (not_39_out, F3);
  not not_40 (not_40_out, F1);
  not not_41 (not_41_out, F0);
  not not_42 (not_42_out, OP5);
  not not_43 (not_43_out, OP4);
  not not_44 (not_44_out, OP3);
  not not_45 (not_45_out, OP2);
  not not_46 (not_46_out, OP1);
  not not_47 (not_47_out, OP0);
  not not_48 (not_48_out, F4);
  not not_49 (not_49_out, F3);
  not not_50 (not_50_out, F1);
  not not_51 (not_51_out, OP5);
  not not_52 (not_52_out, OP4);
  not not_53 (not_53_out, OP3);
  not not_54 (not_54_out, OP2);
  not not_55 (not_55_out, OP1);
  not not_56 (not_56_out, OP0);
  not not_57 (not_57_out, F4);
  not not_58 (not_58_out, F3);
  not not_59 (not_59_out, OP5);
  not not_60 (not_60_out, OP4);
  not not_61 (not_61_out, OP3);
  not not_62 (not_62_out, OP2);
  not not_63 (not_63_out, OP1);
  not not_64 (not_64_out, OP0);
  not not_65 (not_65_out, F4);
  not not_66 (not_66_out, F2);
  not not_67 (not_67_out, F0);
  not not_68 (not_68_out, OP5);
  not not_69 (not_69_out, OP4);
  not not_70 (not_70_out, OP3);
  not not_71 (not_71_out, OP2);
  not not_72 (not_72_out, OP1);
  not not_73 (not_73_out, OP0);
  not not_74 (not_74_out, F4);
  not not_75 (not_75_out, F2);
  not not_76 (not_76_out, OP5);
  not not_77 (not_77_out, OP4);
  not not_78 (not_78_out, OP3);
  not not_79 (not_79_out, OP2);
  not not_80 (not_80_out, OP1);
  not not_81 (not_81_out, OP0);
  not not_82 (not_82_out, F5);
  not not_83 (not_83_out, F4);
  not not_84 (not_84_out, F2);
  not not_85 (not_85_out, F1);
  not not_86 (not_86_out, F0);
  not not_87 (not_87_out, OP5);
  not not_88 (not_88_out, OP4);
  not not_89 (not_89_out, OP3);
  not not_90 (not_90_out, OP2);
  not not_91 (not_91_out, OP1);
  not not_92 (not_92_out, OP0);
  not not_93 (not_93_out, F5);
  not not_94 (not_94_out, F4);
  not not_95 (not_95_out, F1);
  not not_96 (not_96_out, F0);
  not not_97 (not_97_out, OP5);
  not not_98 (not_98_out, OP4);
  not not_99 (not_99_out, OP3);
  not not_100 (not_100_out, OP1);
  not not_101 (not_101_out, OP0);
  not not_102 (not_102_out, OP5);
  not not_103 (not_103_out, OP4);
  not not_104 (not_104_out, OP3);
  not not_105 (not_105_out, OP1);
  not not_106 (not_106_out, OP5);
  not not_107 (not_107_out, OP4);
  not not_108 (not_108_out, OP2);
  not not_109 (not_109_out, OP1);
  not not_110 (not_110_out, OP0);
  not not_111 (not_111_out, OP5);
  not not_112 (not_112_out, OP4);
  not not_113 (not_113_out, OP1);
  not not_114 (not_114_out, OP0);
  not not_115 (not_115_out, OP5);
  not not_116 (not_116_out, OP4);
  not not_117 (not_117_out, OP2);
  not not_118 (not_118_out, OP1);
  not not_119 (not_119_out, OP5);
  not not_120 (not_120_out, OP4);
  not not_121 (not_121_out, OP2);
  not not_122 (not_122_out, OP0);
  not not_123 (not_123_out, OP5);
  not not_124 (not_124_out, OP4);
  not not_125 (not_125_out, OP1);
  not not_126 (not_126_out, OP4);
  not not_127 (not_127_out, OP3);
  not not_128 (not_128_out, OP2);
  not not_129 (not_129_out, OP4);
  not not_130 (not_130_out, OP2);
  not not_131 (not_131_out, OP5);
  not not_132 (not_132_out, OP4);
  not not_133 (not_133_out, OP3);
  not not_134 (not_134_out, OP2);
  not not_135 (not_135_out, OP1);
  not not_136 (not_136_out, OP0);
  not not_137 (not_137_out, F4);
  not not_138 (not_138_out, F3);
  not not_139 (not_139_out, F0);
  not not_140 (not_140_out, OP4);
  not not_141 (not_141_out, OP3);
  not not_142 (not_142_out, OP2);
  not not_143 (not_143_out, OP1);
  not not_144 (not_144_out, OP5);
  not not_145 (not_145_out, OP4);
  not not_146 (not_146_out, OP3);
  not not_147 (not_147_out, OP2);
  not not_148 (not_148_out, OP1);
  not not_149 (not_149_out, OP5);
  not not_150 (not_150_out, OP4);
  not not_151 (not_151_out, OP3);
  not not_152 (not_152_out, OP2);
  not not_153 (not_153_out, OP1);
  not not_154 (not_154_out, OP0);
  not not_155 (not_155_out, F5);
  not not_156 (not_156_out, F4);
  not not_157 (not_157_out, F3);
  not not_158 (not_158_out, F2);
  not not_159 (not_159_out, F1);
  not not_160 (not_160_out, F0);
  not not_161 (not_161_out, OP5);
  not not_162 (not_162_out, OP4);
  not not_163 (not_163_out, OP3);
  not not_164 (not_164_out, OP2);
  not not_165 (not_165_out, OP1);
  not not_166 (not_166_out, OP0);
  not not_167 (not_167_out, F5);
  not not_168 (not_168_out, F4);
  not not_169 (not_169_out, F3);
  not not_170 (not_170_out, F2);
  not not_171 (not_171_out, OP5);
  not not_172 (not_172_out, OP4);
  not not_173 (not_173_out, OP3);
  not not_174 (not_174_out, OP2);
  not not_175 (not_175_out, OP1);
  not not_176 (not_176_out, OP0);
  not not_177 (not_177_out, F5);
  not not_178 (not_178_out, F4);
  not not_179 (not_179_out, F3);
  not not_180 (not_180_out, F2);
  not not_181 (not_181_out, F0);
  not not_182 (not_182_out, OP5);
  not not_183 (not_183_out, OP4);
  not not_184 (not_184_out, OP3);
  not not_185 (not_185_out, OP2);
  not not_186 (not_186_out, OP1);
  not not_187 (not_187_out, OP0);
  not not_188 (not_188_out, F4);
  not not_189 (not_189_out, F3);
  not not_190 (not_190_out, F2);
  not not_191 (not_191_out, F1);
  not not_192 (not_192_out, F0);
  not not_193 (not_193_out, OP5);
  not not_194 (not_194_out, OP4);
  not not_195 (not_195_out, OP3);
  not not_196 (not_196_out, OP2);
  not not_197 (not_197_out, OP1);
  not not_198 (not_198_out, OP0);
  not not_199 (not_199_out, F4);
  not not_200 (not_200_out, F3);
  not not_201 (not_201_out, F2);
  not not_202 (not_202_out, F1);
  not not_203 (not_203_out, OP5);
  not not_204 (not_204_out, OP4);
  not not_205 (not_205_out, OP3);
  not not_206 (not_206_out, OP2);
  not not_207 (not_207_out, OP1);
  not not_208 (not_208_out, OP0);
  not not_209 (not_209_out, F4);
  not not_210 (not_210_out, F3);
  not not_211 (not_211_out, F2);
  not not_212 (not_212_out, F0);
  not not_213 (not_213_out, OP5);
  not not_214 (not_214_out, OP4);
  not not_215 (not_215_out, OP3);
  not not_216 (not_216_out, OP2);
  not not_217 (not_217_out, OP1);
  not not_218 (not_218_out, OP0);
  not not_219 (not_219_out, F4);
  not not_220 (not_220_out, F3);
  not not_221 (not_221_out, F1);
  not not_222 (not_222_out, F0);
  not not_223 (not_223_out, OP5);
  not not_224 (not_224_out, OP4);
  not not_225 (not_225_out, OP3);
  not not_226 (not_226_out, OP2);
  not not_227 (not_227_out, OP1);
  not not_228 (not_228_out, OP0);
  not not_229 (not_229_out, F4);
  not not_230 (not_230_out, F3);
  not not_231 (not_231_out, F1);
  not not_232 (not_232_out, OP5);
  not not_233 (not_233_out, OP4);
  not not_234 (not_234_out, OP3);
  not not_235 (not_235_out, OP2);
  not not_236 (not_236_out, OP1);
  not not_237 (not_237_out, OP0);
  not not_238 (not_238_out, F4);
  not not_239 (not_239_out, F3);
  not not_240 (not_240_out, OP5);
  not not_241 (not_241_out, OP4);
  not not_242 (not_242_out, OP3);
  not not_243 (not_243_out, OP2);
  not not_244 (not_244_out, OP1);
  not not_245 (not_245_out, OP0);
  not not_246 (not_246_out, F4);
  not not_247 (not_247_out, F2);
  not not_248 (not_248_out, F0);
  not not_249 (not_249_out, OP5);
  not not_250 (not_250_out, OP4);
  not not_251 (not_251_out, OP3);
  not not_252 (not_252_out, OP2);
  not not_253 (not_253_out, OP1);
  not not_254 (not_254_out, OP0);
  not not_255 (not_255_out, F4);
  not not_256 (not_256_out, F2);
  not not_257 (not_257_out, OP5);
  not not_258 (not_258_out, OP4);
  not not_259 (not_259_out, OP3);
  not not_260 (not_260_out, OP2);
  not not_261 (not_261_out, OP1);
  not not_262 (not_262_out, OP0);
  not not_263 (not_263_out, F5);
  not not_264 (not_264_out, F4);
  not not_265 (not_265_out, F1);
  not not_266 (not_266_out, F0);
  not not_267 (not_267_out, OP5);
  not not_268 (not_268_out, OP4);
  not not_269 (not_269_out, OP3);
  not not_270 (not_270_out, OP1);
  not not_271 (not_271_out, OP0);
  not not_272 (not_272_out, OP5);
  not not_273 (not_273_out, OP4);
  not not_274 (not_274_out, OP3);
  not not_275 (not_275_out, OP1);
  not not_276 (not_276_out, OP4);
  not not_277 (not_277_out, OP2);
  not not_278 (not_278_out, OP5);
  not not_279 (not_279_out, OP4);
  not not_280 (not_280_out, OP3);
  not not_281 (not_281_out, OP2);
  not not_282 (not_282_out, OP1);
  not not_283 (not_283_out, OP0);
  not not_284 (not_284_out, F4);
  not not_285 (not_285_out, F3);
  not not_286 (not_286_out, F0);
  not not_287 (not_287_out, OP5);
  not not_288 (not_288_out, OP4);
  and and_1 (and_1_out, not_1_out, not_2_out, not_3_out, not_4_out, not_5_out, not_6_out, F5, not_7_out, not_8_out, not_9_out, not_10_out, not_11_out);
  and and_2 (and_2_out, not_12_out, not_13_out, not_14_out, not_15_out, not_16_out, not_17_out, F5, not_18_out, not_19_out, not_20_out, not_21_out, F0);
  and and_3 (and_3_out, not_22_out, not_23_out, not_24_out, not_25_out, not_26_out, not_27_out, F5, not_28_out, not_29_out, not_30_out, F1, not_31_out);
  and and_4 (and_4_out, not_32_out, not_33_out, not_34_out, not_35_out, not_36_out, not_37_out, F5, not_38_out, not_39_out, F2, not_40_out, not_41_out);
  and and_5 (and_5_out, not_42_out, not_43_out, not_44_out, not_45_out, not_46_out, not_47_out, F5, not_48_out, not_49_out, F2, not_50_out, F0);
  and and_6 (and_6_out, not_51_out, not_52_out, not_53_out, not_54_out, not_55_out, not_56_out, F5, not_57_out, not_58_out, F2, F1, F0);
  and and_7 (and_7_out, not_59_out, not_60_out, not_61_out, not_62_out, not_63_out, not_64_out, F5, not_65_out, F3, not_66_out, F1, not_67_out);
  and and_8 (and_8_out, not_68_out, not_69_out, not_70_out, not_71_out, not_72_out, not_73_out, F5, not_74_out, F3, not_75_out, F1, F0);
  and and_9 (and_9_out, not_76_out, not_77_out, not_78_out, not_79_out, not_80_out, not_81_out, not_82_out, not_83_out, F3, not_84_out, not_85_out, not_86_out);
  and and_10 (and_10_out, not_87_out, not_88_out, not_89_out, not_90_out, not_91_out, not_92_out, not_93_out, not_94_out, F3, F2, not_95_out, not_96_out);
  and and_11 (and_11_out, not_97_out, not_98_out, not_99_out, OP2, not_100_out, not_101_out);
  and and_12 (and_12_out, not_102_out, not_103_out, not_104_out, OP2, not_105_out, OP0);
  and and_13 (and_13_out, not_106_out, not_107_out, OP3, not_108_out, not_109_out, not_110_out);
  and and_14 (and_14_out, not_111_out, not_112_out, OP3, OP2, not_113_out, not_114_out);
  and and_15 (and_15_out, not_115_out, not_116_out, OP3, not_117_out, not_118_out, OP0);
  and and_16 (and_16_out, not_119_out, not_120_out, OP3, not_121_out, OP1, not_122_out);
  and and_17 (and_17_out, not_123_out, not_124_out, OP3, OP2, not_125_out, OP0);
  and and_18 (and_18_out, OP5, not_126_out, not_127_out, not_128_out, OP1, OP0);
  and and_19 (and_19_out, OP5, not_129_out, OP3, not_130_out, OP1, OP0);
  and and_20 (and_20_out, not_131_out, not_132_out, not_133_out, not_134_out, not_135_out, not_136_out, F5, not_137_out, not_138_out, F2, F1, not_139_out);
  and and_21 (and_21_out, OP5, not_140_out, not_141_out, not_142_out, not_143_out, OP0);
  and and_22 (and_22_out, not_144_out, not_145_out, not_146_out, not_147_out, not_148_out, OP0);
  and and_23 (and_23_out, not_149_out, not_150_out, not_151_out, not_152_out, not_153_out, not_154_out, not_155_out, not_156_out, not_157_out, not_158_out, not_159_out, not_160_out);
  and and_24 (and_24_out, not_161_out, not_162_out, not_163_out, not_164_out, not_165_out, not_166_out, not_167_out, not_168_out, not_169_out, not_170_out, F1, F0);
  and and_25 (and_25_out, not_171_out, not_172_out, not_173_out, not_174_out, not_175_out, not_176_out, not_177_out, not_178_out, not_179_out, not_180_out, F1, not_181_out);
  and and_26 (and_26_out, not_182_out, not_183_out, not_184_out, not_185_out, not_186_out, not_187_out, F5, not_188_out, not_189_out, not_190_out, not_191_out, not_192_out);
  and and_27 (and_27_out, not_193_out, not_194_out, not_195_out, not_196_out, not_197_out, not_198_out, F5, not_199_out, not_200_out, not_201_out, not_202_out, F0);
  and and_28 (and_28_out, not_203_out, not_204_out, not_205_out, not_206_out, not_207_out, not_208_out, F5, not_209_out, not_210_out, not_211_out, F1, not_212_out);
  and and_29 (and_29_out, not_213_out, not_214_out, not_215_out, not_216_out, not_217_out, not_218_out, F5, not_219_out, not_220_out, F2, not_221_out, not_222_out);
  and and_30 (and_30_out, not_223_out, not_224_out, not_225_out, not_226_out, not_227_out, not_228_out, F5, not_229_out, not_230_out, F2, not_231_out, F0);
  and and_31 (and_31_out, not_232_out, not_233_out, not_234_out, not_235_out, not_236_out, not_237_out, F5, not_238_out, not_239_out, F2, F1, F0);
  and and_32 (and_32_out, not_240_out, not_241_out, not_242_out, not_243_out, not_244_out, not_245_out, F5, not_246_out, F3, not_247_out, F1, not_248_out);
  and and_33 (and_33_out, not_249_out, not_250_out, not_251_out, not_252_out, not_253_out, not_254_out, F5, not_255_out, F3, not_256_out, F1, F0);
  and and_34 (and_34_out, not_257_out, not_258_out, not_259_out, not_260_out, not_261_out, not_262_out, not_263_out, not_264_out, F3, F2, not_265_out, not_266_out);
  and and_35 (and_35_out, not_267_out, not_268_out, not_269_out, OP2, not_270_out, not_271_out);
  and and_36 (and_36_out, not_272_out, not_273_out, not_274_out, OP2, not_275_out, OP0);
  and and_37 (and_37_out, OP5, not_276_out, OP3, not_277_out, OP1, OP0);
  and and_38 (and_38_out, not_278_out, not_279_out, not_280_out, not_281_out, not_282_out, not_283_out, F5, not_284_out, not_285_out, F2, F1, not_286_out);
  and and_39 (and_39_out, not_287_out, not_288_out, OP3, OP2, OP1, OP0);
  or or_1 (R1_Used, and_1_out, and_2_out, and_3_out, and_4_out, and_5_out, and_6_out, and_7_out, and_8_out, and_9_out, and_10_out, and_11_out, and_12_out, and_13_out, and_14_out, and_15_out, and_16_out, and_17_out, and_18_out, and_19_out, and_20_out, and_21_out, and_22_out);
  or or_2 (R2_Used, and_23_out, and_24_out, and_25_out, and_26_out, and_27_out, and_28_out, and_29_out, and_30_out, and_31_out, and_32_out, and_33_out, and_34_out, and_35_out, and_36_out, and_37_out, and_38_out, and_39_out);
endmodule

// 数据相关检测
module \数据相关检测  (
  input  [5:0] OP,
  input  [4:0] EX_WriteReg_num,
  input  EX_RegWrite,
  input  [4:0] MEM_WriteReg_num,
  input  MEM_RegWrite,
  input  [5:0] Func,
  input  [4:0] ID_R1_num,
  input  [4:0] ID_R2_num,
  output \数据相关 
);

  wire and_1_out, and_2_out, and_3_out, and_4_out, and_5_out, and_6_out, comparator_1_eq, comparator_2_eq,
       comparator_3_eq, comparator_4_eq, comparator_5_eq, comparator_6_eq, not_1_out, not_2_out, or_1_out,
       or_2_out, \源寄存器使用情况_1_r1_used , \源寄存器使用情况_1_r2_used ;

  \源寄存器使用情况  \u_源寄存器使用情况_1  (
    .OP0(OP[0]), .OP1(OP[1]), .OP2(OP[2]), .OP3(OP[3]), .OP4(OP[4]), .OP5(OP[5]), .F0(Func[0]), .F1(Func[1]),
    .F2(Func[2]), .F3(Func[3]), .F4(Func[4]), .F5(Func[5]), .R1_Used(\源寄存器使用情况_1_r1_used ),
    .R2_Used(\源寄存器使用情况_1_r2_used ));
  Comparator #(.width(5)) comparator_1 (.a(ID_R1_num), .b(EX_WriteReg_num), .eq(comparator_1_eq));  // open: gt, lt
  Comparator #(.width(5)) comparator_2 (.a(ID_R1_num), .b(MEM_WriteReg_num), .eq(comparator_2_eq));  // open: gt, lt
  Comparator #(.width(5)) comparator_3 (.a(ID_R2_num), .b(EX_WriteReg_num), .eq(comparator_3_eq));  // open: gt, lt
  Comparator #(.width(5)) comparator_4 (.a(ID_R2_num), .b(MEM_WriteReg_num), .eq(comparator_4_eq));  // open: gt, lt
  not not_1 (not_1_out, comparator_5_eq);
  Comparator #(.width(5)) comparator_5 (.a(ID_R1_num), .b({5{1'b0}}), .eq(comparator_5_eq));  // open: gt, lt
  and and_1 (and_1_out, comparator_1_eq, EX_RegWrite);
  and and_2 (and_2_out, comparator_2_eq, MEM_RegWrite);
  and and_3 (and_3_out, comparator_3_eq, EX_RegWrite);
  and and_4 (and_4_out, comparator_4_eq, MEM_RegWrite);
  Comparator #(.width(5)) comparator_6 (.a(ID_R2_num), .b({5{1'b0}}), .eq(comparator_6_eq));  // open: gt, lt
  not not_2 (not_2_out, comparator_6_eq);
  or or_1 (or_1_out, and_1_out, and_2_out);
  or or_2 (or_2_out, and_3_out, and_4_out);
  and and_5 (and_5_out, not_1_out, or_1_out, \源寄存器使用情况_1_r1_used );
  and and_6 (and_6_out, \源寄存器使用情况_1_r2_used , or_2_out, not_2_out);
  or or_3 (\数据相关 , and_5_out, and_6_out);

  // Other names for the same wires on the sheet: OP_CODE[5:0] = OP
endmodule

// IF/ID
module IF_ID (
  input  Hit,
  input  [31:0] PcNext,
  input  [31:0] IR,
  input  [31:0] PC,
  input  \传输状态In_表明当前传输数据有效 ,
  input  CLK,
  input  \同步清零_气泡_高电平有效 ,
  input  \使能端_低电平有效_stall_高电平有效 ,
  output \Hit输出 ,
  output [31:0] \PcNext输出 ,
  output [31:0] \IR输出 ,
  output [31:0] \PC输出 ,
  output \传输状态Out_表明当前传输数据有效 
);

  wire multiplexer_1_out, multiplexer_5_out, not_1_out;
  wire [31:0] multiplexer_2_out, multiplexer_3_out, multiplexer_4_out;

  Multiplexer #(.enable("false")) multiplexer_1 (.in0(Hit), .in1(1'b0), .out(multiplexer_1_out), .sel(\同步清零_气泡_高电平有效 ));
  Multiplexer #(.width(32), .enable("false")) multiplexer_2 (
    .in0(PcNext), .in1({32{1'b0}}), .out(multiplexer_2_out), .sel(\同步清零_气泡_高电平有效 ));
  Multiplexer #(.width(32), .enable("false")) multiplexer_3 (
    .in0(IR), .in1({32{1'b0}}), .out(multiplexer_3_out), .sel(\同步清零_气泡_高电平有效 ));
  Multiplexer #(.width(32), .enable("false")) multiplexer_4 (
    .in0(PC), .in1({32{1'b0}}), .out(multiplexer_4_out), .sel(\同步清零_气泡_高电平有效 ));
  Multiplexer #(.enable("false")) multiplexer_5 (
    .in0(\传输状态In_表明当前传输数据有效 ), .in1(1'b0), .out(multiplexer_5_out), .sel(\同步清零_气泡_高电平有效 ));
  Register #(.width(1)) register_1 (.D(multiplexer_1_out), .en(not_1_out), .Q(\Hit输出 ), .clk(CLK));  // open: clr
  Register #(.width(32)) register_2 (.D(multiplexer_2_out), .en(not_1_out), .Q(\PcNext输出 ), .clk(CLK));  // open: clr
  Register #(.width(32)) register_3 (.D(multiplexer_3_out), .en(not_1_out), .Q(\IR输出 ), .clk(CLK));  // open: clr
  Register #(.width(32)) register_4 (.D(multiplexer_4_out), .en(not_1_out), .Q(\PC输出 ), .clk(CLK));  // open: clr
  Register #(.width(1)) register_5 (
    .D(multiplexer_5_out), .en(not_1_out), .Q(\传输状态Out_表明当前传输数据有效 ), .clk(CLK));  // open: clr
  not not_1 (not_1_out, \使能端_低电平有效_stall_高电平有效 );
endmodule

// ID/EX
module ID_EX (
  input  Hit,
  input  [2:0] ExtIns,
  input  [3:0] Forward,
  input  [31:0] Imm26,
  input  [31:0] PcNext,
  input  [4:0] W_num,
  input  [4:0] shamt,
  input  [15:0] \控制信号 ,
  input  [31:0] R1,
  input  [31:0] R2,
  input  [31:0] IR,
  input  [31:0] PC,
  input  [31:0] Imm16,
  input  \传输状态In_表明当前传输数据有效 ,
  input  CLK,
  input  \同步清零_气泡_高电平有效 ,
  input  \使能端_低电平有效_stall_高电平有效 ,
  output \Hit输出 ,
  output [2:0] \ExtIns输出 ,
  output [3:0] \Forward输出 ,
  output [31:0] \PcNext输出 ,
  output [31:0] \PcNext输出_2 ,
  output [4:0] \W_输出 ,
  output [4:0] \shamt输出 ,
  output [15:0] \控制信号输出 ,
  output [31:0] \R1输出 ,
  output [31:0] \R2输出 ,
  output [31:0] \IR输出 ,
  output [31:0] \PC输出 ,
  output [31:0] \Imm16输出 ,
  output \传输状态Out_表明当前传输数据有效 
);

  wire multiplexer_1_out, multiplexer_14_out, not_1_out;
  wire [2:0] multiplexer_2_out;
  wire [3:0] multiplexer_3_out;
  wire [4:0] multiplexer_6_out, multiplexer_7_out;
  wire [15:0] multiplexer_8_out;
  wire [31:0] multiplexer_4_out, multiplexer_5_out, multiplexer_9_out, multiplexer_10_out,
       multiplexer_11_out, multiplexer_12_out, multiplexer_13_out;

  Multiplexer #(.enable("false")) multiplexer_1 (.in0(Hit), .in1(1'b0), .out(multiplexer_1_out), .sel(\同步清零_气泡_高电平有效 ));
  Multiplexer #(.width(3), .enable("false")) multiplexer_2 (
    .in0(ExtIns), .in1(3'b000), .out(multiplexer_2_out), .sel(\同步清零_气泡_高电平有效 ));
  Multiplexer #(.width(4), .enable("false")) multiplexer_3 (
    .in0(Forward), .in1(4'b0000), .out(multiplexer_3_out), .sel(\同步清零_气泡_高电平有效 ));
  Multiplexer #(.width(32), .enable("false")) multiplexer_4 (
    .in0(Imm26), .in1({32{1'b0}}), .out(multiplexer_4_out), .sel(\同步清零_气泡_高电平有效 ));
  Multiplexer #(.width(32), .enable("false")) multiplexer_5 (
    .in0(PcNext), .in1({32{1'b0}}), .out(multiplexer_5_out), .sel(\同步清零_气泡_高电平有效 ));
  Multiplexer #(.width(5), .enable("false")) multiplexer_6 (
    .in0(W_num), .in1({5{1'b0}}), .out(multiplexer_6_out), .sel(\同步清零_气泡_高电平有效 ));
  Multiplexer #(.width(5), .enable("false")) multiplexer_7 (
    .in0(shamt), .in1({5{1'b0}}), .out(multiplexer_7_out), .sel(\同步清零_气泡_高电平有效 ));
  Multiplexer #(.width(16), .enable("false")) multiplexer_8 (
    .in0(\控制信号 ), .in1({16{1'b0}}), .out(multiplexer_8_out), .sel(\同步清零_气泡_高电平有效 ));
  Multiplexer #(.width(32), .enable("false")) multiplexer_9 (
    .in0(R1), .in1({32{1'b0}}), .out(multiplexer_9_out), .sel(\同步清零_气泡_高电平有效 ));
  Multiplexer #(.width(32), .enable("false")) multiplexer_10 (
    .in0(R2), .in1({32{1'b0}}), .out(multiplexer_10_out), .sel(\同步清零_气泡_高电平有效 ));
  Multiplexer #(.width(32), .enable("false")) multiplexer_11 (
    .in0(IR), .in1({32{1'b0}}), .out(multiplexer_11_out), .sel(\同步清零_气泡_高电平有效 ));
  Multiplexer #(.width(32), .enable("false")) multiplexer_12 (
    .in0(PC), .in1({32{1'b0}}), .out(multiplexer_12_out), .sel(\同步清零_气泡_高电平有效 ));
  Multiplexer #(.width(32), .enable("false")) multiplexer_13 (
    .in0(Imm16), .in1({32{1'b0}}), .out(multiplexer_13_out), .sel(\同步清零_气泡_高电平有效 ));
  Multiplexer #(.enable("false")) multiplexer_14 (
    .in0(\传输状态In_表明当前传输数据有效 ), .in1(1'b0), .out(multiplexer_14_out), .sel(\同步清零_气泡_高电平有效 ));
  Register #(.width(1)) register_1 (.D(multiplexer_1_out), .en(not_1_out), .Q(\Hit输出 ), .clk(CLK));  // open: clr
  Register #(.width(3)) register_2 (.D(multiplexer_2_out), .en(not_1_out), .Q(\ExtIns输出 ), .clk(CLK));  // open: clr
  Register #(.width(4)) register_3 (.D(multiplexer_3_out), .en(not_1_out), .Q(\Forward输出 ), .clk(CLK));  // open: clr
  Register #(.width(32)) register_4 (.D(multiplexer_4_out), .en(not_1_out), .Q(\PcNext输出 ), .clk(CLK));  // open: clr
  Register #(.width(32)) register_5 (.D(multiplexer_5_out), .en(not_1_out), .Q(\PcNext输出_2 ), .clk(CLK));  // open: clr
  Register #(.width(5)) register_6 (.D(multiplexer_6_out), .en(not_1_out), .Q(\W_输出 ), .clk(CLK));  // open: clr
  Register #(.width(5)) register_7 (.D(multiplexer_7_out), .en(not_1_out), .Q(\shamt输出 ), .clk(CLK));  // open: clr
  Register #(.width(16)) register_8 (.D(multiplexer_8_out), .en(not_1_out), .Q(\控制信号输出 ), .clk(CLK));  // open: clr
  Register #(.width(32)) register_9 (.D(multiplexer_9_out), .en(not_1_out), .Q(\R1输出 ), .clk(CLK));  // open: clr
  Register #(.width(32)) register_10 (.D(multiplexer_10_out), .en(not_1_out), .Q(\R2输出 ), .clk(CLK));  // open: clr
  Register #(.width(32)) register_11 (.D(multiplexer_11_out), .en(not_1_out), .Q(\IR输出 ), .clk(CLK));  // open: clr
  Register #(.width(32)) register_12 (.D(multiplexer_12_out), .en(not_1_out), .Q(\PC输出 ), .clk(CLK));  // open: clr
  Register #(.width(32)) register_13 (.D(multiplexer_13_out), .en(not_1_out), .Q(\Imm16输出 ), .clk(CLK));  // open: clr
  Register #(.width(1)) register_14 (
    .D(multiplexer_14_out), .en(not_1_out), .Q(\传输状态Out_表明当前传输数据有效 ), .clk(CLK));  // open: clr
  not not_1 (not_1_out, \使能端_低电平有效_stall_高电平有效 );
endmodule

// EX/MEM
module EX_MEM (
  input  [2:0] ExtIns,
  input  EQ,
  input  [31:0] PcNext,
  input  [4:0] W_num,
  input  [15:0] \控制信号 ,
  input  [31:0] MemDin,
  input  [31:0] AluR,
  input  [31:0] IR,
  input  [31:0] PC,
  input  \传输状态In_表明当前传输数据有效 ,
  input  CLK,
  input  \同步清零_气泡_高电平有效 ,
  input  \使能端_低电平有效_stall_高电平有效 ,
  output [2:0] \ExtIns输出 ,
  output \EQ输出 ,
  output [31:0] \PcNext输出 ,
  output [4:0] \W_输出 ,
  output [15:0] \控制信号输出 ,
  output [31:0] \MemDin输出 ,
  output [31:0] \AluR输出 ,
  output [31:0] \IR输出 ,
  output [31:0] \PC输出 ,
  output \传输状态Out_表明当前传输数据有效 
);

  wire multiplexer_2_out, multiplexer_10_out, not_1_out;
  wire [2:0] multiplexer_1_out;
  wire [4:0] multiplexer_4_out;
  wire [15:0] multiplexer_5_out;
  wire [31:0] multiplexer_3_out, multiplexer_6_out, multiplexer_7_out, multiplexer_8_out, multiplexer_9_out;

  Multiplexer #(.width(3), .enable("false")) multiplexer_1 (
    .in0(ExtIns), .in1(3'b000), .out(multiplexer_1_out), .sel(\同步清零_气泡_高电平有效 ));
  Multiplexer #(.enable("false")) multiplexer_2 (.in0(EQ), .in1(1'b0), .out(multiplexer_2_out), .sel(\同步清零_气泡_高电平有效 ));
  Multiplexer #(.width(32), .enable("false")) multiplexer_3 (
    .in0(PcNext), .in1({32{1'b0}}), .out(multiplexer_3_out), .sel(\同步清零_气泡_高电平有效 ));
  Multiplexer #(.width(5), .enable("false")) multiplexer_4 (
    .in0(W_num), .in1({5{1'b0}}), .out(multiplexer_4_out), .sel(\同步清零_气泡_高电平有效 ));
  Multiplexer #(.width(16), .enable("false")) multiplexer_5 (
    .in0(\控制信号 ), .in1({16{1'b0}}), .out(multiplexer_5_out), .sel(\同步清零_气泡_高电平有效 ));
  Multiplexer #(.width(32), .enable("false")) multiplexer_6 (
    .in0(MemDin), .in1({32{1'b0}}), .out(multiplexer_6_out), .sel(\同步清零_气泡_高电平有效 ));
  Multiplexer #(.width(32), .enable("false")) multiplexer_7 (
    .in0(AluR), .in1({32{1'b0}}), .out(multiplexer_7_out), .sel(\同步清零_气泡_高电平有效 ));
  Multiplexer #(.width(32), .enable("false")) multiplexer_8 (
    .in0(IR), .in1({32{1'b0}}), .out(multiplexer_8_out), .sel(\同步清零_气泡_高电平有效 ));
  Multiplexer #(.width(32), .enable("false")) multiplexer_9 (
    .in0(PC), .in1({32{1'b0}}), .out(multiplexer_9_out), .sel(\同步清零_气泡_高电平有效 ));
  Multiplexer #(.enable("false")) multiplexer_10 (
    .in0(\传输状态In_表明当前传输数据有效 ), .in1(1'b0), .out(multiplexer_10_out), .sel(\同步清零_气泡_高电平有效 ));
  Register #(.width(3)) register_1 (.D(multiplexer_1_out), .en(not_1_out), .Q(\ExtIns输出 ), .clk(CLK));  // open: clr
  Register #(.width(1)) register_2 (.D(multiplexer_2_out), .en(not_1_out), .Q(\EQ输出 ), .clk(CLK));  // open: clr
  Register #(.width(32)) register_3 (.D(multiplexer_3_out), .en(not_1_out), .Q(\PcNext输出 ), .clk(CLK));  // open: clr
  Register #(.width(5)) register_4 (.D(multiplexer_4_out), .en(not_1_out), .Q(\W_输出 ), .clk(CLK));  // open: clr
  Register #(.width(16)) register_5 (.D(multiplexer_5_out), .en(not_1_out), .Q(\控制信号输出 ), .clk(CLK));  // open: clr
  Register #(.width(32)) register_6 (.D(multiplexer_6_out), .en(not_1_out), .Q(\MemDin输出 ), .clk(CLK));  // open: clr
  Register #(.width(32)) register_7 (.D(multiplexer_7_out), .en(not_1_out), .Q(\AluR输出 ), .clk(CLK));  // open: clr
  Register #(.width(32)) register_8 (.D(multiplexer_8_out), .en(not_1_out), .Q(\IR输出 ), .clk(CLK));  // open: clr
  Register #(.width(32)) register_9 (.D(multiplexer_9_out), .en(not_1_out), .Q(\PC输出 ), .clk(CLK));  // open: clr
  Register #(.width(1)) register_10 (
    .D(multiplexer_10_out), .en(not_1_out), .Q(\传输状态Out_表明当前传输数据有效 ), .clk(CLK));  // open: clr
  not not_1 (not_1_out, \使能端_低电平有效_stall_高电平有效 );
endmodule
// MEM/WB
module MEM_WB (
  input  [2:0] ExtIns,
  input  EQ,
  input  [31:0] PcNext,
  input  [4:0] W_num,
  input  [15:0] \控制信号 ,
  input  [31:0] Mem,
  input  [31:0] Alu,
  input  [31:0] IR,
  input  [31:0] PC,
  input  [31:0] v0,
  input  \传输状态In_表明当前传输数据有效 ,
  input  CLK,
  input  \同步清零_气泡_高电平有效 ,
  input  \使能端_低电平有效_stall_高电平有效 ,
  output [2:0] \ExtIns输出 ,
  output EQ_2,
  output [31:0] \PcNext输出 ,
  output [4:0] \W_输出 ,
  output [15:0] \控制信号输出 ,
  output [31:0] \Mem输出 ,
  output [31:0] \Alu输出 ,
  output [31:0] \IR输出 ,
  output [31:0] \PC输出 ,
  output [31:0] \v0输出 ,
  output \传输状态Out_表明当前传输数据有效 
);

  wire multiplexer_2_out, multiplexer_11_out, not_1_out;
  wire [2:0] multiplexer_1_out;
  wire [4:0] multiplexer_4_out;
  wire [15:0] multiplexer_5_out;
  wire [31:0] multiplexer_3_out, multiplexer_6_out, multiplexer_7_out, multiplexer_8_out, multiplexer_9_out,
       multiplexer_10_out;

  Multiplexer #(.width(3), .enable("false")) multiplexer_1 (
    .in0(ExtIns), .in1(3'b000), .out(multiplexer_1_out), .sel(\同步清零_气泡_高电平有效 ));
  Multiplexer #(.enable("false")) multiplexer_2 (.in0(EQ), .in1(1'b0), .out(multiplexer_2_out), .sel(\同步清零_气泡_高电平有效 ));
  Multiplexer #(.width(32), .enable("false")) multiplexer_3 (
    .in0(PcNext), .in1({32{1'b0}}), .out(multiplexer_3_out), .sel(\同步清零_气泡_高电平有效 ));
  Multiplexer #(.width(5), .enable("false")) multiplexer_4 (
    .in0(W_num), .in1({5{1'b0}}), .out(multiplexer_4_out), .sel(\同步清零_气泡_高电平有效 ));
  Multiplexer #(.width(16), .enable("false")) multiplexer_5 (
    .in0(\控制信号 ), .in1({16{1'b0}}), .out(multiplexer_5_out), .sel(\同步清零_气泡_高电平有效 ));
  Multiplexer #(.width(32), .enable("false")) multiplexer_6 (
    .in0(Mem), .in1({32{1'b0}}), .out(multiplexer_6_out), .sel(\同步清零_气泡_高电平有效 ));
  Multiplexer #(.width(32), .enable("false")) multiplexer_7 (
    .in0(Alu), .in1({32{1'b0}}), .out(multiplexer_7_out), .sel(\同步清零_气泡_高电平有效 ));
  Multiplexer #(.width(32), .enable("false")) multiplexer_8 (
    .in0(IR), .in1({32{1'b0}}), .out(multiplexer_8_out), .sel(\同步清零_气泡_高电平有效 ));
  Multiplexer #(.width(32), .enable("false")) multiplexer_9 (
    .in0(PC), .in1({32{1'b0}}), .out(multiplexer_9_out), .sel(\同步清零_气泡_高电平有效 ));
  Multiplexer #(.width(32), .enable("false")) multiplexer_10 (
    .in0(v0), .in1({32{1'b0}}), .out(multiplexer_10_out), .sel(\同步清零_气泡_高电平有效 ));
  Multiplexer #(.enable("false")) multiplexer_11 (
    .in0(\传输状态In_表明当前传输数据有效 ), .in1(1'b0), .out(multiplexer_11_out), .sel(\同步清零_气泡_高电平有效 ));
  not not_1 (not_1_out, \使能端_低电平有效_stall_高电平有效 );
  Register #(.width(3)) register_1 (.D(multiplexer_1_out), .en(not_1_out), .Q(\ExtIns输出 ), .clk(CLK));  // open: clr
  Register #(.width(1)) register_2 (.D(multiplexer_2_out), .en(not_1_out), .Q(EQ_2), .clk(CLK));  // open: clr
  Register #(.width(32)) register_3 (.D(multiplexer_3_out), .en(not_1_out), .Q(\PcNext输出 ), .clk(CLK));  // open: clr
  Register #(.width(5)) register_4 (.D(multiplexer_4_out), .en(not_1_out), .Q(\W_输出 ), .clk(CLK));  // open: clr
  Register #(.width(16)) register_5 (.D(multiplexer_5_out), .en(not_1_out), .Q(\控制信号输出 ), .clk(CLK));  // open: clr
  Register #(.width(32)) register_6 (.D(multiplexer_6_out), .en(not_1_out), .Q(\Mem输出 ), .clk(CLK));  // open: clr
  Register #(.width(32)) register_7 (.D(multiplexer_7_out), .en(not_1_out), .Q(\Alu输出 ), .clk(CLK));  // open: clr
  Register #(.width(32)) register_8 (.D(multiplexer_8_out), .en(not_1_out), .Q(\IR输出 ), .clk(CLK));  // open: clr
  Register #(.width(32)) register_9 (.D(multiplexer_9_out), .en(not_1_out), .Q(\PC输出 ), .clk(CLK));  // open: clr
  Register #(.width(32)) register_10 (.D(multiplexer_10_out), .en(not_1_out), .Q(\v0输出 ), .clk(CLK));  // open: clr
  Register #(.width(1)) register_11 (
    .D(multiplexer_11_out), .en(not_1_out), .Q(\传输状态Out_表明当前传输数据有效 ), .clk(CLK));  // open: clr
endmodule

module \分支相关流水线  (
);

  wire and_1_out, and_2_out, and_3_out, and_4_out, and_5_out, and_6_out, CLK, d_ff_1_q, EQ, EQHalt,
       \ex_mem_1_eq输出 , \ex_mem_1_传输状态out_表明当前传输数据有效 , Go, Halt, \id_ex_1_传输状态out_表明当前传输数据有效 ,
       \if_id_1_传输状态out_表明当前传输数据有效 , IR1, IR2, IR3, JR, mips_alu_1_equal, not_1_out, not_2_out, not_3_out,
       not_4_out, not_5_out, not_6_out, or_1_out, or_2_out, RST, Syscall, SyscallHalt, undriven, W1, W2, W3,
       \无条件分支 , \条件分支 ;
  wire [4:0] \ex_mem_1_w_输出 , \id_ex_1_shamt输出 , \id_ex_1_w_输出 , \mem_wb_1_w_输出 , multiplexer_3_out,
       selreg_1_r1_num, selreg_1_r2_num, \指令译码_1_rd , \指令译码_1_rs , \指令译码_1_rt , \指令译码_1_shamt ;
  wire [5:0] \指令译码_1_func , \指令译码_1_op ;
  wire [11:0] EX_PC, ID_PC, IF_PC, MEM_PC, WB_PC;
  wire [15:0] \ex_mem_1_控制信号输出 , \id_ex_1_控制信号输出 , \LoadUse次数 , \mem_wb_1_控制信号输出 , \总周期数 , \指令译码_1_imm16 ,
       \插入气泡数 , \无条件分支数 , \条件分支成功数 , \硬布线控制器_封装_1_controlsig ;
  wire [25:0] \指令译码_1_imm26 ;
  wire [31:0] adder_1_out, adder_2_out, \ex_mem_1_alur输出 , \ex_mem_1_ir输出 , \ex_mem_1_memdin输出 ,
       \ex_mem_1_pcnext输出 , \ex_mem_1_pc输出 , \id_ex_1_imm16输出 , \id_ex_1_ir输出 , \id_ex_1_pcnext输出 ,
       \id_ex_1_pcnext输出_2 , \id_ex_1_pc输出 , \id_ex_1_r1输出 , \if_id_1_ir输出 , \if_id_1_pcnext输出 ,
       \if_id_1_pc输出 , immext_1_imm16out, immext_1_imm26out, LedData, \mem_wb_1_alu输出 , \mem_wb_1_mem输出 ,
       \mem_wb_1_pcnext输出 , mips_alu_1_result, mips_regifile_1_r1, mips_regifile_1_r2, multiplexer_1_out,
       multiplexer_2_out, multiplexer_4_out, multiplexer_5_out, multiplexer_6_out, PC_q, ram_1_data,
       rom_1_data, v0;

  Button \u_总复位  (.out(RST));
  Button _1 (.out(IR1));
  Button _2 (.out(IR2));
  Button _3 (.out(IR3));
  Button \u_继续运行  (.out(Go));
  LED led_1 (.in(W1));
  LED led_2 (.in(W2));
  LED led_3 (.in(W3));
  Multiplexer #(.width(32), .enable("false")) multiplexer_1 (
    .in0(\id_ex_1_pcnext输出 ), .in1(\id_ex_1_r1输出 ), .out(multiplexer_1_out), .sel(JR));
  Hex_Digit_Display hex_digit_display_1 (.value(LedData[31:28]));  // open: dp
  Hex_Digit_Display hex_digit_display_2 (.value(LedData[23:20]));  // open: dp
  Hex_Digit_Display hex_digit_display_3 (.value(LedData[27:24]));  // open: dp
  Register #(.width(32)) PC (.D(multiplexer_2_out), .en(Halt), .Q(PC_q), .clk(CLK), .clr(RST));
  Multiplexer #(.select(2), .width(32), .enable("false")) multiplexer_2 (
    .in0(adder_1_out), .in1(adder_2_out), .in2(multiplexer_1_out), .out(multiplexer_2_out),
    .sel({\无条件分支 , \条件分支 }));  // open: in3
  Hex_Digit_Display hex_digit_display_4 (.value(LedData[15:12]));  // open: dp
  Hex_Digit_Display hex_digit_display_5 (.value(LedData[19:16]));  // open: dp
  Hex_Digit_Display hex_digit_display_6 (.value(LedData[11:8]));  // open: dp
  Hex_Digit_Display hex_digit_display_7 (.value(LedData[7:4]));  // open: dp
  Clock clock_1 (.out(CLK));
  Hex_Digit_Display hex_digit_display_8 (.value(LedData[3:0]));  // open: dp
  Adder #(.width(32)) adder_1 (.a(32'h1), .b(PC_q), .out(adder_1_out));  // open: cin, cout
  ROM #(.addrWidth(10), .dataWidth(32)) rom_1 (.addr(PC_q[9:0]), .data(rom_1_data));  // open: sel
  not not_1 (not_1_out, 1'b1);
  or or_1 (or_1_out, RST, \条件分支 , \无条件分支 );
  IF_ID if_id_1 (
    .IR(rom_1_data), .\IR输出 (\if_id_1_ir输出 ), .PC(PC_q), .\PC输出 (\if_id_1_pc输出 ), .\传输状态In_表明当前传输数据有效 (1'b1),
    .\传输状态Out_表明当前传输数据有效 (\if_id_1_传输状态out_表明当前传输数据有效 ), .CLK(CLK), .\同步清零_气泡_高电平有效 (or_1_out),
    .\使能端_低电平有效_stall_高电平有效 (not_1_out), .PcNext(adder_1_out), .\PcNext输出 (\if_id_1_pcnext输出 ));  // open: Hit, Hit输出
  // Probe on \总周期数 
  // Probe on \无条件分支数 
  // Probe on \条件分支成功数 
  // Probe on \插入气泡数 
  // Probe on \LoadUse次数 
  \指令译码  \u_指令译码_1  (
    .Op(\指令译码_1_op ), .Imm16(\指令译码_1_imm16 ), .Func(\指令译码_1_func ), .Rs(\指令译码_1_rs ),
    .Instruction(\if_id_1_ir输出 ), .Rt(\指令译码_1_rt ), .Imm26(\指令译码_1_imm26 ), .Rd(\指令译码_1_rd ),
    .shamt(\指令译码_1_shamt ));
  // Probe on IF_PC
  \硬布线控制器_封装  \u_硬布线控制器_封装_1  (.OP(\指令译码_1_op ), .Func(\指令译码_1_func ), .ControlSig(\硬布线控制器_封装_1_controlsig ));
  ImmExt immext_1 (
    .Imm16(\指令译码_1_imm16 ), .Imm26(\指令译码_1_imm26 ), .Imm16Out(immext_1_imm16out),
    .Imm26Out(immext_1_imm26out), .SignedExt(\硬布线控制器_封装_1_controlsig [10]));
  // Probe on ID_PC
  // Probe on MEM_PC
  // Probe on EX_PC
  Multiplexer #(.select(2), .width(5), .enable("false")) multiplexer_3 (
    .in0(\指令译码_1_rt ), .in1(\指令译码_1_rd ), .in2({5{1'b1}}), .in3({5{1'b1}}), .out(multiplexer_3_out),
    .sel({\硬布线控制器_封装_1_controlsig [6], \硬布线控制器_封装_1_controlsig [7]}));
  // Probe on WB_PC
  SelReg selreg_1 (
    .in_1(\硬布线控制器_封装_1_controlsig [11]), .Rs(\指令译码_1_rs ), .Rt(\指令译码_1_rt ), .R1_num(selreg_1_r1_num),
    .R2_num(selreg_1_r2_num));
  MIPS_Regifile mips_regifile_1 (
    .Din(multiplexer_6_out), .Clk(CLK), .R1(mips_regifile_1_r1), .R2(mips_regifile_1_r2),
    .WE(\mem_wb_1_控制信号输出 [5]), .W_num(\mem_wb_1_w_输出 ), .R1_num(selreg_1_r1_num), .R2_num(selreg_1_r2_num));
  and and_1 (and_1_out, Halt, \条件分支 );
  and and_2 (and_2_out, Halt, \无条件分支 );
  or or_2 (or_2_out, RST, \条件分支 , \无条件分支 );
  ID_EX id_ex_1 (
    .PC(\if_id_1_pc输出 ), .\PC输出 (\id_ex_1_pc输出 ), .\传输状态In_表明当前传输数据有效 (\if_id_1_传输状态out_表明当前传输数据有效 ),
    .\传输状态Out_表明当前传输数据有效 (\id_ex_1_传输状态out_表明当前传输数据有效 ), .CLK(CLK), .\同步清零_气泡_高电平有效 (or_2_out),
    .\使能端_低电平有效_stall_高电平有效 (not_2_out), .IR(\if_id_1_ir输出 ), .\IR输出 (\id_ex_1_ir输出 ),
    .\控制信号 (\硬布线控制器_封装_1_controlsig ),
    .\控制信号输出 ({\id_ex_1_控制信号输出 [15:12], Syscall, \id_ex_1_控制信号输出 [10], JR, \无条件分支 , \id_ex_1_控制信号输出 [7:0]}),
    .Imm16(immext_1_imm16out), .\Imm16输出 (\id_ex_1_imm16输出 ), .R1(mips_regifile_1_r1),
    .\R1输出 (\id_ex_1_r1输出 ), .\R2输出 (v0), .R2(mips_regifile_1_r2), .shamt(\指令译码_1_shamt ),
    .\shamt输出 (\id_ex_1_shamt输出 ), .W_num(multiplexer_3_out), .\W_输出 (\id_ex_1_w_输出 ),
    .PcNext(\if_id_1_pcnext输出 ), .\PcNext输出_2 (\id_ex_1_pcnext输出_2 ), .Imm26(immext_1_imm26out),
    .\PcNext输出 (\id_ex_1_pcnext输出 ));  // open: Forward, Forward输出, ExtIns, ExtIns输出, Hit, Hit输出
  not not_2 (not_2_out, \if_id_1_传输状态out_表明当前传输数据有效 );
  Counter #(.width(16), .max('hffff)) counter_1 (
    .count(and_1_out), .Q(\条件分支成功数 ), .clk(CLK), .clr(RST));  // open: load, D, carry
  Counter #(.width(16), .max('hffff)) counter_2 (
    .count(and_2_out), .Q(\无条件分支数 ), .clk(CLK), .clr(RST));  // open: load, D, carry
  Adder #(.width(32)) adder_2 (.a(\id_ex_1_imm16输出 ), .b(\id_ex_1_pcnext输出_2 ), .out(adder_2_out));  // open: cin, cout
  Multiplexer #(.width(32), .enable("false")) multiplexer_4 (
    .in0(v0), .in1(\id_ex_1_imm16输出 ), .out(multiplexer_4_out), .sel(\id_ex_1_控制信号输出 [4]));
  not not_3 (not_3_out, mips_alu_1_equal);
  MIPS_ALU mips_alu_1 (
    .X(\id_ex_1_r1输出 ), .Y(multiplexer_4_out), .AluOP(\id_ex_1_控制信号输出 [15:12]), .Equal(mips_alu_1_equal),
    .Result(mips_alu_1_result), .shamt(\id_ex_1_shamt输出 ));  // open: Result_2
  Comparator #(.width(32), .mode("unsigned")) comparator_1 (.a(\id_ex_1_r1输出 ), .b(32'h22), .eq(EQ));  // open: gt, lt
  Register #(.width(32)) register_1 (.D(v0), .en(and_3_out), .Q(LedData), .clk(CLK));  // open: clr
  and and_3 (and_3_out, EQ, Syscall);
  and and_4 (and_4_out, mips_alu_1_equal, \id_ex_1_控制信号输出 [0]);
  and and_5 (and_5_out, not_3_out, \id_ex_1_控制信号输出 [1]);
  EX_MEM ex_mem_1 (
    .\控制信号 ({\id_ex_1_控制信号输出 [15:12], Syscall, \id_ex_1_控制信号输出 [10], JR, \无条件分支 , \id_ex_1_控制信号输出 [7:0]}),
    .\控制信号输出 (\ex_mem_1_控制信号输出 ), .AluR(mips_alu_1_result), .\AluR输出 (\ex_mem_1_alur输出 ),
    .IR(\id_ex_1_ir输出 ), .\IR输出 (\ex_mem_1_ir输出 ), .PC(\id_ex_1_pc输出 ), .\PC输出 (\ex_mem_1_pc输出 ),
    .\传输状态In_表明当前传输数据有效 (\id_ex_1_传输状态out_表明当前传输数据有效 ), .\传输状态Out_表明当前传输数据有效 (\ex_mem_1_传输状态out_表明当前传输数据有效 ),
    .CLK(CLK), .\同步清零_气泡_高电平有效 (RST), .\使能端_低电平有效_stall_高电平有效 (not_4_out), .MemDin(v0),
    .\MemDin输出 (\ex_mem_1_memdin输出 ), .W_num(\id_ex_1_w_输出 ), .\W_输出 (\ex_mem_1_w_输出 ),
    .PcNext(\id_ex_1_pcnext输出_2 ), .\PcNext输出 (\ex_mem_1_pcnext输出 ), .EQ(EQ), .\EQ输出 (\ex_mem_1_eq输出 ));  // open: ExtIns, ExtIns输出
  not not_4 (not_4_out, undriven);
  or or_3 (\条件分支 , and_4_out, and_5_out);
  Counter #(.width(16), .max('hffff)) counter_3 (
    .count(Halt), .Q(\总周期数 ), .clk(CLK), .clr(RST));  // open: load, D, carry
  not not_5 (not_5_out, EQHalt);
  RAM #(.addrWidth(10), .dataWidth(32), .bus("separate")) ram_1 (
    .addr(\ex_mem_1_alur输出 [11:2]), .din(\ex_mem_1_memdin输出 ), .data(ram_1_data), .str(\ex_mem_1_控制信号输出 [3]),
    .clk(CLK), .clr(RST));  // open: sel, ld
  and and_6 (and_6_out, not_5_out, SyscallHalt);
  MEM_WB mem_wb_1 (
    .\控制信号 (\ex_mem_1_控制信号输出 ), .\控制信号输出 ({\mem_wb_1_控制信号输出 [15:12], SyscallHalt, \mem_wb_1_控制信号输出 [10:0]}),
    .Mem(ram_1_data), .\Mem输出 (\mem_wb_1_mem输出 ), .Alu(\ex_mem_1_alur输出 ), .\Alu输出 (\mem_wb_1_alu输出 ),
    .IR(\ex_mem_1_ir输出 ), .PC(\ex_mem_1_pc输出 ), .\传输状态In_表明当前传输数据有效 (\ex_mem_1_传输状态out_表明当前传输数据有效 ),
    .CLK(CLK), .\同步清零_气泡_高电平有效 (RST), .\使能端_低电平有效_stall_高电平有效 (not_6_out), .W_num(\ex_mem_1_w_输出 ),
    .\W_输出 (\mem_wb_1_w_输出 ), .PcNext(\ex_mem_1_pcnext输出 ), .\PcNext输出 (\mem_wb_1_pcnext输出 ),
    .EQ(\ex_mem_1_eq输出 ), .EQ_2(EQHalt));  // open: IR输出, PC输出, 传输状态Out_表明当前传输数据有效, ExtIns, ExtIns输出, v0, v0输出
  not not_6 (not_6_out, \ex_mem_1_传输状态out_表明当前传输数据有效 );
  D_Flip_Flop #(.trigger("high")) d_ff_1 (
    .clk(CLK), .D(and_6_out), .Q(d_ff_1_q), .en(SyscallHalt), .reset(Go));  // open: Qn, preset
  Multiplexer #(.width(32), .enable("false")) multiplexer_5 (
    .in0(\mem_wb_1_alu输出 ), .in1(\mem_wb_1_mem输出 ), .out(multiplexer_5_out), .sel(\mem_wb_1_控制信号输出 [2]));
  not not_7 (Halt, d_ff_1_q);
  Multiplexer #(.width(32), .enable("false")) multiplexer_6 (
    .in0(multiplexer_5_out), .in1(\mem_wb_1_pcnext输出 ), .out(multiplexer_6_out), .sel(\mem_wb_1_控制信号输出 [6]));

  // Notes on the sheet:
  //   中断源
  //   0:Beq
  //   1:Bne
  //   2:MemToReg
  //   3:MemWrite
  //   4:AluSrcB
  //   5:RegWrite
  //   6:JAL
  //   7:RegDst
  //   8:JMP
  //   9:JR
  //   10:SignedExt
  //   11:Syscall
  //   12-15:AluOp
  //   中断等待指示
  //   数码管输出
  //   指令存储器
  //   contents of rom_1 (hex, n*v repeats v):
  //   20110020 20020022 8000c06 20110000 20110000 2002000a 10000003 20110000 20110000 2002000a 14110003
  //   20110000 20110000 2002000a c000c14 2002000a 0 0 0 c 2231ffff 0 0 0 112020 0 0 0 c 1620fff6 3e00008
  //   SignedExt
  //   流水调试日志用
  //   RegDst
  //   JAL
  //   Syscall
  //   RegWrite
  //   JAL
  //   无条件分支
  //   AlcSrcB
  //   MemWrite
endmodule

module \气泡流水线  (
);

  wire and_1_out, and_2_out, and_3_out, and_4_out, and_5_out, and_6_out, and_7_out, and_8_out, and_9_out,
       CLK, comparator_1_eq, d_ff_1_q, EQHalt, \ex_mem_1_eq输出 , \ex_mem_1_传输状态out_表明当前传输数据有效 , Ex_RegWrite,
       Go, Halt, \id_ex_1_传输状态out_表明当前传输数据有效 , \if_id_1_传输状态out_表明当前传输数据有效 , IR1, IR2, IR3, JR, LH, LUI,
       Mem_RegWrite, mips_alu_1_equal, not_1_out, not_2_out, not_3_out, not_4_out, not_6_out, not_7_out,
       not_8_out, or_1_out, or_2_out, or_3_out, or_4_out, RST, SyscallHalt, W1, W2, W3, WB_JAL, \数据相关 ,
       \无条件分支 , \条件分支 ;
  wire [2:0] \ex_mem_1_extins输出 , \id_ex_1_extins输出 , \拓展指令信号_1_lui ;
  wire [2:2] \mem_wb_1_extins输出 ;
  wire [4:0] Ex_WriteReg_num, \id_ex_1_shamt输出 , ID_R1_num, ID_R2_num, \mem_wb_1_w_输出 , Mem_WriteReg_num,
       multiplexer_3_out, \指令译码_1_rd , \指令译码_1_rs , \指令译码_1_rt , \指令译码_1_shamt ;
  wire [5:0] Func, Op;
  wire [15:0] \ex_mem_1_控制信号输出 , \id_ex_1_控制信号输出 , \LoadUse次数 , \mem_wb_1_控制信号输出 , \总周期数 , \指令译码_1_imm16 ,
       \插入气泡数 , \无条件分支数 , \条件分支成功数 , \硬布线控制器_封装_1_controlsig ;
  wire [25:0] \指令译码_1_imm26 ;
  wire [31:0] adder_1_out, adder_2_out, \ex_mem_1_alur输出 , \ex_mem_1_ir输出 , \ex_mem_1_memdin输出 ,
       \ex_mem_1_pcnext输出 , EX_PC, \id_ex_1_imm16输出 , \id_ex_1_ir输出 , \id_ex_1_pcnext输出 ,
       \id_ex_1_pcnext输出_2 , \id_ex_1_r1输出 , \id_ex_1_r2输出 , ID_PC, \if_id_1_ir输出 , \if_id_1_pcnext输出 ,
       IF_PC, immext_1_imm16out, immext_1_imm26out, LedData, \lh指令_1_dout , \lui指令_1_dout , MEM_PC,
       \mem_wb_1_alu输出 , \mem_wb_1_ir输出 , \mem_wb_1_mem输出 , mips_alu_1_result, mips_regifile_1_r1,
       mips_regifile_1_r2, multiplexer_1_out, multiplexer_2_out, multiplexer_4_out, multiplexer_5_out,
       ram_1_data, rom_1_data, v0, WB_PC, WB_PcNext;

  Button \u_总复位  (.out(RST));
  Button _1 (.out(IR1));
  Button _2 (.out(IR2));
  Button _3 (.out(IR3));
  Button \u_继续运行  (.out(Go));
  LED led_1 (.in(W1));
  LED led_2 (.in(W2));
  LED led_3 (.in(W3));
  Multiplexer #(.width(32), .enable("false")) multiplexer_1 (
    .in0(\id_ex_1_pcnext输出 ), .in1(\id_ex_1_r1输出 ), .out(multiplexer_1_out), .sel(JR));
  Hex_Digit_Display hex_digit_display_1 (.value(LedData[31:28]));  // open: dp
  Hex_Digit_Display hex_digit_display_2 (.value(LedData[27:24]));  // open: dp
  Hex_Digit_Display hex_digit_display_3 (.value(LedData[23:20]));  // open: dp
  Multiplexer #(.select(2), .width(32), .enable("false")) multiplexer_2 (
    .in0(adder_1_out), .in1(adder_2_out), .in2(multiplexer_1_out), .out(multiplexer_2_out),
    .sel({\id_ex_1_控制信号输出 [8], \条件分支 }));  // open: in3
  Register #(.width(32)) PC (.D(multiplexer_2_out), .en(and_1_out), .Q(IF_PC), .clk(CLK), .clr(RST));
  and and_1 (and_1_out, Halt, not_1_out);
  not not_1 (not_1_out, \数据相关 );
  Hex_Digit_Display hex_digit_display_4 (.value(LedData[19:16]));  // open: dp
  Hex_Digit_Display hex_digit_display_5 (.value(LedData[15:12]));  // open: dp
  Hex_Digit_Display hex_digit_display_6 (.value(LedData[11:8]));  // open: dp
  Hex_Digit_Display hex_digit_display_7 (.value(LedData[7:4]));  // open: dp
  Clock clock_1 (.out(CLK));
  Hex_Digit_Display hex_digit_display_8 (.value(LedData[3:0]));  // open: dp
  Adder #(.width(32)) adder_1 (.a(32'h1), .b(IF_PC), .out(adder_1_out));  // open: cin, cout
  ROM #(.addrWidth(10), .dataWidth(32)) rom_1 (.addr(IF_PC[9:0]), .data(rom_1_data));  // open: sel
  or or_1 (or_1_out, \数据相关 , not_2_out);
  not not_2 (not_2_out, Halt);
  or or_2 (or_2_out, RST, \条件分支 , \id_ex_1_控制信号输出 [8]);
  IF_ID if_id_1 (
    .IR(rom_1_data), .\IR输出 (\if_id_1_ir输出 ), .PC(IF_PC), .\PC输出 (ID_PC), .\传输状态In_表明当前传输数据有效 (1'b1),
    .\传输状态Out_表明当前传输数据有效 (\if_id_1_传输状态out_表明当前传输数据有效 ), .CLK(CLK), .\同步清零_气泡_高电平有效 (or_2_out),
    .\使能端_低电平有效_stall_高电平有效 (or_1_out), .PcNext(adder_1_out), .\PcNext输出 (\if_id_1_pcnext输出 ));  // open: Hit, Hit输出
  // Probe on \总周期数 
  // Probe on \无条件分支数 
  // Probe on \条件分支成功数 
  // Probe on \插入气泡数 
  // Probe on \LoadUse次数 
  \指令译码  \u_指令译码_1  (
    .Op(Op), .Imm16(\指令译码_1_imm16 ), .Func(Func), .Rs(\指令译码_1_rs ), .Instruction(\if_id_1_ir输出 ),
    .Rt(\指令译码_1_rt ), .Imm26(\指令译码_1_imm26 ), .Rd(\指令译码_1_rd ), .shamt(\指令译码_1_shamt ));
  // Probe on IF_PC[11:0]
  \数据相关检测  \u_数据相关检测_1  (
    .OP(Op), .EX_WriteReg_num(Ex_WriteReg_num), .EX_RegWrite(Ex_RegWrite),
    .MEM_WriteReg_num(Mem_WriteReg_num), .MEM_RegWrite(Mem_RegWrite), .\数据相关 (\数据相关 ), .Func(Func),
    .ID_R1_num(ID_R1_num), .ID_R2_num(ID_R2_num));
  \硬布线控制器_封装  \u_硬布线控制器_封装_1  (.OP(Op), .Func(Func), .ControlSig(\硬布线控制器_封装_1_controlsig ));
  ImmExt immext_1 (
    .Imm16(\指令译码_1_imm16 ), .Imm26(\指令译码_1_imm26 ), .Imm16Out(immext_1_imm16out),
    .Imm26Out(immext_1_imm26out), .SignedExt(\硬布线控制器_封装_1_controlsig [10]));
  // Probe on ID_PC[11:0]
  // Probe on MEM_PC[11:0]
  // Probe on EX_PC[11:0]
  Multiplexer #(.select(2), .width(5), .enable("false")) multiplexer_3 (
    .in0(\指令译码_1_rt ), .in1(\指令译码_1_rd ), .in2({5{1'b1}}), .in3({5{1'b1}}), .out(multiplexer_3_out),
    .sel({\硬布线控制器_封装_1_controlsig [6], \硬布线控制器_封装_1_controlsig [7]}));
  // Probe on WB_PC[11:0]
  \拓展指令信号  \u_拓展指令信号_1  (
    .OP0(Op[0]), .OP1(Op[1]), .OP2(Op[2]), .OP3(Op[3]), .OP4(Op[4]), .OP5(Op[5]), .F0(Func[0]), .F1(Func[1]),
    .F2(Func[2]), .F3(Func[3]), .F4(Func[4]), .F5(Func[5]), .LUI(\拓展指令信号_1_lui [0]), .LH(\拓展指令信号_1_lui [1]),
    .BLTZ(\拓展指令信号_1_lui [2]));
  SelReg selreg_1 (
    .in_1(\硬布线控制器_封装_1_controlsig [11]), .Rs(\指令译码_1_rs ), .Rt(\指令译码_1_rt ), .R1_num(ID_R1_num),
    .R2_num(ID_R2_num));
  not not_3 (not_3_out, EQHalt);
  MIPS_Regifile mips_regifile_1 (
    .Din(\lui指令_1_dout ), .Clk(CLK), .R1(mips_regifile_1_r1), .R2(mips_regifile_1_r2),
    .WE(\mem_wb_1_控制信号输出 [5]), .W_num(\mem_wb_1_w_输出 ), .R1_num(ID_R1_num), .R2_num(ID_R2_num));
  and and_2 (and_2_out, Halt, \条件分支 );
  and and_3 (and_3_out, Halt, \无条件分支 );
  and and_4 (and_4_out, not_3_out, SyscallHalt);
  or or_3 (or_3_out, RST, \条件分支 , \id_ex_1_控制信号输出 [8], \数据相关 );
  ID_EX id_ex_1 (
    .PC(ID_PC), .\PC输出 (EX_PC), .\传输状态In_表明当前传输数据有效 (\if_id_1_传输状态out_表明当前传输数据有效 ),
    .\传输状态Out_表明当前传输数据有效 (\id_ex_1_传输状态out_表明当前传输数据有效 ), .CLK(CLK), .\同步清零_气泡_高电平有效 (or_3_out),
    .\使能端_低电平有效_stall_高电平有效 (not_4_out), .IR(\if_id_1_ir输出 ), .\IR输出 (\id_ex_1_ir输出 ),
    .\控制信号 (\硬布线控制器_封装_1_controlsig ),
    .\控制信号输出 ({\id_ex_1_控制信号输出 [15:10], JR, \id_ex_1_控制信号输出 [8:6], Ex_RegWrite, \id_ex_1_控制信号输出 [4:0]}),
    .Imm16(immext_1_imm16out), .\Imm16输出 (\id_ex_1_imm16输出 ), .R1(mips_regifile_1_r1),
    .\R1输出 (\id_ex_1_r1输出 ), .\R2输出 (\id_ex_1_r2输出 ), .R2(mips_regifile_1_r2), .shamt(\指令译码_1_shamt ),
    .\shamt输出 (\id_ex_1_shamt输出 ), .W_num(multiplexer_3_out), .\W_输出 (Ex_WriteReg_num),
    .PcNext(\if_id_1_pcnext输出 ), .\PcNext输出_2 (\id_ex_1_pcnext输出_2 ), .Imm26(immext_1_imm26out),
    .\PcNext输出 (\id_ex_1_pcnext输出 ), .ExtIns(\拓展指令信号_1_lui ), .\ExtIns输出 (\id_ex_1_extins输出 ));  // open: Forward, Forward输出, Hit, Hit输出
  not not_4 (not_4_out, Halt);
  Counter #(.width(16), .max('hffff)) counter_1 (
    .count(and_2_out), .Q(\条件分支成功数 ), .clk(CLK), .clr(RST));  // open: load, D, carry
  Counter #(.width(16), .max('hffff)) counter_2 (
    .count(and_3_out), .Q(\无条件分支数 ), .clk(CLK), .clr(RST));  // open: load, D, carry
  D_Flip_Flop #(.trigger("high")) d_ff_1 (
    .clk(CLK), .D(and_4_out), .Q(d_ff_1_q), .en(SyscallHalt), .reset(Go));  // open: Qn, preset
  not not_5 (Halt, d_ff_1_q);
  Adder #(.width(32)) adder_2 (.a(\id_ex_1_imm16输出 ), .b(\id_ex_1_pcnext输出_2 ), .out(adder_2_out));  // open: cin, cout
  Multiplexer #(.width(32), .enable("false")) multiplexer_4 (
    .in0(\id_ex_1_r2输出 ), .in1(\id_ex_1_imm16输出 ), .out(multiplexer_4_out), .sel(\id_ex_1_控制信号输出 [4]));
  not not_6 (not_6_out, mips_alu_1_equal);
  MIPS_ALU mips_alu_1 (
    .X(\id_ex_1_r1输出 ), .Y(multiplexer_4_out), .AluOP(\id_ex_1_控制信号输出 [15:12]), .Equal(mips_alu_1_equal),
    .Result(mips_alu_1_result), .shamt(\id_ex_1_shamt输出 ));  // open: Result_2
  Comparator #(.width(32), .mode("unsigned")) comparator_1 (
    .a(\id_ex_1_r1输出 ), .b(32'h22), .eq(comparator_1_eq));  // open: gt, lt
  Register #(.width(32)) register_1 (.D(v0), .en(and_5_out), .Q(LedData), .clk(CLK));  // open: clr
  and and_5 (and_5_out, EQHalt, SyscallHalt);
  and and_6 (and_6_out, mips_alu_1_equal, \id_ex_1_控制信号输出 [0]);
  and and_7 (and_7_out, not_6_out, \id_ex_1_控制信号输出 [1]);
  EX_MEM ex_mem_1 (
    .\控制信号 ({\id_ex_1_控制信号输出 [15:10], JR, \id_ex_1_控制信号输出 [8:6], Ex_RegWrite, \id_ex_1_控制信号输出 [4:0]}),
    .\控制信号输出 ({\ex_mem_1_控制信号输出 [15:6], Mem_RegWrite, \ex_mem_1_控制信号输出 [4:0]}), .AluR(mips_alu_1_result),
    .\AluR输出 (\ex_mem_1_alur输出 ), .IR(\id_ex_1_ir输出 ), .\IR输出 (\ex_mem_1_ir输出 ), .PC(EX_PC), .\PC输出 (MEM_PC),
    .\传输状态In_表明当前传输数据有效 (\id_ex_1_传输状态out_表明当前传输数据有效 ), .\传输状态Out_表明当前传输数据有效 (\ex_mem_1_传输状态out_表明当前传输数据有效 ),
    .CLK(CLK), .\同步清零_气泡_高电平有效 (RST), .\使能端_低电平有效_stall_高电平有效 (not_7_out), .MemDin(\id_ex_1_r2输出 ),
    .\MemDin输出 (\ex_mem_1_memdin输出 ), .W_num(Ex_WriteReg_num), .\W_输出 (Mem_WriteReg_num),
    .PcNext(\id_ex_1_pcnext输出_2 ), .\PcNext输出 (\ex_mem_1_pcnext输出 ), .EQ(comparator_1_eq),
    .\EQ输出 (\ex_mem_1_eq输出 ), .ExtIns(\id_ex_1_extins输出 ), .\ExtIns输出 (\ex_mem_1_extins输出 ));
  not not_7 (not_7_out, Halt);
  or or_4 (or_4_out, and_6_out, and_7_out);
  and and_8 (and_8_out, \id_ex_1_extins输出 [2], mips_alu_1_result[0]);
  and and_9 (and_9_out, Halt, \数据相关 );
  or or_5 (\条件分支 , or_4_out, and_8_out);
  Counter #(.width(16), .max('hffff)) counter_3 (
    .count(Halt), .Q(\总周期数 ), .clk(CLK), .clr(RST));  // open: load, D, carry
  Counter #(.width(16), .max('hffff)) counter_4 (
    .count(and_9_out), .Q(\插入气泡数 ), .clk(CLK), .clr(RST));  // open: load, D, carry
  RAM #(.addrWidth(10), .dataWidth(32), .bus("separate")) ram_1 (
    .addr(\ex_mem_1_alur输出 [11:2]), .din(\ex_mem_1_memdin输出 ), .data(ram_1_data), .str(\ex_mem_1_控制信号输出 [3]),
    .clk(CLK), .clr(RST));  // open: sel, ld
  MEM_WB mem_wb_1 (
    .\控制信号 ({\ex_mem_1_控制信号输出 [15:6], Mem_RegWrite, \ex_mem_1_控制信号输出 [4:0]}),
    .\控制信号输出 ({\mem_wb_1_控制信号输出 [15:12], SyscallHalt, \mem_wb_1_控制信号输出 [10:9], \无条件分支 , \mem_wb_1_控制信号输出 [7], WB_JAL, \mem_wb_1_控制信号输出 [5:0]}),
    .Mem(ram_1_data), .\Mem输出 (\mem_wb_1_mem输出 ), .Alu(\ex_mem_1_alur输出 ), .\Alu输出 (\mem_wb_1_alu输出 ),
    .IR(\ex_mem_1_ir输出 ), .\IR输出 (\mem_wb_1_ir输出 ), .PC(MEM_PC), .\PC输出 (WB_PC),
    .\传输状态In_表明当前传输数据有效 (\ex_mem_1_传输状态out_表明当前传输数据有效 ), .CLK(CLK), .\同步清零_气泡_高电平有效 (RST),
    .\使能端_低电平有效_stall_高电平有效 (not_8_out), .W_num(Mem_WriteReg_num), .\W_输出 (\mem_wb_1_w_输出 ),
    .PcNext(\ex_mem_1_pcnext输出 ), .\PcNext输出 (WB_PcNext), .EQ(\ex_mem_1_eq输出 ), .EQ_2(EQHalt),
    .ExtIns(\ex_mem_1_extins输出 ), .\ExtIns输出 ({\mem_wb_1_extins输出 [2], LH, LUI}), .v0(\ex_mem_1_memdin输出 ),
    .\v0输出 (v0));  // open: 传输状态Out_表明当前传输数据有效
  not not_8 (not_8_out, Halt);
  Multiplexer #(.width(32), .enable("false")) multiplexer_5 (
    .in0(\mem_wb_1_alu输出 ), .in1(\mem_wb_1_mem输出 ), .out(multiplexer_5_out), .sel(\mem_wb_1_控制信号输出 [2]));
  \LH指令  \lh指令_1  (.Dout(\lh指令_1_dout ), .Din(multiplexer_5_out), .LH(LH), .SEL(\mem_wb_1_alu输出 [1]));
  \LUI指令  \lui指令_1  (
    .Imm16(\mem_wb_1_ir输出 [15:0]), .Dout(\lui指令_1_dout ), .Din(\lh指令_1_dout ), .PcNext(WB_PcNext),
    .JAL(WB_JAL), .LUI(LUI));

  // Notes on the sheet:
  //   中断源
  //   0:Beq
  //   1:Bne
  //   2:MemToReg
  //   3:MemWrite
  //   4:AluSrcB
  //   5:RegWrite
  //   6:JAL
  //   7:RegDst
  //   8:JMP
  //   9:JR
  //   10:SignedExt
  //   11:Syscall
  //   12-15:AluOp
  //   中断等待指示
  //   数码管输出
  //   指令存储器
  //   contents of rom_1 (hex, n*v repeats v):
  //   20110005 8100006 20110001 20120002 20130003 20140004 810000b 20110001 20120002 20130003 20140004
  //   8100010 20110001 20120002 20130003 20140004 8100015 20110001 20120002 20130003 20140004 810001a
  //   20110001 20120002 20130003 20140004 810001f 20110001 20120002 20130003 20140004 8100024 20110001
  //   20120002 20130003 20140004 8100029 20110001 20120002 20130003 20140004 2231ffff 1620ffe0 20100001
  //   201200ff 20110001 20130003 12120005 12100004 20110001 20120002 20130003 20140004 16310004 16320003
  //   20110001 20120002 20130003 c10003d 2002000a c 20100000 22100001 102020 20020022 c 3e00008
  //   SignedExt
  //   流水调试日志用
  //   RegDst
  //   JAL
  //   Syscall
  //   RegWrite
  //   JAL
  //   无条件分支
  //   AlcSrcB
  //   BNE+BEQ
  //   BLTZ
  //   MemWrite
endmodule

module \重定向流水线  (
);

  wire AluSrcB, and_1_out, and_2_out, and_3_out, and_4_out, and_5_out, and_6_out, and_7_out, and_8_out,
       and_9_out, CLK, d_ff_1_q, EQ, EQHalt, \ex_mem_1_eq输出 , \ex_mem_1_传输状态out_表明当前传输数据有效 , Ex_MemToReg,
       Ex_RegWrite, Go, Halt, \id_ex_1_传输状态out_表明当前传输数据有效 , \if_id_1_传输状态out_表明当前传输数据有效 , IR1, IR2, IR3, JR,
       LH, \LoadUse相关 , LUI, Mem_MemToReg, Mem_RegWrite, mips_alu_1_equal, not_1_out, not_2_out, not_3_out,
       not_4_out, not_5_out, not_7_out, or_1_out, or_2_out, or_3_out, RST, Syscall, SyscallHalt, W1, W2, W3,
       WB_JAL, \无条件分支 , \条件分支 ;
  wire [1:0] Forward1, Forward2;
  wire [2:0] \ex_mem_1_extins输出 , \id_ex_1_extins输出 , \拓展指令信号_1_lui ;
  wire [2:2] \mem_wb_1_extins输出 ;
  wire [3:0] ID_Forward;
  wire [4:0] Ex_WriteReg_num, \id_ex_1_shamt输出 , ID_R1_num, ID_R2_num, \mem_wb_1_w_输出 , Mem_WriteReg_num,
       multiplexer_5_out, \指令译码_1_rd , \指令译码_1_rs , \指令译码_1_rt , \指令译码_1_shamt ;
  wire [5:0] Func, Op;
  wire [15:0] \ex_mem_1_控制信号输出 , \id_ex_1_控制信号输出 , \LoadUse次数 , \mem_wb_1_控制信号输出 , \总周期数 , \指令译码_1_imm16 ,
       \插入气泡数 , \无条件分支数 , \条件分支成功数 , \硬布线控制器_封装_1_controlsig ;
  wire [25:0] \指令译码_1_imm26 ;
  wire [31:0] adder_1_out, adder_2_out, \ex_mem_1_ir输出 , \ex_mem_1_memdin输出 , \ex_mem_1_pcnext输出 , EX_PC,
       EX_R1, EX_R2, \id_ex_1_imm16输出 , \id_ex_1_ir输出 , \id_ex_1_pcnext输出 , \id_ex_1_pcnext输出_2 , ID_PC,
       \if_id_1_ir输出 , \if_id_1_pcnext输出 , IF_PC, immext_1_imm16out, immext_1_imm26out, LedData,
       \lh指令_1_dout , \lui指令_1_dout , MEM_AluR, MEM_PC, \mem_wb_1_ir输出 , \mem_wb_1_mem输出 , mips_alu_1_result,
       mips_regifile_1_r1, mips_regifile_1_r2, multiplexer_1_out, multiplexer_2_out, multiplexer_6_out,
       multiplexer_7_out, multiplexer_9_out, ram_1_data, Redir_A, Redir_B, rom_1_data, WB_AluR, WB_Mem,
       WB_PC, WB_PcNext;

  Button \u_总复位  (.out(RST));
  Button _1 (.out(IR1));
  Button _2 (.out(IR2));
  Button _3 (.out(IR3));
  Button \u_继续运行  (.out(Go));
  LED led_1 (.in(W1));
  LED led_2 (.in(W2));
  LED led_3 (.in(W3));
  Multiplexer #(.width(32), .enable("false")) multiplexer_1 (
    .in0(\id_ex_1_pcnext输出 ), .in1(EX_R1), .out(multiplexer_1_out), .sel(JR));
  Hex_Digit_Display hex_digit_display_1 (.value(LedData[31:28]));  // open: dp
  Hex_Digit_Display hex_digit_display_2 (.value(LedData[27:24]));  // open: dp
  Hex_Digit_Display hex_digit_display_3 (.value(LedData[23:20]));  // open: dp
  Multiplexer #(.select(2), .width(32), .enable("false")) multiplexer_2 (
    .in0(adder_1_out), .in1(adder_2_out), .in2(multiplexer_1_out), .out(multiplexer_2_out),
    .sel({\id_ex_1_控制信号输出 [8], \条件分支 }));  // open: in3
  Register #(.width(32)) PC (.D(multiplexer_2_out), .en(and_1_out), .Q(IF_PC), .clk(CLK), .clr(RST));
  and and_1 (and_1_out, Halt, not_1_out);
  not not_1 (not_1_out, \LoadUse相关 );
  Hex_Digit_Display hex_digit_display_4 (.value(LedData[15:12]));  // open: dp
  Hex_Digit_Display hex_digit_display_5 (.value(LedData[19:16]));  // open: dp
  \重定向检测  \u_重定向检测_1  (
    .OP(Op), .EX_WriteReg_num(Ex_WriteReg_num), .EX_RegWrite(Ex_RegWrite), .Load_use(\LoadUse相关 ),
    .ID_R1_num(ID_R1_num), .MEM_RegWrite(Mem_RegWrite), .forwardR1(ID_Forward[1:0]), .Func(Func),
    .ID_R2_num(ID_R2_num), .EX_MemToReg(Ex_MemToReg), .forwardR2(ID_Forward[3:2]),
    .MEM_W_num(Mem_WriteReg_num), .MEM_MemToReg(Mem_MemToReg));
  Hex_Digit_Display hex_digit_display_6 (.value(LedData[11:8]));  // open: dp
  Hex_Digit_Display hex_digit_display_7 (.value(LedData[7:4]));  // open: dp
  Clock clock_1 (.out(CLK));
  // Probe on Forward1
  Multiplexer #(.select(2), .width(32), .enable("false")) multiplexer_3 (
    .in0(EX_R1), .in1(WB_Mem), .in2(WB_AluR), .in3(MEM_AluR), .out(Redir_A), .sel(Forward1));
  // Probe on Forward2
  Multiplexer #(.select(2), .width(32), .enable("false")) multiplexer_4 (
    .in0(EX_R2), .in1(WB_Mem), .in2(WB_AluR), .in3(MEM_AluR), .out(Redir_B), .sel(Forward2));
  Hex_Digit_Display hex_digit_display_8 (.value(LedData[3:0]));  // open: dp
  Adder #(.width(32)) adder_1 (.a(32'h1), .b(IF_PC), .out(adder_1_out));  // open: cin, cout
  ROM #(.addrWidth(10), .dataWidth(32)) rom_1 (.addr(IF_PC[9:0]), .data(rom_1_data));  // open: sel
  or or_1 (or_1_out, RST, \条件分支 , \id_ex_1_控制信号输出 [8]);
  IF_ID if_id_1 (
    .IR(rom_1_data), .\IR输出 (\if_id_1_ir输出 ), .PC(IF_PC), .\PC输出 (ID_PC), .\传输状态In_表明当前传输数据有效 (1'b1),
    .\传输状态Out_表明当前传输数据有效 (\if_id_1_传输状态out_表明当前传输数据有效 ), .CLK(CLK), .\同步清零_气泡_高电平有效 (or_1_out),
    .\使能端_低电平有效_stall_高电平有效 (\LoadUse相关 ), .PcNext(adder_1_out), .\PcNext输出 (\if_id_1_pcnext输出 ));  // open: Hit, Hit输出
  // Probe on \总周期数 
  // Probe on \无条件分支数 
  // Probe on \条件分支成功数 
  // Probe on \插入气泡数 
  // Probe on \LoadUse次数 
  \指令译码  \u_指令译码_1  (
    .Op(Op), .Imm16(\指令译码_1_imm16 ), .Func(Func), .Rs(\指令译码_1_rs ), .Instruction(\if_id_1_ir输出 ),
    .Rt(\指令译码_1_rt ), .Imm26(\指令译码_1_imm26 ), .Rd(\指令译码_1_rd ), .shamt(\指令译码_1_shamt ));
  // Probe on IF_PC[11:0]
  \硬布线控制器_封装  \u_硬布线控制器_封装_1  (.OP(Op), .Func(Func), .ControlSig(\硬布线控制器_封装_1_controlsig ));
  ImmExt immext_1 (
    .Imm16(\指令译码_1_imm16 ), .Imm26(\指令译码_1_imm26 ), .Imm16Out(immext_1_imm16out),
    .Imm26Out(immext_1_imm26out), .SignedExt(\硬布线控制器_封装_1_controlsig [10]));
  // Probe on ID_PC[11:0]
  // Probe on MEM_PC[11:0]
  // Probe on EX_PC[11:0]
  Multiplexer #(.select(2), .width(5), .enable("false")) multiplexer_5 (
    .in0(\指令译码_1_rt ), .in1(\指令译码_1_rd ), .in2({5{1'b1}}), .in3({5{1'b1}}), .out(multiplexer_5_out),
    .sel({\硬布线控制器_封装_1_controlsig [6], \硬布线控制器_封装_1_controlsig [7]}));
  // Probe on WB_PC[11:0]
  \拓展指令信号  \u_拓展指令信号_1  (
    .OP0(Op[0]), .OP1(Op[1]), .OP2(Op[2]), .OP3(Op[3]), .OP4(Op[4]), .OP5(Op[5]), .F0(Func[0]), .F1(Func[1]),
    .F2(Func[2]), .F3(Func[3]), .F4(Func[4]), .F5(Func[5]), .LUI(\拓展指令信号_1_lui [0]), .LH(\拓展指令信号_1_lui [1]),
    .BLTZ(\拓展指令信号_1_lui [2]));
  SelReg selreg_1 (
    .in_1(\硬布线控制器_封装_1_controlsig [11]), .Rs(\指令译码_1_rs ), .Rt(\指令译码_1_rt ), .R1_num(ID_R1_num),
    .R2_num(ID_R2_num));
  MIPS_Regifile mips_regifile_1 (
    .Din(\lui指令_1_dout ), .Clk(CLK), .R1(mips_regifile_1_r1), .R2(mips_regifile_1_r2),
    .WE(\mem_wb_1_控制信号输出 [5]), .W_num(\mem_wb_1_w_输出 ), .R1_num(ID_R1_num), .R2_num(ID_R2_num));
  and and_2 (and_2_out, Halt, \条件分支 );
  and and_3 (and_3_out, Halt, \无条件分支 );
  or or_2 (or_2_out, RST, \条件分支 , \id_ex_1_控制信号输出 [8], \LoadUse相关 );
  ID_EX id_ex_1 (
    .PC(ID_PC), .\PC输出 (EX_PC), .\传输状态In_表明当前传输数据有效 (\if_id_1_传输状态out_表明当前传输数据有效 ),
    .\传输状态Out_表明当前传输数据有效 (\id_ex_1_传输状态out_表明当前传输数据有效 ), .CLK(CLK), .\同步清零_气泡_高电平有效 (or_2_out),
    .\使能端_低电平有效_stall_高电平有效 (not_2_out), .IR(\if_id_1_ir输出 ), .\IR输出 (\id_ex_1_ir输出 ),
    .\控制信号 (\硬布线控制器_封装_1_controlsig ),
    .\控制信号输出 ({\id_ex_1_控制信号输出 [15:12], Syscall, \id_ex_1_控制信号输出 [10], JR, \id_ex_1_控制信号输出 [8:6], Ex_RegWrite, AluSrcB, \id_ex_1_控制信号输出 [3], Ex_MemToReg, \id_ex_1_控制信号输出 [1:0]}),
    .Imm16(immext_1_imm16out), .\Imm16输出 (\id_ex_1_imm16输出 ), .R1(mips_regifile_1_r1), .\R1输出 (EX_R1),
    .\R2输出 (EX_R2), .R2(mips_regifile_1_r2), .shamt(\指令译码_1_shamt ), .\shamt输出 (\id_ex_1_shamt输出 ),
    .W_num(multiplexer_5_out), .\W_输出 (Ex_WriteReg_num), .PcNext(\if_id_1_pcnext输出 ),
    .\PcNext输出_2 (\id_ex_1_pcnext输出_2 ), .Imm26(immext_1_imm26out), .\PcNext输出 (\id_ex_1_pcnext输出 ),
    .Forward(ID_Forward), .\Forward输出 ({Forward2, Forward1}), .ExtIns(\拓展指令信号_1_lui ),
    .\ExtIns输出 (\id_ex_1_extins输出 ));  // open: Hit, Hit输出
  not not_2 (not_2_out, Halt);
  Counter #(.width(16), .max('hffff)) counter_1 (
    .count(and_2_out), .Q(\条件分支成功数 ), .clk(CLK), .clr(RST));  // open: load, D, carry
  Counter #(.width(16), .max('hffff)) counter_2 (
    .count(and_3_out), .Q(\无条件分支数 ), .clk(CLK), .clr(RST));  // open: load, D, carry
  Adder #(.width(32)) adder_2 (.a(\id_ex_1_imm16输出 ), .b(\id_ex_1_pcnext输出_2 ), .out(adder_2_out));  // open: cin, cout
  Multiplexer #(.width(32), .enable("false")) multiplexer_6 (
    .in0(Redir_B), .in1(\id_ex_1_imm16输出 ), .out(multiplexer_6_out), .sel(AluSrcB));
  not not_3 (not_3_out, mips_alu_1_equal);
  MIPS_ALU mips_alu_1 (
    .X(Redir_A), .Y(multiplexer_6_out), .AluOP(\id_ex_1_控制信号输出 [15:12]), .Equal(mips_alu_1_equal),
    .Result(mips_alu_1_result), .shamt(\id_ex_1_shamt输出 ));  // open: Result_2
  Comparator #(.width(32), .mode("unsigned")) comparator_1 (.a(Redir_A), .b(32'h22), .eq(EQ));  // open: gt, lt
  // Probe on \lui指令_1_dout 
  Register #(.width(32)) register_1 (.D(Redir_B), .en(and_4_out), .Q(LedData), .clk(CLK));  // open: clr
  and and_4 (and_4_out, EQ, Syscall);
  and and_5 (and_5_out, mips_alu_1_equal, \id_ex_1_控制信号输出 [0]);
  and and_6 (and_6_out, not_3_out, \id_ex_1_控制信号输出 [1]);
  EX_MEM ex_mem_1 (
    .\控制信号 ({\id_ex_1_控制信号输出 [15:12], Syscall, \id_ex_1_控制信号输出 [10], JR, \id_ex_1_控制信号输出 [8:6], Ex_RegWrite, AluSrcB, \id_ex_1_控制信号输出 [3], Ex_MemToReg, \id_ex_1_控制信号输出 [1:0]}),
    .\控制信号输出 ({\ex_mem_1_控制信号输出 [15:6], Mem_RegWrite, \ex_mem_1_控制信号输出 [4:3], Mem_MemToReg, \ex_mem_1_控制信号输出 [1:0]}),
    .AluR(multiplexer_7_out), .\AluR输出 (MEM_AluR), .IR(\id_ex_1_ir输出 ), .\IR输出 (\ex_mem_1_ir输出 ), .PC(EX_PC),
    .\PC输出 (MEM_PC), .\传输状态In_表明当前传输数据有效 (\id_ex_1_传输状态out_表明当前传输数据有效 ),
    .\传输状态Out_表明当前传输数据有效 (\ex_mem_1_传输状态out_表明当前传输数据有效 ), .CLK(CLK), .\同步清零_气泡_高电平有效 (RST),
    .\使能端_低电平有效_stall_高电平有效 (not_4_out), .MemDin(Redir_B), .\MemDin输出 (\ex_mem_1_memdin输出 ),
    .W_num(Ex_WriteReg_num), .\W_输出 (Mem_WriteReg_num), .PcNext(\id_ex_1_pcnext输出_2 ),
    .\PcNext输出 (\ex_mem_1_pcnext输出 ), .EQ(EQ), .\EQ输出 (\ex_mem_1_eq输出 ), .ExtIns(\id_ex_1_extins输出 ),
    .\ExtIns输出 (\ex_mem_1_extins输出 ));
  Multiplexer #(.width(32), .enable("false")) multiplexer_7 (
    .in0(mips_alu_1_result), .in1({\id_ex_1_imm16输出 [15:0], {16{1'b0}}}), .out(multiplexer_7_out),
    .sel(\id_ex_1_extins输出 [0]));
  not not_4 (not_4_out, Halt);
  not not_5 (not_5_out, EQHalt);
  or or_3 (or_3_out, and_5_out, and_6_out);
  and and_7 (and_7_out, \id_ex_1_extins输出 [2], multiplexer_7_out[0]);
  and and_8 (and_8_out, Halt, \LoadUse相关 );
  and and_9 (and_9_out, not_5_out, SyscallHalt);
  or or_4 (\条件分支 , or_3_out, and_7_out);
  Counter #(.width(16), .max('hffff)) counter_3 (
    .count(Halt), .Q(\总周期数 ), .clk(CLK), .clr(RST));  // open: load, D, carry
  Counter #(.width(16), .max('hffff)) counter_4 (
    .count(and_8_out), .Q(\LoadUse次数 ), .clk(CLK), .clr(RST));  // open: load, D, carry
  D_Flip_Flop #(.trigger("high")) d_ff_1 (
    .clk(CLK), .D(and_9_out), .Q(d_ff_1_q), .en(SyscallHalt), .reset(Go));  // open: Qn, preset
  RAM #(.addrWidth(10), .dataWidth(32), .bus("separate")) ram_1 (
    .addr(MEM_AluR[11:2]), .din(\ex_mem_1_memdin输出 ), .data(ram_1_data), .str(\ex_mem_1_控制信号输出 [3]),
    .clk(CLK), .clr(RST));  // open: sel, ld
  not not_6 (Halt, d_ff_1_q);
  MEM_WB mem_wb_1 (
    .\控制信号 ({\ex_mem_1_控制信号输出 [15:6], Mem_RegWrite, \ex_mem_1_控制信号输出 [4:3], Mem_MemToReg, \ex_mem_1_控制信号输出 [1:0]}),
    .\控制信号输出 ({\mem_wb_1_控制信号输出 [15:12], SyscallHalt, \mem_wb_1_控制信号输出 [10:9], \无条件分支 , \mem_wb_1_控制信号输出 [7], WB_JAL, \mem_wb_1_控制信号输出 [5:0]}),
    .Mem(ram_1_data), .\Mem输出 (\mem_wb_1_mem输出 ), .Alu(MEM_AluR), .\Alu输出 (WB_AluR), .IR(\ex_mem_1_ir输出 ),
    .\IR输出 (\mem_wb_1_ir输出 ), .PC(MEM_PC), .\PC输出 (WB_PC),
    .\传输状态In_表明当前传输数据有效 (\ex_mem_1_传输状态out_表明当前传输数据有效 ), .CLK(CLK), .\同步清零_气泡_高电平有效 (RST),
    .\使能端_低电平有效_stall_高电平有效 (not_7_out), .W_num(Mem_WriteReg_num), .\W_输出 (\mem_wb_1_w_输出 ),
    .PcNext(\ex_mem_1_pcnext输出 ), .\PcNext输出 (WB_PcNext), .EQ(\ex_mem_1_eq输出 ), .EQ_2(EQHalt),
    .ExtIns(\ex_mem_1_extins输出 ), .\ExtIns输出 ({\mem_wb_1_extins输出 [2], LH, LUI}));  // open: 传输状态Out_表明当前传输数据有效, v0, v0输出
  not not_7 (not_7_out, Halt);
  Multiplexer #(.width(32), .enable("false")) multiplexer_8 (
    .in0(\mem_wb_1_mem输出 ), .in1(\lh指令_1_dout ), .out(WB_Mem), .sel(LH));
  Multiplexer #(.width(32), .enable("false")) multiplexer_9 (
    .in0(WB_AluR), .in1(\mem_wb_1_mem输出 ), .out(multiplexer_9_out), .sel(\mem_wb_1_控制信号输出 [2]));
  \LH指令  \lh指令_1  (.Dout(\lh指令_1_dout ), .Din(multiplexer_9_out), .LH(LH), .SEL(WB_AluR[1]));
  \LUI指令  \lui指令_1  (
    .Imm16(\mem_wb_1_ir输出 [15:0]), .Dout(\lui指令_1_dout ), .Din(\lh指令_1_dout ), .PcNext(WB_PcNext),
    .JAL(WB_JAL), .LUI(LUI));

  // Other names for the same wires on the sheet: v0[31:0] = Redir_B

  // Notes on the sheet:
  //   中断源
  //   0:Beq
  //   1:Bne
  //   2:MemToReg
  //   3:MemWrite
  //   4:AluSrcB
  //   5:RegWrite
  //   6:JAL
  //   7:RegDst
  //   8:JMP
  //   9:JR
  //   10:SignedExt
  //   11:Syscall
  //   12-15:AluOp
  //   中断等待指示
  //   数码管输出
  //   指令存储器
  //   contents of rom_1 (hex, n*v repeats v):
  //   20110001 8100005 20110001 20120002 20130003 8100009 20110001 20120002 20130003 810000d 20110001
  //   20120002 20130003 8100011 20110001 20120002 20130003 c1000fc 20100001 20110001 118fc0 112020
  //   20020022 c 118882 12200001 8100015 112020 20020022 c 20110001 118880 112020 20020022 c 12200001
  //   810001f 20110001 118fc0 112020 20020022 c 1188c3 112020 20020022 c 118903 112020 20020022 c 118903
  //   112020 20020022 c 118903 112020 20020022 c 118903 112020 20020022 c 118903 112020 20020022 c 118903
  //   112020 20020022 c 118903 112020 20020022 c 20100001 109fc0 139fc3 8021 2012000c 24160003 26100001
  //   3210000f 20080008 20090001 139900 2709825 132020 20020022 c 1094022 1500fff9 22100001 2018000f
  //   2188024 108700 20080008 20090001 139902 2709825 132021 20020022 c 1094022 1500fff9 108702 2c9b022
  //   12c00001 8100050 4020 1084027 84400 3508ffff 82021 20020022 c 2010ffff 20110000 ae300000 22100001
  //   22310004 ae300000 22100001 22310004 ae300000 22100001 22310004 ae300000 22100001 22310004 ae300000
  //   22100001 22310004 ae300000 22100001 22310004 ae300000 22100001 22310004 ae300000 22100001 22310004
  //   ae300000 22100001 22310004 ae300000 22100001 22310004 ae300000 22100001 22310004 ae300000 22100001
  //   22310004 ae300000 22100001 22310004 ae300000 22100001 22310004 ae300000 22100001 22310004 ae300000
  //   22100001 22310004 22100001 8020 2011003c 8e130000 8e340000 274402a 11000002 ae330000 ae140000
  //   2231fffc 1611fff8 102020 20020022 c 22100004 2011003c 1611fff2 20020032 c 2008ffff 20117777 112020
  //   20020022 c 200b0010 2288826 112020 20020022 c 216bffff 1560fffa 2002000a c 200b0008 3c11fedc
  //   3631ffff 112020 20020022 c 3c11ba98 112020 c 3c117654 112020 c 3c113210 112020 c 216bffff 1560fff0
  //   2002000a c 0 0 0 20090000 200b0010 34118483 20120404 118c00 129400 36318281 22520404 ad310000
  //   2328820 21290004 216bffff 1560fffb 200b0020 20090000 85310000 112020 20020022 c 21290002 216bffff
  //   1560fff9 2002000a c 2011fff1 112020 20020022 c 22310001 620fffb 2002000a c 20100000 22100001 102020
  //   20020022 c 22100002 102020 20020022 c 22100003 102020 20020022 c 22100004 102020 20020022 c 22100005
  //   102020 20020022 c 22100006 102020 20020022 c 22100007 102020 20020022 c 22100008 102020 20020022
  //   20020022 c 3e00008
  //   SignedExt
  //   流水调试日志用
  //   RegDst
  //   JAL
  //   Syscall
  //   RegWrite
  //   JAL
  //   无条件分支
  //   AlcSrcB
  //   BNE+BEQ
  //   BLTZ
  //   MemWrite
endmodule

module \动态分支预测  (
);

  wire AluSrcB, and_1_out, and_2_out, and_3_out, and_4_out, and_6_out, and_7_out, and_8_out, and_9_out,
       and_10_out, and_11_out, and_12_out, and_13_out, and_14_out, and_15_out, and_16_out, and_17_out,
       and_18_out, and_19_out, and_20_out, \cache全相连_1_miss , CLK, comparator_1_eq, comparator_2_eq,
       comparator_4_eq, comparator_5_eq, d_ff_1_q, EQ, EQHalt, EX_Hit, \ex_mem_1_eq输出 ,
       \ex_mem_1_传输状态out_表明当前传输数据有效 , Ex_MemToReg, Ex_RegWrite, Go, Halt, Hit, \id_ex_1_传输状态out_表明当前传输数据有效 ,
       \if_id_1_hit输出 , \if_id_1_传输状态out_表明当前传输数据有效 , IR1, IR2, IR3, JR, L1Rst, L2Rst, LH, \LoadUse相关 , LUI,
       Mem_MemToReg, Mem_RegWrite, mips_alu_1_equal, not_1_out, not_3_out, not_4_out, not_5_out, not_6_out,
       not_8_out, or_2_out, or_8_out, RST, Syscall, SyscallHalt, W1, W2, W3, WB_JAL, \产生气泡 , \无条件分支 ,
       \无条件跳转指令 , \条件分支 , \条件跳转指令 , \预测失败 , \预测成功 ;
  wire [1:0] Forward1, Forward2;
  wire [2:0] \ex_mem_1_extins输出 , \id_ex_1_extins输出 , \拓展指令信号_1_lui ;
  wire [2:2] \mem_wb_1_extins输出 ;
  wire [3:0] ID_Forward;
  wire [4:0] Ex_WriteReg_num, \id_ex_1_shamt输出 , ID_R1_num, ID_R2_num, \mem_wb_1_w_输出 , Mem_WriteReg_num,
       multiplexer_9_out, \指令译码_1_rd , \指令译码_1_rs , \指令译码_1_rt , \指令译码_1_shamt ;
  wire [5:0] Func, Op;
  wire [9:0] multiplexer_7_out;
  wire [15:0] \B指令气泡数 , \ex_mem_1_控制信号输出 , \id_ex_1_控制信号输出 , \LoadUse次数 , \mem_wb_1_控制信号输出 , \命中次数 , \总周期数 ,
       \指令译码_1_imm16 , \无条件分支数 , \条件分支成功数 , \硬布线控制器_封装_1_controlsig , \预测成功次数 ;
  wire [25:0] \指令译码_1_imm26 ;
  wire [31:0] adder_1_out, adder_2_out, \ex_mem_1_ir输出 , \ex_mem_1_memdin输出 , \ex_mem_1_pcnext输出 , EX_PC,
       Ex_PcNext, EX_R1, EX_R2, HitData, \id_ex_1_imm16输出 , \id_ex_1_ir输出 , \id_ex_1_pcnext输出 , ID_PC,
       \if_id_1_ir输出 , \if_id_1_pcnext输出 , IF_PC, immext_1_imm16out, immext_1_imm26out, LedData,
       \lh指令_1_dout , \lui指令_1_dout , MEM_AluR, MEM_PC, \mem_wb_1_ir输出 , \mem_wb_1_mem输出 , mips_alu_1_result,
       mips_regifile_1_r1, mips_regifile_1_r2, multiplexer_1_out, multiplexer_3_out, multiplexer_4_out,
       multiplexer_8_out, multiplexer_11_out, multiplexer_12_out, multiplexer_14_out, ram_1_data, Redir_A,
       Redir_B, rom_1_data, WB_AluR, WB_Mem, WB_PC, WB_PcNext, \无条件跳转地址 , \条件跳转地址 ;

  Button \u_总复位  (.out(RST));
  Button _1 (.out(IR1));
  Button _2 (.out(IR2));
  Button _3 (.out(IR3));
  Button \u_继续运行  (.out(Go));
  LED led_1 (.in(W1));
  LED led_2 (.in(W2));
  LED led_3 (.in(W3));
  and and_1 (and_1_out, \无条件跳转指令 , \预测失败 );
  Multiplexer #(.width(32), .enable("false")) multiplexer_1 (
    .in0(multiplexer_4_out), .in1(\无条件跳转地址 ), .out(multiplexer_1_out), .sel(and_1_out));
  Multiplexer #(.width(32), .enable("false")) multiplexer_2 (
    .in0(\id_ex_1_pcnext输出 ), .in1(EX_R1), .out(\无条件跳转地址 ), .sel(JR));
  Hex_Digit_Display hex_digit_display_1 (.value(LedData[31:28]));  // open: dp
  and and_2 (and_2_out, \条件跳转指令 , \预测失败 );
  Hex_Digit_Display hex_digit_display_2 (.value(LedData[23:20]));  // open: dp
  Hex_Digit_Display hex_digit_display_3 (.value(LedData[27:24]));  // open: dp
  Register #(.width(32)) PC (.D(multiplexer_3_out), .en(and_3_out), .Q(IF_PC), .clk(CLK), .clr(RST));
  Multiplexer #(.width(32), .enable("false")) multiplexer_3 (
    .in0(multiplexer_1_out), .in1(\条件跳转地址 ), .out(multiplexer_3_out), .sel(and_2_out));
  and and_3 (and_3_out, Halt, not_1_out);
  not not_1 (not_1_out, \LoadUse相关 );
  Hex_Digit_Display hex_digit_display_4 (.value(LedData[15:12]));  // open: dp
  Hex_Digit_Display hex_digit_display_5 (.value(LedData[19:16]));  // open: dp
  \重定向检测  \u_重定向检测_1  (
    .OP(Op), .EX_WriteReg_num(Ex_WriteReg_num), .EX_RegWrite(Ex_RegWrite), .Load_use(\LoadUse相关 ),
    .ID_R1_num(ID_R1_num), .MEM_RegWrite(Mem_RegWrite), .forwardR1(ID_Forward[1:0]), .Func(Func),
    .ID_R2_num(ID_R2_num), .EX_MemToReg(Ex_MemToReg), .forwardR2(ID_Forward[3:2]),
    .MEM_W_num(Mem_WriteReg_num), .MEM_MemToReg(Mem_MemToReg));
  Multiplexer #(.width(32), .enable("false")) multiplexer_4 (
    .in0(adder_1_out), .in1(HitData), .out(multiplexer_4_out), .sel(Hit));
  Hex_Digit_Display hex_digit_display_6 (.value(LedData[11:8]));  // open: dp
  Hex_Digit_Display hex_digit_display_7 (.value(LedData[7:4]));  // open: dp
  Clock clock_1 (.out(CLK));
  // Probe on Forward1
  Multiplexer #(.select(2), .width(32), .enable("false")) multiplexer_5 (
    .in0(EX_R1), .in1(WB_Mem), .in2(WB_AluR), .in3(MEM_AluR), .out(Redir_A), .sel(Forward1));
  // Probe on Forward2
  Multiplexer #(.select(2), .width(32), .enable("false")) multiplexer_6 (
    .in0(EX_R2), .in1(WB_Mem), .in2(WB_AluR), .in3(MEM_AluR), .out(Redir_B), .sel(Forward2));
  Hex_Digit_Display hex_digit_display_8 (.value(LedData[3:0]));  // open: dp
  Adder #(.width(32)) adder_1 (.a(32'h1), .b(IF_PC), .out(adder_1_out));  // open: cin, cout
  ROM #(.addrWidth(10), .dataWidth(32)) rom_1 (.addr(IF_PC[9:0]), .data(rom_1_data));  // open: sel
  Multiplexer #(.width(10), .enable("false")) multiplexer_7 (
    .in0(IF_PC[9:0]), .in1(EX_PC[9:0]), .out(multiplexer_7_out), .sel(\预测失败 ));
  // OR_Gate or_1 has open pins: in0=RST, in1=\条件跳转指令 , in2=\无条件跳转指令 , out=open
  IF_ID if_id_1 (
    .IR(rom_1_data), .\IR输出 (\if_id_1_ir输出 ), .PC(IF_PC), .\PC输出 (ID_PC), .\传输状态In_表明当前传输数据有效 (1'b1),
    .\传输状态Out_表明当前传输数据有效 (\if_id_1_传输状态out_表明当前传输数据有效 ), .CLK(CLK), .\同步清零_气泡_高电平有效 (L1Rst),
    .\使能端_低电平有效_stall_高电平有效 (\LoadUse相关 ), .PcNext(adder_1_out), .\PcNext输出 (\if_id_1_pcnext输出 ), .Hit(Hit),
    .\Hit输出 (\if_id_1_hit输出 ));
  // Probe on \总周期数 
  // Probe on \无条件分支数 
  // Probe on \条件分支成功数 
  // Probe on \命中次数 
  // Probe on \LoadUse次数 
  // Probe on \预测成功次数 
  // Probe on \B指令气泡数 
  \指令译码  \u_指令译码_1  (
    .Op(Op), .Imm16(\指令译码_1_imm16 ), .Func(Func), .Rs(\指令译码_1_rs ), .Instruction(\if_id_1_ir输出 ),
    .Rt(\指令译码_1_rt ), .Imm26(\指令译码_1_imm26 ), .Rd(\指令译码_1_rd ), .shamt(\指令译码_1_shamt ));
  \Cache全相连  \cache全相连_1  (
    .BlockDataIn(multiplexer_8_out), .Addr(multiplexer_7_out), .BlkDataReady(and_4_out), .CLK(CLK),
    .Enable(Halt), .Miss(\cache全相连_1_miss ), .DataOut(HitData));
  // Probe on IF_PC[11:0]
  \硬布线控制器_封装  \u_硬布线控制器_封装_1  (.OP(Op), .Func(Func), .ControlSig(\硬布线控制器_封装_1_controlsig ));
  ImmExt immext_1 (
    .Imm16(\指令译码_1_imm16 ), .Imm26(\指令译码_1_imm26 ), .Imm16Out(immext_1_imm16out),
    .Imm26Out(immext_1_imm26out), .SignedExt(\硬布线控制器_封装_1_controlsig [10]));
  not not_2 (Hit, \cache全相连_1_miss );
  and and_4 (and_4_out, \预测失败 , ~Hit);  // AND_Gate
  or or_2 (or_2_out, \无条件跳转指令 , \条件跳转指令 );
  // Probe on ID_PC[11:0]
  Multiplexer #(.width(32), .enable("false")) multiplexer_8 (
    .in0(\条件跳转地址 ), .in1(\无条件跳转地址 ), .out(multiplexer_8_out), .sel(\无条件跳转指令 ));
  and and_5 (\产生气泡 , or_2_out, ~\预测成功 );  // AND_Gate
  // Probe on EX_PC[11:0]
  // Probe on MEM_PC[11:0]
  Multiplexer #(.select(2), .width(5), .enable("false")) multiplexer_9 (
    .in0(\指令译码_1_rt ), .in1(\指令译码_1_rd ), .in2({5{1'b1}}), .in3({5{1'b1}}), .out(multiplexer_9_out),
    .sel({\硬布线控制器_封装_1_controlsig [6], \硬布线控制器_封装_1_controlsig [7]}));
  // Probe on WB_PC[11:0]
  \拓展指令信号  \u_拓展指令信号_1  (
    .OP0(Op[0]), .OP1(Op[1]), .OP2(Op[2]), .OP3(Op[3]), .OP4(Op[4]), .OP5(Op[5]), .F0(Func[0]), .F1(Func[1]),
    .F2(Func[2]), .F3(Func[3]), .F4(Func[4]), .F5(Func[5]), .LUI(\拓展指令信号_1_lui [0]), .LH(\拓展指令信号_1_lui [1]),
    .BLTZ(\拓展指令信号_1_lui [2]));
  or or_3 (L1Rst, RST, \产生气泡 );
  or or_4 (L2Rst, L1Rst, \LoadUse相关 );
  SelReg selreg_1 (
    .in_1(\硬布线控制器_封装_1_controlsig [11]), .Rs(\指令译码_1_rs ), .Rt(\指令译码_1_rt ), .R1_num(ID_R1_num),
    .R2_num(ID_R2_num));
  MIPS_Regifile mips_regifile_1 (
    .Din(\lui指令_1_dout ), .Clk(CLK), .R1(mips_regifile_1_r1), .R2(mips_regifile_1_r2),
    .WE(\mem_wb_1_控制信号输出 [5]), .W_num(\mem_wb_1_w_输出 ), .R1_num(ID_R1_num), .R2_num(ID_R2_num));
  and and_6 (and_6_out, Halt, \条件分支 );
  and and_7 (and_7_out, Halt, \无条件分支 );
  and and_8 (and_8_out, Halt, \预测成功 , EX_Hit);
  // OR_Gate or_5 has open pins: in0=RST, in1=\条件跳转指令 , in2=\无条件跳转指令 , in3=\LoadUse相关 , out=open
  ID_EX id_ex_1 (
    .PC(ID_PC), .\PC输出 (EX_PC), .\传输状态In_表明当前传输数据有效 (\if_id_1_传输状态out_表明当前传输数据有效 ),
    .\传输状态Out_表明当前传输数据有效 (\id_ex_1_传输状态out_表明当前传输数据有效 ), .CLK(CLK), .\同步清零_气泡_高电平有效 (L2Rst),
    .\使能端_低电平有效_stall_高电平有效 (not_3_out), .IR(\if_id_1_ir输出 ), .\IR输出 (\id_ex_1_ir输出 ),
    .\控制信号 (\硬布线控制器_封装_1_controlsig ),
    .\控制信号输出 ({\id_ex_1_控制信号输出 [15:12], Syscall, \id_ex_1_控制信号输出 [10], JR, \无条件跳转指令 , \id_ex_1_控制信号输出 [7:6], Ex_RegWrite, AluSrcB, \id_ex_1_控制信号输出 [3], Ex_MemToReg, \id_ex_1_控制信号输出 [1:0]}),
    .Imm16(immext_1_imm16out), .\Imm16输出 (\id_ex_1_imm16输出 ), .R1(mips_regifile_1_r1), .\R1输出 (EX_R1),
    .\R2输出 (EX_R2), .R2(mips_regifile_1_r2), .shamt(\指令译码_1_shamt ), .\shamt输出 (\id_ex_1_shamt输出 ),
    .W_num(multiplexer_9_out), .\W_输出 (Ex_WriteReg_num), .PcNext(\if_id_1_pcnext输出 ),
    .\PcNext输出_2 (Ex_PcNext), .Imm26(immext_1_imm26out), .\PcNext输出 (\id_ex_1_pcnext输出 ),
    .Forward(ID_Forward), .\Forward输出 ({Forward2, Forward1}), .ExtIns(\拓展指令信号_1_lui ),
    .\ExtIns输出 (\id_ex_1_extins输出 ), .Hit(\if_id_1_hit输出 ), .\Hit输出 (EX_Hit));
  not not_3 (not_3_out, Halt);
  Counter #(.width(16), .max('hffff)) counter_1 (
    .count(and_6_out), .Q(\条件分支成功数 ), .clk(CLK), .clr(RST));  // open: load, D, carry
  Counter #(.width(16), .max('hffff)) counter_2 (
    .count(and_7_out), .Q(\无条件分支数 ), .clk(CLK), .clr(RST));  // open: load, D, carry
  Counter #(.width(16), .max('hffff)) counter_3 (
    .count(and_8_out), .Q(\预测成功次数 ), .clk(CLK), .clr(RST));  // open: load, D, carry
  Multiplexer #(.width(32), .enable("false")) multiplexer_10 (
    .in0(Ex_PcNext), .in1(adder_2_out), .out(\条件跳转地址 ), .sel(\条件分支 ));
  Comparator #(.width(10)) comparator_1 (.a(\无条件跳转地址 [9:0]), .b(ID_PC[9:0]), .eq(comparator_1_eq));  // open: gt, lt
  Comparator #(.width(10)) comparator_2 (.a(\条件跳转地址 [9:0]), .b(ID_PC[9:0]), .eq(comparator_2_eq));  // open: gt, lt
  or or_6 (\条件跳转指令 , \id_ex_1_控制信号输出 [0], \id_ex_1_控制信号输出 [1], \id_ex_1_extins输出 [2]);
  Adder #(.width(32)) adder_2 (.a(\id_ex_1_imm16输出 ), .b(Ex_PcNext), .out(adder_2_out));  // open: cin, cout
  Multiplexer #(.width(32), .enable("false")) multiplexer_11 (
    .in0(Redir_B), .in1(\id_ex_1_imm16输出 ), .out(multiplexer_11_out), .sel(AluSrcB));
  and and_9 (and_9_out, \无条件跳转指令 , comparator_1_eq);
  and and_10 (and_10_out, \条件跳转指令 , comparator_2_eq);
  not not_4 (not_4_out, mips_alu_1_equal);
  MIPS_ALU mips_alu_1 (
    .X(Redir_A), .Y(multiplexer_11_out), .AluOP(\id_ex_1_控制信号输出 [15:12]), .Equal(mips_alu_1_equal),
    .Result(mips_alu_1_result), .shamt(\id_ex_1_shamt输出 ));  // open: Result_2
  Comparator #(.width(32), .mode("unsigned")) comparator_3 (.a(Redir_A), .b(32'h22), .eq(EQ));  // open: gt, lt
  or or_7 (\预测成功 , and_9_out, and_10_out);
  Register #(.width(32)) register_1 (.D(Redir_B), .en(and_11_out), .Q(LedData), .clk(CLK));  // open: clr
  and and_11 (and_11_out, EQ, Syscall);
  and and_12 (and_12_out, mips_alu_1_equal, \id_ex_1_控制信号输出 [0]);
  and and_13 (and_13_out, not_4_out, \id_ex_1_控制信号输出 [1]);
  EX_MEM ex_mem_1 (
    .\控制信号 ({\id_ex_1_控制信号输出 [15:12], Syscall, \id_ex_1_控制信号输出 [10], JR, \无条件跳转指令 , \id_ex_1_控制信号输出 [7:6], Ex_RegWrite, AluSrcB, \id_ex_1_控制信号输出 [3], Ex_MemToReg, \id_ex_1_控制信号输出 [1:0]}),
    .\控制信号输出 ({\ex_mem_1_控制信号输出 [15:6], Mem_RegWrite, \ex_mem_1_控制信号输出 [4:3], Mem_MemToReg, \ex_mem_1_控制信号输出 [1:0]}),
    .AluR(multiplexer_12_out), .\AluR输出 (MEM_AluR), .IR(\id_ex_1_ir输出 ), .\IR输出 (\ex_mem_1_ir输出 ),
    .PC(EX_PC), .\PC输出 (MEM_PC), .\传输状态In_表明当前传输数据有效 (\id_ex_1_传输状态out_表明当前传输数据有效 ),
    .\传输状态Out_表明当前传输数据有效 (\ex_mem_1_传输状态out_表明当前传输数据有效 ), .CLK(CLK), .\同步清零_气泡_高电平有效 (RST),
    .\使能端_低电平有效_stall_高电平有效 (not_5_out), .MemDin(Redir_B), .\MemDin输出 (\ex_mem_1_memdin输出 ),
    .W_num(Ex_WriteReg_num), .\W_输出 (Mem_WriteReg_num), .PcNext(Ex_PcNext), .\PcNext输出 (\ex_mem_1_pcnext输出 ),
    .EQ(EQ), .\EQ输出 (\ex_mem_1_eq输出 ), .ExtIns(\id_ex_1_extins输出 ), .\ExtIns输出 (\ex_mem_1_extins输出 ));
  Multiplexer #(.width(32), .enable("false")) multiplexer_12 (
    .in0(mips_alu_1_result), .in1({\id_ex_1_imm16输出 [15:0], {16{1'b0}}}), .out(multiplexer_12_out),
    .sel(\id_ex_1_extins输出 [0]));
  not not_5 (not_5_out, Halt);
  not not_6 (not_6_out, EQHalt);
  or or_8 (or_8_out, and_12_out, and_13_out);
  and and_14 (and_14_out, \id_ex_1_extins输出 [2], multiplexer_12_out[0]);
  and and_15 (and_15_out, Halt, \LoadUse相关 );
  and and_16 (and_16_out, not_6_out, SyscallHalt);
  or or_9 (\条件分支 , or_8_out, and_14_out);
  Comparator #(.width(10)) comparator_4 (.a(\无条件跳转地址 [9:0]), .b(ID_PC[9:0]), .eq(comparator_4_eq));  // open: gt, lt
  Comparator #(.width(10)) comparator_5 (.a(\条件跳转地址 [9:0]), .b(ID_PC[9:0]), .eq(comparator_5_eq));  // open: gt, lt
  Counter #(.width(16), .max('hffff)) counter_4 (
    .count(Halt), .Q(\总周期数 ), .clk(CLK), .clr(RST));  // open: load, D, carry
  Counter #(.width(16), .max('hffff)) counter_5 (
    .count(and_15_out), .Q(\LoadUse次数 ), .clk(CLK), .clr(RST));  // open: load, D, carry
  D_Flip_Flop #(.trigger("high")) d_ff_1 (
    .clk(CLK), .D(and_16_out), .Q(d_ff_1_q), .en(SyscallHalt), .reset(Go));  // open: Qn, preset
  RAM #(.addrWidth(10), .dataWidth(32), .bus("separate")) ram_1 (
    .addr(MEM_AluR[11:2]), .din(\ex_mem_1_memdin输出 ), .data(ram_1_data), .str(\ex_mem_1_控制信号输出 [3]),
    .clk(CLK), .clr(RST));  // open: sel, ld
  and and_17 (and_17_out, \无条件跳转指令 , ~comparator_4_eq);  // AND_Gate
  and and_18 (and_18_out, \条件跳转指令 , ~comparator_5_eq);  // AND_Gate
  not not_7 (Halt, d_ff_1_q);
  MEM_WB mem_wb_1 (
    .\控制信号 ({\ex_mem_1_控制信号输出 [15:6], Mem_RegWrite, \ex_mem_1_控制信号输出 [4:3], Mem_MemToReg, \ex_mem_1_控制信号输出 [1:0]}),
    .\控制信号输出 ({\mem_wb_1_控制信号输出 [15:12], SyscallHalt, \mem_wb_1_控制信号输出 [10:9], \无条件分支 , \mem_wb_1_控制信号输出 [7], WB_JAL, \mem_wb_1_控制信号输出 [5:0]}),
    .Mem(ram_1_data), .\Mem输出 (\mem_wb_1_mem输出 ), .Alu(MEM_AluR), .\Alu输出 (WB_AluR), .IR(\ex_mem_1_ir输出 ),
    .\IR输出 (\mem_wb_1_ir输出 ), .PC(MEM_PC), .\PC输出 (WB_PC),
    .\传输状态In_表明当前传输数据有效 (\ex_mem_1_传输状态out_表明当前传输数据有效 ), .CLK(CLK), .\同步清零_气泡_高电平有效 (RST),
    .\使能端_低电平有效_stall_高电平有效 (not_8_out), .W_num(Mem_WriteReg_num), .\W_输出 (\mem_wb_1_w_输出 ),
    .PcNext(\ex_mem_1_pcnext输出 ), .\PcNext输出 (WB_PcNext), .EQ(\ex_mem_1_eq输出 ), .EQ_2(EQHalt),
    .ExtIns(\ex_mem_1_extins输出 ), .\ExtIns输出 ({\mem_wb_1_extins输出 [2], LH, LUI}));  // open: 传输状态Out_表明当前传输数据有效, v0, v0输出
  not not_8 (not_8_out, Halt);
  or or_10 (\预测失败 , and_17_out, and_18_out);
  and and_19 (and_19_out, ~\预测成功 , ~\条件分支 , \条件跳转指令 );  // AND_Gate
  Multiplexer #(.width(32), .enable("false")) multiplexer_13 (
    .in0(\mem_wb_1_mem输出 ), .in1(\lh指令_1_dout ), .out(WB_Mem), .sel(LH));
  and and_20 (and_20_out, Halt, Hit);
  Counter #(.width(16), .max('hffff)) counter_6 (
    .count(and_19_out), .Q(\B指令气泡数 ), .clk(CLK), .clr(RST));  // open: load, D, carry
  Multiplexer #(.width(32), .enable("false")) multiplexer_14 (
    .in0(WB_AluR), .in1(\mem_wb_1_mem输出 ), .out(multiplexer_14_out), .sel(\mem_wb_1_控制信号输出 [2]));
  Counter #(.width(16), .max('hffff)) counter_7 (
    .count(and_20_out), .Q(\命中次数 ), .clk(CLK), .clr(RST));  // open: load, D, carry
  \LH指令  \lh指令_1  (.Dout(\lh指令_1_dout ), .Din(multiplexer_14_out), .LH(LH), .SEL(WB_AluR[1]));
  \LUI指令  \lui指令_1  (
    .Imm16(\mem_wb_1_ir输出 [15:0]), .Dout(\lui指令_1_dout ), .Din(\lh指令_1_dout ), .PcNext(WB_PcNext),
    .JAL(WB_JAL), .LUI(LUI));

  // Other names for the same wires on the sheet: v0[31:0] = Redir_B

  // Notes on the sheet:
  //   中断源
  //   0:Beq
  //   1:Bne
  //   2:MemToReg
  //   3:MemWrite
  //   4:AluSrcB
  //   5:RegWrite
  //   6:JAL
  //   7:RegDst
  //   8:JMP
  //   9:JR
  //   10:SignedExt
  //   11:Syscall
  //   12-15:AluOp
  //   中断等待指示
  //   数码管输出
  //   指令存储器
  //   contents of rom_1 (hex, n*v repeats v):
  //   20110001 8100005 20110001 20120002 20130003 8100009 20110001 20120002 20130003 810000d 20110001
  //   20120002 20130003 8100011 20110001 20120002 20130003 c1000fc 20100001 20110001 118fc0 112020
  //   20020022 c 118882 12200001 8100015 112020 20020022 c 20110001 118880 112020 20020022 c 12200001
  //   810001f 20110001 118fc0 112020 20020022 c 1188c3 112020 20020022 c 118903 112020 20020022 c 118903
  //   112020 20020022 c 118903 112020 20020022 c 118903 112020 20020022 c 118903 112020 20020022 c 118903
  //   112020 20020022 c 118903 112020 20020022 c 20100001 109fc0 139fc3 8021 2012000c 24160003 26100001
  //   3210000f 20080008 20090001 139900 2709825 132020 20020022 c 1094022 1500fff9 22100001 2018000f
  //   2188024 108700 20080008 20090001 139902 2709825 132021 20020022 c 1094022 1500fff9 108702 2c9b022
  //   12c00001 8100050 4020 1084027 84400 3508ffff 82021 20020022 c 2010ffff 20110000 ae300000 22100001
  //   22310004 ae300000 22100001 22310004 ae300000 22100001 22310004 ae300000 22100001 22310004 ae300000
  //   22100001 22310004 ae300000 22100001 22310004 ae300000 22100001 22310004 ae300000 22100001 22310004
  //   ae300000 22100001 22310004 ae300000 22100001 22310004 ae300000 22100001 22310004 ae300000 22100001
  //   22310004 ae300000 22100001 22310004 ae300000 22100001 22310004 ae300000 22100001 22310004 ae300000
  //   22100001 22310004 22100001 8020 2011003c 8e130000 8e340000 274402a 11000002 ae330000 ae140000
  //   2231fffc 1611fff8 102020 20020022 c 22100004 2011003c 1611fff2 20020032 c 2008ffff 20117777 112020
  //   20020022 c 200b0010 2288826 112020 20020022 c 216bffff 1560fffa 2002000a c 200b0008 3c11fedc
  //   3631ffff 112020 20020022 c 3c11ba98 112020 c 3c117654 112020 c 3c113210 112020 c 216bffff 1560fff0
  //   2002000a c 0 0 0 20090000 200b0010 34118483 20120404 118c00 129400 36318281 22520404 ad310000
  //   2328820 21290004 216bffff 1560fffb 200b0020 20090000 85310000 112020 20020022 c 21290002 216bffff
  //   1560fff9 2002000a c 2011fff1 112020 20020022 c 22310001 620fffb 2002000a c 20100000 22100001 102020
  //   20020022 c 22100002 102020 20020022 c 22100003 102020 20020022 c 22100004 102020 20020022 c 22100005
  //   102020 20020022 c 22100006 102020 20020022 c 22100007 102020 20020022 c 22100008 102020 20020022
  //   20020022 c 3e00008
  //   29
  //   SignedExt
  //   流水调试日志用
  //   RegDst
  //   JAL
  //   Syscall
  //   RegWrite
  //   JAL
  //   无条件分支
  //   AlcSrcB
  //   BNE+BEQ
  //   BLTZ
  //   MemWrite
endmodule

module \指令译码  (
  input  [31:0] Instruction,
  output [5:0] Op,
  output [15:0] Imm16,
  output [5:0] Func,
  output [4:0] Rs,
  output [4:0] Rt,
  output [25:0] Imm26,
  output [4:0] Rd,
  output [4:0] shamt
);


  assign Func = Instruction[5:0];
  assign Imm16 = Instruction[15:0];
  assign Imm26 = Instruction[25:0];
  assign Op = Instruction[31:26];
  assign Rd = Instruction[15:11];
  assign Rs = Instruction[25:21];
  assign Rt = Instruction[20:16];
  assign shamt = Instruction[10:6];

  // Other names for the same wires on the sheet: 指令[31:0] = Instruction
endmodule

module SelReg (
  input  in_1,
  input  [4:0] Rs,
  input  [4:0] Rt,
  output [4:0] R1_num,
  output [4:0] R2_num
);

  Multiplexer #(.width(5), .enable("false")) multiplexer_1 (.in0(Rs), .in1(5'b00010), .out(R1_num), .sel(in_1));
  Multiplexer #(.width(5), .enable("false")) multiplexer_2 (.in0(Rt), .in1(5'b00100), .out(R2_num), .sel(in_1));

  // Other names for the same wires on the sheet: Syscall = in_1
endmodule

// 控制器
module \硬布线控制器_封装  (
  input  [5:0] OP,
  input  [5:0] Func,
  output [15:0] ControlSig
);

  // Probe on OP
  \运算控制器  \u_运算控制器_1  (
    .OP0(OP[0]), .OP1(OP[1]), .OP2(OP[2]), .OP3(OP[3]), .OP4(OP[4]), .OP5(OP[5]), .F0(Func[0]), .F1(Func[1]),
    .F2(Func[2]), .F3(Func[3]), .F4(Func[4]), .F5(Func[5]), .S0(ControlSig[12]), .S1(ControlSig[13]),
    .S2(ControlSig[14]), .S3(ControlSig[15]));
  \控制信号生成  \u_控制信号生成_1  (
    .OP0(OP[0]), .OP1(OP[1]), .OP2(OP[2]), .OP3(OP[3]), .OP4(OP[4]), .OP5(OP[5]), .F0(Func[0]), .F1(Func[1]),
    .F2(Func[2]), .F3(Func[3]), .F4(Func[4]), .F5(Func[5]), .MemToReg(ControlSig[2]),
    .MemWrite(ControlSig[3]), .ALU_SRC(ControlSig[4]), .RegWrite(ControlSig[5]), .SysCALL(ControlSig[11]),
    .SignedExt(ControlSig[10]), .RegDst(ControlSig[7]), .BEQ(ControlSig[0]), .BNE(ControlSig[1]),
    .JR(ControlSig[9]), .JMP(ControlSig[8]), .JAL(ControlSig[6]));
  // Probe on Func
  // Probe on ControlSig[15:12]

  // Other names for the same wires on the sheet: Beq = ControlSig[0]; Bne = ControlSig[1]; MemToReg = ControlSig[2];
  //   MemWrite = ControlSig[3]; ALU_SRC = ControlSig[4]; RegWrite = ControlSig[5]; JAL = ControlSig[6];
  //   RegDst = ControlSig[7]; JMP = ControlSig[8]; JR = ControlSig[9]; SignedExt = ControlSig[10];
  //   Syscall = ControlSig[11]; ALU_OP[3:0] = ControlSig[15:12]; OP_CODE[5:0] = OP

  // Notes on the sheet:
  //   运算器控制器，根据指令生成运算器功能选择信号
  //   控制信号生成，产生数据通路需要的其他控制信号
endmodule

module ImmExt (
  input  SignedExt,
  input  [15:0] Imm16,
  input  [25:0] Imm26,
  output [31:0] Imm16Out,
  output [31:0] Imm26Out
);

  wire and_1_out;

  and and_1 (and_1_out, Imm16[15], SignedExt);
  assign Imm26Out = {{6{Imm26[25]}}, Imm26};  // Bit_Extender bit_extender_1
  assign Imm16Out = {{16{and_1_out}}, Imm16};  // Bit_Extender bit_extender_2
endmodule

module \重定向检测  (
  input  EX_RegWrite,
  input  EX_MemToReg,
  input  [4:0] EX_WriteReg_num,
  input  [5:0] OP,
  input  [5:0] Func,
  input  MEM_RegWrite,
  input  MEM_MemToReg,
  input  [4:0] MEM_W_num,
  input  [4:0] ID_R1_num,
  input  [4:0] ID_R2_num,
  output Load_use,
  output [1:0] forwardR1,
  output [1:0] forwardR2
);

  wire and_4_out, and_5_out, case0_R1, case0_R2, case1_R1, case1_R2, case2_R1, case2_R2, case3_R1, case3_R2,
       comparator_1_eq, comparator_2_eq, comparator_3_eq, comparator_4_eq, comparator_5_eq, comparator_6_eq,
       comparator_7_eq, comparator_10_eq, comparator_11_eq, comparator_12_eq, not_1_out, not_2_out,
       not_3_out, not_4_out, or_1_out, R1_Used, R2_Used;
  wire [1:0] multiplexer_1_out, multiplexer_2_out, multiplexer_3_out, multiplexer_5_out, multiplexer_6_out,
       multiplexer_7_out;

  Multiplexer #(.width(2), .enable("false")) multiplexer_1 (
    .in0(2'b00), .in1(2'b01), .out(multiplexer_1_out), .sel(case1_R1));
  Comparator #(.width(5)) comparator_1 (.a(ID_R1_num), .b(MEM_W_num), .eq(comparator_1_eq));  // open: gt, lt
  Comparator #(.width(5)) comparator_2 (.a(ID_R1_num), .b(MEM_W_num), .eq(comparator_2_eq));  // open: gt, lt
  Comparator #(.width(5)) comparator_3 (.a(ID_R1_num), .b(EX_WriteReg_num), .eq(comparator_3_eq));  // open: gt, lt
  \源寄存器使用情况  \u_源寄存器使用情况_1  (
    .OP0(OP[0]), .OP1(OP[1]), .OP2(OP[2]), .OP3(OP[3]), .OP4(OP[4]), .OP5(OP[5]), .F0(Func[0]), .F1(Func[1]),
    .F2(Func[2]), .F3(Func[3]), .F4(Func[4]), .F5(Func[5]), .R1_Used(R1_Used), .R2_Used(R2_Used));
  Multiplexer #(.width(2), .enable("false")) multiplexer_2 (
    .in0(multiplexer_1_out), .in1(2'b10), .out(multiplexer_2_out), .sel(case2_R1));
  and and_1 (case1_R1, comparator_1_eq, R1_Used, MEM_RegWrite, MEM_MemToReg);
  and and_2 (case2_R1, comparator_2_eq, R1_Used, MEM_RegWrite, not_1_out);
  not not_1 (not_1_out, MEM_MemToReg);
  and and_3 (case3_R1, comparator_3_eq, R1_Used, EX_RegWrite);
  Multiplexer #(.width(2), .enable("false")) multiplexer_3 (
    .in0(multiplexer_2_out), .in1(2'b11), .out(multiplexer_3_out), .sel(case3_R1));
  Comparator #(.width(5)) comparator_4 (.a(ID_R1_num), .b({5{1'b0}}), .eq(comparator_4_eq));  // open: gt, lt
  Comparator #(.width(5)) comparator_5 (.a(ID_R1_num), .b(EX_WriteReg_num), .eq(comparator_5_eq));  // open: gt, lt
  Comparator #(.width(5)) comparator_6 (.a(ID_R2_num), .b({5{1'b0}}), .eq(comparator_6_eq));  // open: gt, lt
  Comparator #(.width(5)) comparator_7 (.a(ID_R2_num), .b(EX_WriteReg_num), .eq(comparator_7_eq));  // open: gt, lt
  Comparator #(.width(5)) comparator_8 (.a(ID_R1_num), .b({5{1'b0}}), .eq(case0_R1));  // open: gt, lt
  Comparator #(.width(5)) comparator_9 (.a(ID_R2_num), .b({5{1'b0}}), .eq(case0_R2));  // open: gt, lt
  Multiplexer #(.width(2), .enable("false")) multiplexer_4 (
    .in0(multiplexer_3_out), .in1(2'b00), .out(forwardR1), .sel(case0_R1));
  not not_2 (not_2_out, comparator_4_eq);
  not not_3 (not_3_out, comparator_6_eq);
  and and_4 (and_4_out, not_2_out, comparator_5_eq, EX_RegWrite, R1_Used);
  and and_5 (and_5_out, not_3_out, comparator_7_eq, EX_RegWrite, R2_Used);
  or or_1 (or_1_out, and_4_out, and_5_out);
  Comparator #(.width(5)) comparator_10 (.a(ID_R2_num), .b(MEM_W_num), .eq(comparator_10_eq));  // open: gt, lt
  Comparator #(.width(5)) comparator_11 (.a(ID_R2_num), .b(MEM_W_num), .eq(comparator_11_eq));  // open: gt, lt
  Comparator #(.width(5)) comparator_12 (.a(ID_R2_num), .b(EX_WriteReg_num), .eq(comparator_12_eq));  // open: gt, lt
  Multiplexer #(.width(2), .enable("false")) multiplexer_5 (
    .in0(2'b00), .in1(2'b01), .out(multiplexer_5_out), .sel(case1_R2));
  Multiplexer #(.width(2), .enable("false")) multiplexer_6 (
    .in0(multiplexer_5_out), .in1(2'b10), .out(multiplexer_6_out), .sel(case2_R2));
  and and_6 (Load_use, or_1_out, EX_MemToReg);
  not not_4 (not_4_out, MEM_MemToReg);
  Multiplexer #(.width(2), .enable("false")) multiplexer_7 (
    .in0(multiplexer_6_out), .in1(2'b11), .out(multiplexer_7_out), .sel(case3_R2));
  and and_7 (case1_R2, comparator_10_eq, R2_Used, MEM_RegWrite, MEM_MemToReg);
  and and_8 (case2_R2, comparator_11_eq, R2_Used, MEM_RegWrite, not_4_out);
  and and_9 (case3_R2, comparator_12_eq, R2_Used, EX_RegWrite);
  Multiplexer #(.width(2), .enable("false")) multiplexer_8 (
    .in0(multiplexer_7_out), .in1(2'b00), .out(forwardR2), .sel(case0_R2));

  // Other names for the same wires on the sheet: EX_W_num[4:0] = EX_WriteReg_num; OP_CODE[5:0] = OP

  // Notes on the sheet:
  //   重定向WB.ALUR
  //   重定向WB.Mem
  //   重定向MEM.ALUR
  //   0号寄存器直接使用
  //   0号寄存器直接使用
  //   判断是否为load指令
  //   重定向WB.ALUR
  //   重定向WB.Mem
  //   重定向MEM.ALUR
endmodule

module \拓展指令信号  (
  input  OP0,
  input  OP1,
  input  OP2,
  input  OP3,
  input  OP4,
  input  OP5,
  input  F0,
  input  F1,
  input  F2,
  input  F3,
  input  F4,
  input  F5,
  output LUI,
  output LH,
  output BLTZ
);

  wire not_1_out, not_2_out, not_3_out, not_4_out, not_5_out, not_6_out, not_7_out, not_8_out, not_9_out,
       not_10_out, not_11_out;

  not not_1 (not_1_out, OP5);
  not not_2 (not_2_out, OP4);
  not not_3 (not_3_out, OP4);
  not not_4 (not_4_out, OP3);
  not not_5 (not_5_out, OP2);
  not not_6 (not_6_out, OP1);
  not not_7 (not_7_out, OP5);
  not not_8 (not_8_out, OP4);
  not not_9 (not_9_out, OP3);
  not not_10 (not_10_out, OP2);
  not not_11 (not_11_out, OP1);
  and and_1 (LUI, not_1_out, not_2_out, OP3, OP2, OP1, OP0);
  and and_2 (LH, OP5, not_3_out, not_4_out, not_5_out, not_6_out, OP0);
  and and_3 (BLTZ, not_7_out, not_8_out, not_9_out, not_10_out, not_11_out, OP0);
endmodule

module \LH指令  (
  input  SEL,
  input  LH,
  input  [31:0] Din,
  output [31:0] Dout
);

  wire [31:0] bit_extender_1_out, bit_extender_2_out;

  Multiplexer #(.select(2), .width(32), .enable("false")) multiplexer_1 (
    .in0(Din), .in1(Din), .in2(bit_extender_1_out), .in3(bit_extender_2_out), .out(Dout), .sel({LH, SEL}));
  assign bit_extender_1_out = {{16{Din[15]}}, Din[15:0]};  // Bit_Extender bit_extender_1
  assign bit_extender_2_out = {{16{Din[31]}}, Din[31:16]};  // Bit_Extender bit_extender_2
endmodule

module \LUI指令  (
  input  JAL,
  input  LUI,
  input  [15:0] Imm16,
  input  [31:0] Din,
  input  [31:0] PcNext,
  output [31:0] Dout
);

  Multiplexer #(.select(2), .width(32), .enable("false")) multiplexer_1 (
    .in0(Din), .in1(PcNext), .in2({Imm16, {16{1'b0}}}), .out(Dout), .sel({LUI, JAL}));  // open: in3
endmodule

module \_24条重定向流水线  (
);

  wire AluSrcB, and_1_out, and_2_out, and_3_out, and_4_out, and_5_out, and_6_out, and_7_out, and_8_out, CLK,
       d_ff_1_q, EQ, EQHalt, \ex_mem_1_eq输出 , \ex_mem_1_传输状态out_表明当前传输数据有效 , Ex_MemToReg, Ex_RegWrite, Go,
       Halt, \id_ex_1_传输状态out_表明当前传输数据有效 , \if_id_1_传输状态out_表明当前传输数据有效 , IR1, IR2, IR3, JR, \LoadUse相关 ,
       Mem_MemToReg, Mem_RegWrite, mips_alu_1_equal, not_1_out, not_2_out, not_3_out, not_4_out, not_5_out,
       not_7_out, or_1_out, or_2_out, RST, Syscall, SyscallHalt, W1, W2, W3, \无条件分支 , \条件分支 ;
  wire [1:0] Forward1, Forward2;
  wire [3:0] ID_Forward;
  wire [4:0] Ex_WriteReg_num, \id_ex_1_shamt输出 , ID_R1_num, ID_R2_num, \mem_wb_1_w_输出 , Mem_WriteReg_num,
       multiplexer_5_out, \指令译码_1_rd , \指令译码_1_rs , \指令译码_1_rt , \指令译码_1_shamt ;
  wire [5:0] Func, Op;
  wire [15:0] \ex_mem_1_控制信号输出 , \id_ex_1_控制信号输出 , \LoadUse次数 , \mem_wb_1_控制信号输出 , \总周期数 , \指令译码_1_imm16 ,
       \插入气泡数 , \无条件分支数 , \条件分支成功数 , \硬布线控制器_封装_1_controlsig ;
  wire [25:0] \指令译码_1_imm26 ;
  wire [31:0] adder_1_out, adder_2_out, \ex_mem_1_ir输出 , \ex_mem_1_memdin输出 , \ex_mem_1_pcnext输出 , EX_PC,
       EX_R1, EX_R2, \id_ex_1_imm16输出 , \id_ex_1_ir输出 , \id_ex_1_pcnext输出 , \id_ex_1_pcnext输出_2 , ID_PC,
       \if_id_1_ir输出 , \if_id_1_pcnext输出 , IF_PC, immext_1_imm16out, immext_1_imm26out, LedData, MEM_AluR,
       MEM_PC, \mem_wb_1_pcnext输出 , mips_alu_1_result, mips_regifile_1_r1, mips_regifile_1_r2,
       multiplexer_1_out, multiplexer_2_out, multiplexer_6_out, multiplexer_7_out, multiplexer_8_out,
       ram_1_data, Redir_A, Redir_B, rom_1_data, WB_AluR, WB_Mem, WB_PC;

  Button \u_总复位  (.out(RST));
  Button _1 (.out(IR1));
  Button _2 (.out(IR2));
  Button _3 (.out(IR3));
  Button \u_继续运行  (.out(Go));
  LED led_1 (.in(W1));
  LED led_2 (.in(W2));
  LED led_3 (.in(W3));
  Multiplexer #(.width(32), .enable("false")) multiplexer_1 (
    .in0(\id_ex_1_pcnext输出 ), .in1(EX_R1), .out(multiplexer_1_out), .sel(JR));
  Hex_Digit_Display hex_digit_display_1 (.value(LedData[31:28]));  // open: dp
  Hex_Digit_Display hex_digit_display_2 (.value(LedData[27:24]));  // open: dp
  Hex_Digit_Display hex_digit_display_3 (.value(LedData[23:20]));  // open: dp
  Multiplexer #(.select(2), .width(32), .enable("false")) multiplexer_2 (
    .in0(adder_1_out), .in1(adder_2_out), .in2(multiplexer_1_out), .out(multiplexer_2_out),
    .sel({\id_ex_1_控制信号输出 [8], \条件分支 }));  // open: in3
  Register #(.width(32)) PC (.D(multiplexer_2_out), .en(and_1_out), .Q(IF_PC), .clk(CLK), .clr(RST));
  and and_1 (and_1_out, Halt, not_1_out);
  not not_1 (not_1_out, \LoadUse相关 );
  Hex_Digit_Display hex_digit_display_4 (.value(LedData[15:12]));  // open: dp
  Hex_Digit_Display hex_digit_display_5 (.value(LedData[19:16]));  // open: dp
  \重定向检测  \u_重定向检测_1  (
    .OP(Op), .EX_WriteReg_num(Ex_WriteReg_num), .EX_RegWrite(Ex_RegWrite), .Load_use(\LoadUse相关 ),
    .ID_R1_num(ID_R1_num), .MEM_RegWrite(Mem_RegWrite), .forwardR1(ID_Forward[1:0]), .Func(Func),
    .ID_R2_num(ID_R2_num), .EX_MemToReg(Ex_MemToReg), .forwardR2(ID_Forward[3:2]),
    .MEM_W_num(Mem_WriteReg_num), .MEM_MemToReg(Mem_MemToReg));
  Hex_Digit_Display hex_digit_display_6 (.value(LedData[7:4]));  // open: dp
  Hex_Digit_Display hex_digit_display_7 (.value(LedData[11:8]));  // open: dp
  Clock clock_1 (.out(CLK));
  // Probe on Forward1
  Multiplexer #(.select(2), .width(32), .enable("false")) multiplexer_3 (
    .in0(EX_R1), .in1(WB_Mem), .in2(WB_AluR), .in3(MEM_AluR), .out(Redir_A), .sel(Forward1));
  // Probe on Forward2
  Multiplexer #(.select(2), .width(32), .enable("false")) multiplexer_4 (
    .in0(EX_R2), .in1(WB_Mem), .in2(WB_AluR), .in3(MEM_AluR), .out(Redir_B), .sel(Forward2));
  Hex_Digit_Display hex_digit_display_8 (.value(LedData[3:0]));  // open: dp
  Adder #(.width(32)) adder_1 (.a(32'h1), .b(IF_PC), .out(adder_1_out));  // open: cin, cout
  ROM #(.addrWidth(10), .dataWidth(32)) rom_1 (.addr(IF_PC[9:0]), .data(rom_1_data));  // open: sel
  or or_1 (or_1_out, RST, \条件分支 , \id_ex_1_控制信号输出 [8]);
  IF_ID if_id_1 (
    .IR(rom_1_data), .\IR输出 (\if_id_1_ir输出 ), .PC(IF_PC), .\PC输出 (ID_PC), .\传输状态In_表明当前传输数据有效 (1'b1),
    .\传输状态Out_表明当前传输数据有效 (\if_id_1_传输状态out_表明当前传输数据有效 ), .CLK(CLK), .\同步清零_气泡_高电平有效 (or_1_out),
    .\使能端_低电平有效_stall_高电平有效 (\LoadUse相关 ), .PcNext(adder_1_out), .\PcNext输出 (\if_id_1_pcnext输出 ));  // open: Hit, Hit输出
  // Probe on \总周期数 
  // Probe on \无条件分支数 
  // Probe on \条件分支成功数 
  // Probe on \插入气泡数 
  // Probe on \LoadUse次数 
  \指令译码  \u_指令译码_1  (
    .Op(Op), .Imm16(\指令译码_1_imm16 ), .Func(Func), .Rs(\指令译码_1_rs ), .Instruction(\if_id_1_ir输出 ),
    .Rt(\指令译码_1_rt ), .Imm26(\指令译码_1_imm26 ), .Rd(\指令译码_1_rd ), .shamt(\指令译码_1_shamt ));
  // Probe on IF_PC[11:0]
  \硬布线控制器_封装  \u_硬布线控制器_封装_1  (.OP(Op), .Func(Func), .ControlSig(\硬布线控制器_封装_1_controlsig ));
  ImmExt immext_1 (
    .Imm16(\指令译码_1_imm16 ), .Imm26(\指令译码_1_imm26 ), .Imm16Out(immext_1_imm16out),
    .Imm26Out(immext_1_imm26out), .SignedExt(\硬布线控制器_封装_1_controlsig [10]));
  // Probe on ID_PC[11:0]
  // Probe on EX_PC[11:0]
  // Probe on MEM_PC[11:0]
  Multiplexer #(.select(2), .width(5), .enable("false")) multiplexer_5 (
    .in0(\指令译码_1_rt ), .in1(\指令译码_1_rd ), .in2({5{1'b1}}), .in3({5{1'b1}}), .out(multiplexer_5_out),
    .sel({\硬布线控制器_封装_1_controlsig [6], \硬布线控制器_封装_1_controlsig [7]}));
  // Probe on WB_PC[11:0]
  SelReg selreg_1 (
    .in_1(\硬布线控制器_封装_1_controlsig [11]), .Rs(\指令译码_1_rs ), .Rt(\指令译码_1_rt ), .R1_num(ID_R1_num),
    .R2_num(ID_R2_num));
  MIPS_Regifile mips_regifile_1 (
    .Din(multiplexer_8_out), .Clk(CLK), .R1(mips_regifile_1_r1), .R2(mips_regifile_1_r2),
    .WE(\mem_wb_1_控制信号输出 [5]), .W_num(\mem_wb_1_w_输出 ), .R1_num(ID_R1_num), .R2_num(ID_R2_num));
  and and_2 (and_2_out, Halt, \条件分支 );
  and and_3 (and_3_out, Halt, \无条件分支 );
  or or_2 (or_2_out, RST, \条件分支 , \id_ex_1_控制信号输出 [8], \LoadUse相关 );
  ID_EX id_ex_1 (
    .PC(ID_PC), .\PC输出 (EX_PC), .\传输状态In_表明当前传输数据有效 (\if_id_1_传输状态out_表明当前传输数据有效 ),
    .\传输状态Out_表明当前传输数据有效 (\id_ex_1_传输状态out_表明当前传输数据有效 ), .CLK(CLK), .\同步清零_气泡_高电平有效 (or_2_out),
    .\使能端_低电平有效_stall_高电平有效 (not_2_out), .IR(\if_id_1_ir输出 ), .\IR输出 (\id_ex_1_ir输出 ),
    .\控制信号 (\硬布线控制器_封装_1_controlsig ),
    .\控制信号输出 ({\id_ex_1_控制信号输出 [15:12], Syscall, \id_ex_1_控制信号输出 [10], JR, \id_ex_1_控制信号输出 [8:6], Ex_RegWrite, AluSrcB, \id_ex_1_控制信号输出 [3], Ex_MemToReg, \id_ex_1_控制信号输出 [1:0]}),
    .Imm16(immext_1_imm16out), .\Imm16输出 (\id_ex_1_imm16输出 ), .R1(mips_regifile_1_r1), .\R1输出 (EX_R1),
    .\R2输出 (EX_R2), .R2(mips_regifile_1_r2), .shamt(\指令译码_1_shamt ), .\shamt输出 (\id_ex_1_shamt输出 ),
    .W_num(multiplexer_5_out), .\W_输出 (Ex_WriteReg_num), .PcNext(\if_id_1_pcnext输出 ),
    .\PcNext输出_2 (\id_ex_1_pcnext输出_2 ), .Imm26(immext_1_imm26out), .\PcNext输出 (\id_ex_1_pcnext输出 ),
    .Forward(ID_Forward), .\Forward输出 ({Forward2, Forward1}));  // open: ExtIns, ExtIns输出, Hit, Hit输出
  not not_2 (not_2_out, Halt);
  Counter #(.width(16), .max('hffff)) counter_1 (
    .count(and_2_out), .Q(\条件分支成功数 ), .clk(CLK), .clr(RST));  // open: load, D, carry
  Counter #(.width(16), .max('hffff)) counter_2 (
    .count(and_3_out), .Q(\无条件分支数 ), .clk(CLK), .clr(RST));  // open: load, D, carry
  Adder #(.width(32)) adder_2 (.a(\id_ex_1_imm16输出 ), .b(\id_ex_1_pcnext输出_2 ), .out(adder_2_out));  // open: cin, cout
  Multiplexer #(.width(32), .enable("false")) multiplexer_6 (
    .in0(Redir_B), .in1(\id_ex_1_imm16输出 ), .out(multiplexer_6_out), .sel(AluSrcB));
  not not_3 (not_3_out, mips_alu_1_equal);
  MIPS_ALU mips_alu_1 (
    .X(Redir_A), .Y(multiplexer_6_out), .AluOP(\id_ex_1_控制信号输出 [15:12]), .Equal(mips_alu_1_equal),
    .Result(mips_alu_1_result), .shamt(\id_ex_1_shamt输出 ));  // open: Result_2
  Comparator #(.width(32), .mode("unsigned")) comparator_1 (.a(Redir_A), .b(32'h22), .eq(EQ));  // open: gt, lt
  Register #(.width(32)) register_1 (.D(Redir_B), .en(and_4_out), .Q(LedData), .clk(CLK));  // open: clr
  and and_4 (and_4_out, EQ, Syscall);
  and and_5 (and_5_out, mips_alu_1_equal, \id_ex_1_控制信号输出 [0]);
  and and_6 (and_6_out, not_3_out, \id_ex_1_控制信号输出 [1]);
  EX_MEM ex_mem_1 (
    .\控制信号 ({\id_ex_1_控制信号输出 [15:12], Syscall, \id_ex_1_控制信号输出 [10], JR, \id_ex_1_控制信号输出 [8:6], Ex_RegWrite, AluSrcB, \id_ex_1_控制信号输出 [3], Ex_MemToReg, \id_ex_1_控制信号输出 [1:0]}),
    .\控制信号输出 ({\ex_mem_1_控制信号输出 [15:6], Mem_RegWrite, \ex_mem_1_控制信号输出 [4:3], Mem_MemToReg, \ex_mem_1_控制信号输出 [1:0]}),
    .AluR(mips_alu_1_result), .\AluR输出 (MEM_AluR), .IR(\id_ex_1_ir输出 ), .\IR输出 (\ex_mem_1_ir输出 ), .PC(EX_PC),
    .\PC输出 (MEM_PC), .\传输状态In_表明当前传输数据有效 (\id_ex_1_传输状态out_表明当前传输数据有效 ),
    .\传输状态Out_表明当前传输数据有效 (\ex_mem_1_传输状态out_表明当前传输数据有效 ), .CLK(CLK), .\同步清零_气泡_高电平有效 (RST),
    .\使能端_低电平有效_stall_高电平有效 (not_4_out), .MemDin(Redir_B), .\MemDin输出 (\ex_mem_1_memdin输出 ),
    .W_num(Ex_WriteReg_num), .\W_输出 (Mem_WriteReg_num), .PcNext(\id_ex_1_pcnext输出_2 ),
    .\PcNext输出 (\ex_mem_1_pcnext输出 ), .EQ(EQ), .\EQ输出 (\ex_mem_1_eq输出 ));  // open: ExtIns, ExtIns输出
  not not_4 (not_4_out, Halt);
  not not_5 (not_5_out, EQHalt);
  or or_3 (\条件分支 , and_5_out, and_6_out);
  and and_7 (and_7_out, Halt, \LoadUse相关 );
  and and_8 (and_8_out, not_5_out, SyscallHalt);
  Counter #(.width(16), .max('hffff)) counter_3 (
    .count(Halt), .Q(\总周期数 ), .clk(CLK), .clr(RST));  // open: load, D, carry
  Counter #(.width(16), .max('hffff)) counter_4 (
    .count(and_7_out), .Q(\LoadUse次数 ), .clk(CLK), .clr(RST));  // open: load, D, carry
  D_Flip_Flop #(.trigger("high")) d_ff_1 (
    .clk(CLK), .D(and_8_out), .Q(d_ff_1_q), .en(SyscallHalt), .reset(Go));  // open: Qn, preset
  RAM #(.addrWidth(10), .dataWidth(32), .bus("separate")) ram_1 (
    .addr(MEM_AluR[11:2]), .din(\ex_mem_1_memdin输出 ), .data(ram_1_data), .str(\ex_mem_1_控制信号输出 [3]),
    .clk(CLK), .clr(RST));  // open: sel, ld
  not not_6 (Halt, d_ff_1_q);
  MEM_WB mem_wb_1 (
    .\控制信号 ({\ex_mem_1_控制信号输出 [15:6], Mem_RegWrite, \ex_mem_1_控制信号输出 [4:3], Mem_MemToReg, \ex_mem_1_控制信号输出 [1:0]}),
    .\控制信号输出 ({\mem_wb_1_控制信号输出 [15:12], SyscallHalt, \mem_wb_1_控制信号输出 [10:9], \无条件分支 , \mem_wb_1_控制信号输出 [7:0]}),
    .Mem(ram_1_data), .\Mem输出 (WB_Mem), .Alu(MEM_AluR), .\Alu输出 (WB_AluR), .IR(\ex_mem_1_ir输出 ), .PC(MEM_PC),
    .\PC输出 (WB_PC), .\传输状态In_表明当前传输数据有效 (\ex_mem_1_传输状态out_表明当前传输数据有效 ), .CLK(CLK), .\同步清零_气泡_高电平有效 (RST),
    .\使能端_低电平有效_stall_高电平有效 (not_7_out), .W_num(Mem_WriteReg_num), .\W_输出 (\mem_wb_1_w_输出 ),
    .PcNext(\ex_mem_1_pcnext输出 ), .\PcNext输出 (\mem_wb_1_pcnext输出 ), .EQ(\ex_mem_1_eq输出 ), .EQ_2(EQHalt));  // open: IR输出, 传输状态Out_表明当前传输数据有效, ExtIns, ExtIns输出, v0, v0输出
  not not_7 (not_7_out, Halt);
  Multiplexer #(.width(32), .enable("false")) multiplexer_7 (
    .in0(WB_AluR), .in1(WB_Mem), .out(multiplexer_7_out), .sel(\mem_wb_1_控制信号输出 [2]));
  Multiplexer #(.width(32), .enable("false")) multiplexer_8 (
    .in0(multiplexer_7_out), .in1(\mem_wb_1_pcnext输出 ), .out(multiplexer_8_out), .sel(\mem_wb_1_控制信号输出 [6]));

  // Other names for the same wires on the sheet: v0[31:0] = Redir_B

  // Notes on the sheet:
  //   中断源
  //   0:Beq
  //   1:Bne
  //   2:MemToReg
  //   3:MemWrite
  //   4:AluSrcB
  //   5:RegWrite
  //   6:JAL
  //   7:RegDst
  //   8:JMP
  //   9:JR
  //   10:SignedExt
  //   11:Syscall
  //   12-15:AluOp
  //   中断等待指示
  //   数码管输出
  //   指令存储器
  //   contents of rom_1 (hex, n*v repeats v):
  //   20110001 8000c05 20110001 20120002 20130003 8000c09 20110001 20120002 20130003 8000c0d 20110001
  //   20120002 20130003 8000c11 20110001 20120002 20130003 c000cb8 20100001 20110001 118fc0 112020
  //   20020022 c 118882 12200001 8000c15 112020 20020022 c 20110001 118880 112020 20020022 c 12200001
  //   8000c1f 20110001 118fc0 112020 20020022 c 1188c3 112020 20020022 c 118903 112020 20020022 c 118903
  //   112020 20020022 c 118903 112020 20020022 c 118903 112020 20020022 c 118903 112020 20020022 c 118903
  //   112020 20020022 c 118903 112020 20020022 c 20100001 109fc0 139fc3 8021 2012000c 24160003 26100001
  //   3210000f 20080008 20090001 139900 2709825 132020 20020022 c 1094022 1500fff9 22100001 2018000f
  //   2188024 108700 20080008 20090001 139902 2709825 132021 20020022 c 1094022 1500fff9 108702 2c9b022
  //   12c00001 8000c50 4020 1084027 84400 3508ffff 82021 20020022 c 2010ffff 20110000 ae300000 22100001
  //   22310004 ae300000 22100001 22310004 ae300000 22100001 22310004 ae300000 22100001 22310004 ae300000
  //   22100001 22310004 ae300000 22100001 22310004 ae300000 22100001 22310004 ae300000 22100001 22310004
  //   ae300000 22100001 22310004 ae300000 22100001 22310004 ae300000 22100001 22310004 ae300000 22100001
  //   22310004 ae300000 22100001 22310004 ae300000 22100001 22310004 ae300000 22100001 22310004 ae300000
  //   22100001 22310004 22100001 8020 2011003c 8e130000 8e340000 274402a 11000002 ae330000 ae140000
  //   2231fffc 1611fff8 102020 20020022 c 22100004 2011003c 1611fff2 20020032 c 20100000 22100001 102020
  //   20020022 c 22100002 102020 20020022 c 22100003 102020 20020022 c 22100004 102020 20020022 c 22100005
  //   102020 20020022 c 22100006 102020 20020022 c 22100007 102020 20020022 c 22100008 102020 20020022
  //   20020022 c 3e00008
  //   SignedExt
  //   流水调试日志用
  //   RegDst
  //   JAL
  //   Syscall
  //   RegWrite
  //   JAL
  //   无条件分支
  //   AlcSrcB
  //   MemWrite
endmodule

module \Cache全相连  (
  input  [31:0] BlockDataIn,
  input  [9:0] Addr,
  input  BlkDataReady,
  input  CLK,
  input  Enable,
  output Miss,
  output [31:0] DataOut
);

  wire comparator_1_eq, comparator_2_eq, comparator_3_eq, comparator_4_eq, comparator_5_eq, comparator_6_eq,
       comparator_7_eq, comparator_8_eq, Hit, L0, L1, L2, L3, L4, L5, L6, L7, or_2_out,
       priority_encoder_1_p2, priority_encoder_1_p3, priority_encoder_1_p4, priority_encoder_1_p5,
       priority_encoder_1_p6, priority_encoder_1_p7, priority_encoder_1_p8, priority_encoder_1_p9, V0, V1,
       V2, V3, V4, V5, V6, V7, Write0, Write1, Write2, Write3, Write4, Write5, Write6, Write7;
  wire [2:0] max3_1_max_num, max3_2_max_num, max3_3_max_num, max3_4_max_num, max3_5_max_num, max3_6_max_num,
       max3_7_max_num, multiplexer_1_out, priority_encoder_1_p1;
  wire [13:0] TAG0, TAG1, TAG2, TAG3, TAG4, TAG5, TAG6, TAG7;
  wire [15:0] C0, C1, C2, C3, C4, C5, C6, C7, max3_1_max, max3_2_max, max3_3_max, max3_4_max, max3_5_max,
       max3_7_max;
  wire [31:0] \数据块副本_2_q , \数据块副本_3_q , \数据块副本_4_q , \数据块副本_5_q , \数据块副本_6_q , \数据块副本_7_q , \数据块副本_8_q ,
       \数据块副本_q ;

  Comparator #(.width(14)) comparator_1 (.a(TAG0), .b({4'b0000, Addr}), .eq(comparator_1_eq));  // open: gt, lt
  Comparator #(.width(14)) comparator_2 (.a(TAG1), .b({4'b0000, Addr}), .eq(comparator_2_eq));  // open: gt, lt
  Comparator #(.width(14)) comparator_3 (.a(TAG2), .b({4'b0000, Addr}), .eq(comparator_3_eq));  // open: gt, lt
  Comparator #(.width(14)) comparator_4 (.a(TAG3), .b({4'b0000, Addr}), .eq(comparator_4_eq));  // open: gt, lt
  Comparator #(.width(14)) comparator_5 (.a(TAG4), .b({4'b0000, Addr}), .eq(comparator_5_eq));  // open: gt, lt
  Comparator #(.width(14)) comparator_6 (.a(TAG5), .b({4'b0000, Addr}), .eq(comparator_6_eq));  // open: gt, lt
  Comparator #(.width(14)) comparator_7 (.a(TAG6), .b({4'b0000, Addr}), .eq(comparator_7_eq));  // open: gt, lt
  Comparator #(.width(14)) comparator_8 (.a(TAG7), .b({4'b0000, Addr}), .eq(comparator_8_eq));  // open: gt, lt
  Register #(.width(1)) VALID (.D(1'b1), .en(Write0), .Q(V0), .clk(CLK));  // open: clr
  Register #(.width(1)) VALID_2 (.D(1'b1), .en(Write1), .Q(V1), .clk(CLK));  // open: clr
  Register #(.width(1)) VALID_3 (.D(1'b1), .en(Write2), .Q(V2), .clk(CLK));  // open: clr
  Register #(.width(1)) VALID_4 (.D(1'b1), .en(Write3), .Q(V3), .clk(CLK));  // open: clr
  and and_1 (L0, V0, comparator_1_eq);
  and and_2 (L1, V1, comparator_2_eq);
  and and_3 (L2, V2, comparator_3_eq);
  and and_4 (L3, V3, comparator_4_eq);
  and and_5 (L4, V4, comparator_5_eq);
  and and_6 (L5, V5, comparator_6_eq);
  and and_7 (L6, V6, comparator_7_eq);
  and and_8 (L7, V7, comparator_8_eq);
  not not_1 (Miss, Hit);
  or or_1 (Hit, L0, L1, L2, L3, L4, L5, L6, L7);
  Register #(.width(14)) TAG (.D({4'b0000, Addr}), .en(Write0), .Q(TAG0), .clk(CLK));  // open: clr
  Register #(.width(14)) TAG_2 (.D({4'b0000, Addr}), .en(Write1), .Q(TAG1), .clk(CLK));  // open: clr
  Register #(.width(14)) TAG_3 (.D({4'b0000, Addr}), .en(Write2), .Q(TAG2), .clk(CLK));  // open: clr
  Register #(.width(14)) TAG_4 (.D({4'b0000, Addr}), .en(Write3), .Q(TAG3), .clk(CLK));  // open: clr
  Counter #(.width(16), .max('hffff)) \u_淘汰标志位  (.count(Hit), .Q(C0), .clk(CLK), .clr(L0));  // open: load, D, carry
  Counter #(.width(16), .max('hffff)) \u_淘汰标志位_2  (.count(Hit), .Q(C1), .clk(CLK), .clr(L1));  // open: load, D, carry
  Counter #(.width(16), .max('hffff)) \u_淘汰标志位_3  (.count(Hit), .Q(C2), .clk(CLK), .clr(L2));  // open: load, D, carry
  Counter #(.width(16), .max('hffff)) \u_淘汰标志位_4  (.count(Hit), .Q(C3), .clk(CLK), .clr(L3));  // open: load, D, carry
  Max3 max3_1 (.Y(C1), .X(C0), .Y_num(3'b001), .X_num(3'b000), .MAX(max3_1_max), .Max_num(max3_1_max_num));
  Max3 max3_2 (.Y(C3), .X(C2), .Y_num(3'b011), .X_num(3'b010), .MAX(max3_2_max), .Max_num(max3_2_max_num));
  Max3 max3_3 (.Y(C5), .X(C4), .Y_num(3'b101), .X_num(3'b100), .MAX(max3_3_max), .Max_num(max3_3_max_num));
  Max3 max3_4 (.Y(C7), .X(C6), .Y_num(3'b111), .X_num(3'b110), .MAX(max3_4_max), .Max_num(max3_4_max_num));
  Max3 max3_5 (
    .Y(max3_2_max), .X(max3_1_max), .Y_num(max3_2_max_num), .X_num(max3_1_max_num), .MAX(max3_5_max),
    .Max_num(max3_5_max_num));
  Max3 max3_6 (
    .Y(max3_7_max), .X(max3_5_max), .Y_num(max3_7_max_num), .X_num(max3_5_max_num), .Max_num(max3_6_max_num));  // open: MAX
  Max3 max3_7 (
    .Y(max3_4_max), .X(max3_3_max), .Y_num(max3_4_max_num), .X_num(max3_3_max_num), .MAX(max3_7_max),
    .Max_num(max3_7_max_num));
  Register #(.width(32)) \u_数据块副本  (.D(BlockDataIn), .en(Write0), .Q(\数据块副本_q ), .clk(CLK));  // open: clr
  assign DataOut = L0 ? \数据块副本_q  : 32'bz;  // Controlled_Buffer controlled_buffer_1
  assign DataOut = L1 ? \数据块副本_2_q  : 32'bz;  // Controlled_Buffer controlled_buffer_2
  Register #(.width(32)) \u_数据块副本_2  (.D(BlockDataIn), .en(Write1), .Q(\数据块副本_2_q ), .clk(CLK));  // open: clr
  Register #(.width(32)) \u_数据块副本_3  (.D(BlockDataIn), .en(Write2), .Q(\数据块副本_3_q ), .clk(CLK));  // open: clr
  assign DataOut = L2 ? \数据块副本_3_q  : 32'bz;  // Controlled_Buffer controlled_buffer_3
  assign DataOut = L3 ? \数据块副本_4_q  : 32'bz;  // Controlled_Buffer controlled_buffer_4
  Register #(.width(32)) \u_数据块副本_4  (.D(BlockDataIn), .en(Write3), .Q(\数据块副本_4_q ), .clk(CLK));  // open: clr
  Demultiplexer #(.select(3), .enable("false")) demultiplexer_1 (
    .out0(Write0), .out1(Write1), .out2(Write2), .out3(Write3), .out4(Write4), .out5(Write5), .out6(Write6),
    .out7(Write7), .in(BlkDataReady), .sel(multiplexer_1_out));
  Multiplexer #(.width(3), .enable("false")) multiplexer_1 (
    .in0(max3_6_max_num), .in1(priority_encoder_1_p1), .out(multiplexer_1_out), .sel(or_2_out));
  // Priority_Encoder priority_encoder_1: pin names not known; wires that end beside it: priority_encoder_1_p1, priority_encoder_1_p2, priority_encoder_1_p3, priority_encoder_1_p4, priority_encoder_1_p5, priority_encoder_1_p6, priority_encoder_1_p7, priority_encoder_1_p8, priority_encoder_1_p9
  Register #(.width(1)) VALID_5 (.D(1'b1), .en(Write4), .Q(V4), .clk(CLK));  // open: clr
  Register #(.width(1)) VALID_6 (.D(1'b1), .en(Write5), .Q(V5), .clk(CLK));  // open: clr
  Register #(.width(1)) VALID_7 (.D(1'b1), .en(Write6), .Q(V6), .clk(CLK));  // open: clr
  Register #(.width(1)) VALID_8 (.D(1'b1), .en(Write7), .Q(V7), .clk(CLK));  // open: clr
  or or_2 (or_2_out, priority_encoder_1_p9, priority_encoder_1_p8, priority_encoder_1_p7, priority_encoder_1_p6, priority_encoder_1_p5, priority_encoder_1_p4, priority_encoder_1_p3, priority_encoder_1_p2);
  not not_2 (priority_encoder_1_p2, V0);
  not not_3 (priority_encoder_1_p3, V1);
  not not_4 (priority_encoder_1_p4, V2);
  not not_5 (priority_encoder_1_p5, V3);
  not not_6 (priority_encoder_1_p6, V4);
  not not_7 (priority_encoder_1_p7, V5);
  not not_8 (priority_encoder_1_p8, V6);
  not not_9 (priority_encoder_1_p9, V7);
  Register #(.width(14)) TAG_5 (.D({4'b0000, Addr}), .en(Write4), .Q(TAG4), .clk(CLK));  // open: clr
  Register #(.width(14)) TAG_6 (.D({4'b0000, Addr}), .en(Write5), .Q(TAG5), .clk(CLK));  // open: clr
  Register #(.width(14)) TAG_7 (.D({4'b0000, Addr}), .en(Write6), .Q(TAG6), .clk(CLK));  // open: clr
  Register #(.width(14)) TAG_8 (.D({4'b0000, Addr}), .en(Write7), .Q(TAG7), .clk(CLK));  // open: clr
  Counter #(.width(16), .max('hffff)) \u_淘汰标志位_5  (.count(Hit), .Q(C4), .clk(CLK), .clr(L4));  // open: load, D, carry
  Counter #(.width(16), .max('hffff)) \u_淘汰标志位_6  (.count(Hit), .Q(C5), .clk(CLK), .clr(L5));  // open: load, D, carry
  Counter #(.width(16), .max('hffff)) \u_淘汰标志位_7  (.count(Hit), .Q(C6), .clk(CLK), .clr(L6));  // open: load, D, carry
  Counter #(.width(16), .max('hffff)) \u_淘汰标志位_8  (.count(Hit), .Q(C7), .clk(CLK), .clr(L7));  // open: load, D, carry
  assign DataOut = L4 ? \数据块副本_5_q  : 32'bz;  // Controlled_Buffer controlled_buffer_5
  Register #(.width(32)) \u_数据块副本_5  (.D(BlockDataIn), .en(Write4), .Q(\数据块副本_5_q ), .clk(CLK));  // open: clr
  assign DataOut = L5 ? \数据块副本_6_q  : 32'bz;  // Controlled_Buffer controlled_buffer_6
  Register #(.width(32)) \u_数据块副本_6  (.D(BlockDataIn), .en(Write5), .Q(\数据块副本_6_q ), .clk(CLK));  // open: clr
  assign DataOut = L6 ? \数据块副本_7_q  : 32'bz;  // Controlled_Buffer controlled_buffer_7
  Register #(.width(32)) \u_数据块副本_7  (.D(BlockDataIn), .en(Write6), .Q(\数据块副本_7_q ), .clk(CLK));  // open: clr
  Register #(.width(32)) \u_数据块副本_8  (.D(BlockDataIn), .en(Write7), .Q(\数据块副本_8_q ), .clk(CLK));  // open: clr
  assign DataOut = L7 ? \数据块副本_8_q  : 32'bz;  // Controlled_Buffer controlled_buffer_8

  // Other names for the same wires on the sheet: Blk[31:0] = BlockDataIn; BlkReady = BlkDataReady; En = Enable;
  //   SlotData[31:0] = DataOut; TAG[9:0] = Addr; 字节地址[9:0] = Addr

  // Notes on the sheet:
  //   输入引脚区
  //   请勿增改引脚，请勿修改子电路封装
  //   电路功能：利用上面给定的隧道构建8行的Cache，cache映射方式自选
  //   请在下方利用上方输入输出引脚的隧道信号构建电路，ctrl+d复制选择部件
  //   输出引脚区
endmodule
module \单级中断  (
);

  wire and_1_out, and_2_out, and_3_out, and_4_out, and_5_out, and_6_out, and_7_out, CLK, \CPU中断Sig ,
       d_ff_1_q, EQ, ERET, Go, Halt, IE, INT_q, IR1, IR1Sig, IR2, IR2Sig, IR3, IR3Sig, JAL, mips_alu_1_equal,
       not_1_out, not_3_out, RST, SignedExt, Syscall, W1, W2, W3, \中断Rst1 , \中断Rst2 , \中断Rst3 , \无条件分支 ,
       \条件分支 , \硬布线控制器_1_alu_src , \硬布线控制器_1_beq , \硬布线控制器_1_bne , \硬布线控制器_1_jr , \硬布线控制器_1_memtoreg ,
       \硬布线控制器_1_memwrite , \硬布线控制器_1_regdst , \硬布线控制器_1_regwrite , \解码信号 ;
  wire [1:0] multiplexer_13_out, \中断号 , \正在执行的中断程序 ;
  wire [3:0] \硬布线控制器_1_alu_op ;
  wire [4:0] multiplexer_5_out, multiplexer_7_out, multiplexer_8_out, multiplexer_9_out;
  wire [15:0] \总周期数 , \无条件分支数 , \条件分支成功数 ;
  wire [31:0] adder_1_out, adder_2_out, bit_extender_1_out, bit_extender_2_out, EPC, Instruction, LedData,
       mips_alu_1_result, mips_regifile_1_r1, multiplexer_1_out, multiplexer_2_out, multiplexer_3_out,
       multiplexer_4_out, multiplexer_6_out, multiplexer_10_out, multiplexer_11_out, PC, ram_1_data, v0,
       \中断程序地址 ;

  Multiplexer #(.width(32), .enable("false")) multiplexer_1 (
    .in0(bit_extender_1_out), .in1(mips_regifile_1_r1), .out(multiplexer_1_out), .sel(\硬布线控制器_1_jr ));
  or or_1 (\条件分支 , and_7_out, and_6_out);
  Button \u_总复位  (.out(RST));
  Button \u_继续运行  (.out(Go));
  Clock clock_1 (.out(CLK));
  Multiplexer #(.select(2), .width(32), .enable("false")) multiplexer_2 (
    .in0(adder_1_out), .in1(adder_2_out), .in2(multiplexer_1_out), .out(multiplexer_2_out),
    .sel({\无条件分支 , \条件分支 }));  // open: in3
  Multiplexer #(.width(32), .enable("false")) multiplexer_3 (
    .in0(multiplexer_2_out), .in1(\中断程序地址 ), .out(multiplexer_3_out), .sel(\CPU中断Sig ));
  Hex_Digit_Display hex_digit_display_1 (.value(LedData[27:24]));  // open: dp
  Hex_Digit_Display hex_digit_display_2 (.value(LedData[31:28]));  // open: dp
  Multiplexer #(.width(32), .enable("false")) multiplexer_4 (
    .in0(multiplexer_3_out), .in1(EPC), .out(multiplexer_4_out), .sel(ERET));
  Hex_Digit_Display hex_digit_display_3 (.value(LedData[23:20]));  // open: dp
  Hex_Digit_Display hex_digit_display_4 (.value(LedData[19:16]));  // open: dp
  and and_1 (and_1_out, Halt, \无条件分支 );
  Register #(.width(32)) u_PC (.D(multiplexer_4_out), .en(Halt), .Q(PC), .clk(CLK), .clr(RST));
  Hex_Digit_Display hex_digit_display_5 (.value(LedData[15:12]));  // open: dp
  Hex_Digit_Display hex_digit_display_6 (.value(LedData[11:8]));  // open: dp
  Counter #(.width(16), .max('hffff)) counter_1 (
    .count(Halt), .Q(\总周期数 ), .clk(CLK), .clr(RST));  // open: load, D, carry
  Counter #(.width(16), .max('hffff)) counter_2 (
    .count(and_1_out), .Q(\无条件分支数 ), .clk(CLK), .clr(RST));  // open: load, D, carry
  Adder #(.width(32)) adder_1 (.a(PC), .b(32'h1), .out(adder_1_out));  // open: cin, cout
  Comparator #(.width(32)) comparator_1 (.a(Instruction), .b(32'h42000018), .eq(ERET));  // open: gt, lt
  Hex_Digit_Display hex_digit_display_7 (.value(LedData[7:4]));  // open: dp
  Hex_Digit_Display hex_digit_display_8 (.value(LedData[3:0]));  // open: dp
  // MIPS_Probe mips_probe_1: pin names not known; wires that end beside it: Instruction, Instruction
  ROM #(.addrWidth(10), .dataWidth(32)) rom_1 (.addr(PC[9:0]), .data(Instruction));  // open: sel
  assign bit_extender_1_out = {{6{Instruction[25]}}, Instruction[25:0]};  // Bit_Extender bit_extender_1
  // Probe on bit_extender_1_out
  Counter #(.width(16), .max('hffff)) counter_3 (
    .count(and_2_out), .Q(\条件分支成功数 ), .clk(CLK), .clr(RST));  // open: load, D, carry
  and and_2 (and_2_out, Halt, \条件分支 );
  and and_3 (and_3_out, Instruction[15], SignedExt);
  \硬布线控制器  \u_硬布线控制器_1  (
    .Func(Instruction[5:0]), .OP(Instruction[31:26]), .ALU_OP(\硬布线控制器_1_alu_op ),
    .MemToReg(\硬布线控制器_1_memtoreg ), .MemWrite(\硬布线控制器_1_memwrite ), .ALU_SRC(\硬布线控制器_1_alu_src ),
    .RegWrite(\硬布线控制器_1_regwrite ), .SysCALL(Syscall), .SignedExt(SignedExt), .RegDst(\硬布线控制器_1_regdst ),
    .JR(\硬布线控制器_1_jr ), .JMP(\无条件分支 ), .Beq(\硬布线控制器_1_beq ), .JAL(JAL), .Bne(\硬布线控制器_1_bne ));  // open: LUI, LH, BLTZ
  Multiplexer #(.width(5), .enable("false")) multiplexer_5 (
    .in0(Instruction[20:16]), .in1(Instruction[15:11]), .out(multiplexer_5_out), .sel(\硬布线控制器_1_regdst ));
  Multiplexer #(.width(32), .enable("false")) multiplexer_6 (
    .in0(multiplexer_11_out), .in1(adder_1_out), .out(multiplexer_6_out), .sel(JAL));
  assign bit_extender_2_out = {{16{and_3_out}}, Instruction[15:0]};  // Bit_Extender bit_extender_2
  // Probe on \总周期数 
  // Probe on \无条件分支数 
  // Probe on \条件分支成功数 
  Register #(.width(32)) register_1 (.D(v0), .en(and_4_out), .Q(LedData), .clk(CLK));  // open: clr
  and and_4 (and_4_out, EQ, Syscall);
  Multiplexer #(.width(5), .enable("false")) multiplexer_7 (
    .in0(Instruction[25:21]), .in1(5'b00010), .out(multiplexer_7_out), .sel(Syscall));
  Multiplexer #(.width(5), .enable("false")) multiplexer_8 (
    .in0(Instruction[20:16]), .in1(5'b00100), .out(multiplexer_8_out), .sel(Syscall));
  Multiplexer #(.width(5), .enable("false")) multiplexer_9 (
    .in0(multiplexer_5_out), .in1({5{1'b1}}), .out(multiplexer_9_out), .sel(JAL));
  Button _1 (.out(IR1));
  Button _2 (.out(IR2));
  Button _3 (.out(IR3));
  LED led_1 (.in(W1));
  LED led_2 (.in(W2));
  LED led_3 (.in(W3));
  not not_1 (not_1_out, EQ);
  and and_5 (and_5_out, not_1_out, Syscall);
  MIPS_Regifile mips_regifile_1 (
    .Din(multiplexer_6_out), .Clk(CLK), .R1(mips_regifile_1_r1), .R2(v0), .WE(\硬布线控制器_1_regwrite ),
    .W_num(multiplexer_9_out), .R1_num(multiplexer_7_out), .R2_num(multiplexer_8_out));
  D_Flip_Flop #(.trigger("high")) d_ff_1 (
    .clk(CLK), .D(and_5_out), .Q(d_ff_1_q), .en(Syscall), .reset(Go));  // open: Qn, preset
  Comparator #(.width(32), .mode("unsigned")) comparator_2 (
    .a(32'h22), .b(mips_regifile_1_r1), .eq(EQ));  // open: gt, lt
  Multiplexer #(.width(32), .enable("false")) multiplexer_10 (
    .in0(v0), .in1(bit_extender_2_out), .out(multiplexer_10_out), .sel(\硬布线控制器_1_alu_src ));
  not not_2 (Halt, d_ff_1_q);
  MIPS_ALU mips_alu_1 (
    .X(mips_regifile_1_r1), .Y(multiplexer_10_out), .AluOP(\硬布线控制器_1_alu_op ), .Equal(mips_alu_1_equal),
    .Result(mips_alu_1_result), .shamt(Instruction[10:6]));  // open: Result_2
  Adder #(.width(32)) adder_2 (.a(bit_extender_2_out), .b(adder_1_out), .out(adder_2_out));  // open: cin, cout
  and and_6 (and_6_out, mips_alu_1_equal, \硬布线控制器_1_beq );
  not not_3 (not_3_out, mips_alu_1_equal);
  and and_7 (and_7_out, not_3_out, \硬布线控制器_1_bne );
  Priority_Encoder #(.select(2)) priority_encoder_1 (
    .in0(IR1Sig), .in1(IR2Sig), .in2(IR3Sig), .in3(1'b0), .out(\中断号 ), .gs(\解码信号 ), .en_in(1'b1));  // open: en_out
  and and_8 (\CPU中断Sig , \解码信号 , IE);
  RAM #(.addrWidth(10), .dataWidth(32), .bus("separate")) ram_1 (
    .addr(mips_alu_1_result[11:2]), .din(v0), .data(ram_1_data), .str(\硬布线控制器_1_memwrite ), .clk(CLK),
    .ld(\硬布线控制器_1_memtoreg ), .clr(RST));  // open: sel
  Multiplexer #(.width(32), .enable("false")) multiplexer_11 (
    .in0(mips_alu_1_result), .in1(ram_1_data), .out(multiplexer_11_out), .sel(\硬布线控制器_1_memtoreg ));
  Register #(.width(2)) INTNUM (.D(\中断号 ), .en(\CPU中断Sig ), .Q(\正在执行的中断程序 ), .clk(CLK));  // open: clr
  Register #(.width(1)) INT (.D(\CPU中断Sig ), .en(\CPU中断Sig ), .Q(INT_q), .clk(CLK), .clr(ERET));
  D_Flip_Flop u_IE (.clk(CLK), .D(1'b1), .Q(IE), .reset(INT_q));  // open: Qn, preset, en
  Register #(.width(32)) u_EPC (.D(PC), .en(\CPU中断Sig ), .Q(EPC), .clk(CLK), .clr(RST));
  \中断按键采样电路  \u_中断按键采样电路_1  (.CLK(CLK), .\中断信号 (IR1), .\和中断屏蔽位与 (IR1Sig), .\同步清零信号 (\中断Rst1 ), .\中断等待指示灯 (W1));
  \中断按键采样电路  \u_中断按键采样电路_2  (.CLK(CLK), .\中断信号 (IR2), .\和中断屏蔽位与 (IR2Sig), .\同步清零信号 (\中断Rst2 ), .\中断等待指示灯 (W2));
  \中断按键采样电路  \u_中断按键采样电路_3  (.CLK(CLK), .\中断信号 (IR3), .\和中断屏蔽位与 (IR3Sig), .\同步清零信号 (\中断Rst3 ), .\中断等待指示灯 (W3));
  Multiplexer #(.select(2), .width(32), .enable("false")) multiplexer_12 (
    .in0(32'h8), .in1(32'h36), .in2(32'h64), .out(\中断程序地址 ), .sel(\中断号 ));  // open: in3
  Demultiplexer #(.select(2), .enable("false")) demultiplexer_1 (
    .out0(\中断Rst1 ), .out1(\中断Rst2 ), .out2(\中断Rst3 ), .in(ERET), .sel(multiplexer_13_out));  // open: out3
  Multiplexer #(.width(2), .enable("false")) multiplexer_13 (
    .in0(2'b11), .in1(\正在执行的中断程序 ), .out(multiplexer_13_out), .sel(\解码信号 ));

  // Notes on the sheet:
  //   数码管输出应该用寄存器锁存，否则显示数据只能一闪而过
  //   可以通过项目增加Logisim库的方式将前几次实验完成的电路作为子电路引入到本电路中使用
  //   数码管输出
  //   指令存储器
  //   contents of rom_1 (hex, n*v repeats v):
  //   20112000 20020022 112020 c 2231ffff 1620fffc 20020032 c 3c01000f 3421ffff 1e820 23bdfffc afa20000
  //   23bdfffc afa40000 23bdfffc afb00000 23bdfffc afb30000 23bdfffc afb40000 23bdfffc afb50000 23bdfffc
  //   afb60000 20160001 20140006 20150001 168020 108100 2149825 132020 20020022 c 1600fffa 295a022
  //   1680fff7 2002000a 8fb60000 27bd0004 8fb50000 27bd0004 8fb40000 27bd0004 8fb30000 27bd0004 8fb00000
  //   27bd0004 8fa40000 27bd0004 8fa20000 27bd0004 42000018 c 3c01000f 3421ffff 1e820 23bdfffc afa20000
  //   23bdfffc afa40000 23bdfffc afb00000 23bdfffc afb30000 23bdfffc afb40000 23bdfffc afb50000 23bdfffc
  //   afb60000 20160002 20140006 20150001 168020 108100 2149825 132020 20020022 c 1600fffa 295a022
  //   1680fff7 2002000a 8fb60000 27bd0004 8fb50000 27bd0004 8fb40000 27bd0004 8fb30000 27bd0004 8fb00000
  //   27bd0004 8fa40000 27bd0004 8fa20000 27bd0004 42000018 c 3c01000f 3421ffff 1e820 23bdfffc afa20000
  //   23bdfffc afa40000 23bdfffc afb00000 23bdfffc afb30000 23bdfffc afb40000 23bdfffc afb50000 23bdfffc
  //   afb60000 20160003 20140006 20150001 168020 108100 2149825 132020 20020022 c 1600fffa 295a022
  //   1680fff7 2002000a 8fb60000 27bd0004 8fb50000 27bd0004 8fb40000 27bd0004 8fb30000 27bd0004 8fb00000
  //   27bd0004 8fa40000 27bd0004 8fa20000 27bd0004 42000018 c 2002000a c
  //   JMP
  //   JR
  //   Op
  //   Func
  //   总复位信号应将除ROM以外所有存储组件全部清零
  //   Beq
  //   JAL
  //   rs
  //   rt
  //   rd
  //   Bne
  //   MemToReg
  //   MemWrite
  //   AluOP
  //   AluSrcB
  //   RegWrite
  //   RegDst
  //   v0
  //   a0
  //   中断源
  //   中断等待指示
endmodule

// 按键采样
module \中断按键采样电路  (
  input  CLK,
  input  \中断信号 ,
  input  \同步清零信号 ,
  output \和中断屏蔽位与 ,
  output \中断等待指示灯 
);

  wire and_1_out, IR1_q, or_2_out;

  or or_1 (\中断等待指示灯 , \和中断屏蔽位与 , IR1_q);
  D_Flip_Flop IR1 (.clk(\中断信号 ), .D(1'b1), .Q(IR1_q), .reset(\和中断屏蔽位与 ));  // open: Qn, preset, en
  or or_2 (or_2_out, IR1_q, \和中断屏蔽位与 );
  and and_1 (and_1_out, or_2_out, ~\同步清零信号 );  // AND_Gate
  D_Flip_Flop IR1_2 (.clk(CLK), .D(and_1_out), .Q(\和中断屏蔽位与 ));  // open: Qn, preset, en, reset
endmodule

module \流水中断  (
);

  wire AluSrcB, and_1_out, and_2_out, and_3_out, and_4_out, and_5_out, and_6_out, and_7_out, and_8_out,
       and_9_out, CLK, comparator_3_eq, \CPU中断Sig , d_ff_1_q, EQ, EQHalt, ERET, \ex_mem_1_eq输出 ,
       \ex_mem_1_传输状态out_表明当前传输数据有效 , Ex_MemToReg, Ex_RegWrite, Go, Halt, \id_ex_1_传输状态out_表明当前传输数据有效 , IE,
       \if_id_1_传输状态out_表明当前传输数据有效 , INT_q, IR1, IR1Sig, IR2, IR2Sig, IR3, IR3Sig, JR, LH, \LoadUse相关 , LUI,
       Mem_MemToReg, Mem_RegWrite, mips_alu_1_equal, not_1_out, not_2_out, not_3_out, not_4_out, not_5_out,
       not_7_out, or_1_out, or_2_out, or_3_out, or_4_out, or_5_out, RST, Syscall, SyscallHalt, W1, W2, W3,
       WB_JAL, \中断Rst1 , \中断Rst2 , \中断Rst3 , \无条件分支 , \条件分支 , \解码信号 ;
  wire [1:0] Forward1, Forward2, multiplexer_13_out, \中断号 , \正在执行的中断程序 , \硬布线控制器_封装_1_controlsig_2 ;
  wire [2:0] \ex_mem_1_extins输出 , \id_ex_1_extins输出 , \拓展指令信号_1_lui ;
  wire [2:2] \mem_wb_1_extins输出 ;
  wire [3:0] ID_Forward;
  wire [4:0] Ex_WriteReg_num, \id_ex_1_shamt输出 , ID_R1_num, ID_R2_num, \mem_wb_1_w_输出 , Mem_WriteReg_num,
       multiplexer_7_out, \指令译码_1_rd , \指令译码_1_rs , \指令译码_1_rt , \指令译码_1_shamt ;
  wire [5:0] Func, Op;
  wire [15:0] \ex_mem_1_控制信号输出 , \id_ex_1_控制信号输出 , \LoadUse次数 , \mem_wb_1_控制信号输出 , \总周期数 , \指令译码_1_imm16 ,
       \插入气泡数 , \无条件分支数 , \条件分支成功数 , \硬布线控制器_封装_1_controlsig ;
  wire [25:0] \指令译码_1_imm26 ;
  wire [31:0] adder_1_out, adder_2_out, EPC, EPc_t, \ex_mem_1_ir输出 , \ex_mem_1_memdin输出 ,
       \ex_mem_1_pcnext输出 , EX_PC, EX_R1, EX_R2, \id_ex_1_imm16输出 , \id_ex_1_ir输出 , \id_ex_1_pcnext输出 ,
       \id_ex_1_pcnext输出_2 , ID_PC, \if_id_1_ir输出 , \if_id_1_pcnext输出 , IF_PC, immext_1_imm16out,
       immext_1_imm26out, LedData, \lh指令_1_dout , \lui指令_1_dout , MEM_AluR, MEM_PC, \mem_wb_1_ir输出 ,
       \mem_wb_1_mem输出 , mips_probe_1_p1, mips_probe_3_p3, mips_regifile_1_r1, mips_regifile_1_r2,
       multiplexer_1_out, multiplexer_2_out, multiplexer_5_out, multiplexer_6_out, multiplexer_8_out,
       multiplexer_9_out, multiplexer_11_out, ram_1_data, Redir_A, Redir_B, WB_AluR, WB_Mem, WB_PC,
       WB_PcNext, \中断程序地址 ;

  Button \u_总复位  (.out(RST));
  Button _1 (.out(IR1));
  Button _2 (.out(IR2));
  Button _3 (.out(IR3));
  Button \u_继续运行  (.out(Go));
  LED led_1 (.in(W1));
  LED led_2 (.in(W2));
  LED led_3 (.in(W3));
  Hex_Digit_Display hex_digit_display_1 (.value(LedData[31:28]));  // open: dp
  Hex_Digit_Display hex_digit_display_2 (.value(LedData[27:24]));  // open: dp
  Hex_Digit_Display hex_digit_display_3 (.value(LedData[23:20]));  // open: dp
  Hex_Digit_Display hex_digit_display_4 (.value(LedData[19:16]));  // open: dp
  Multiplexer #(.width(32), .enable("false")) multiplexer_1 (
    .in0(\id_ex_1_pcnext输出 ), .in1(EX_R1), .out(multiplexer_1_out), .sel(JR));
  Hex_Digit_Display hex_digit_display_5 (.value(LedData[11:8]));  // open: dp
  Hex_Digit_Display hex_digit_display_6 (.value(LedData[15:12]));  // open: dp
  \重定向检测  \u_重定向检测_1  (
    .OP(Op), .EX_WriteReg_num(Ex_WriteReg_num), .EX_RegWrite(Ex_RegWrite), .Load_use(\LoadUse相关 ),
    .ID_R1_num(ID_R1_num), .MEM_RegWrite(Mem_RegWrite), .forwardR1(ID_Forward[1:0]), .Func(Func),
    .ID_R2_num(ID_R2_num), .EX_MemToReg(Ex_MemToReg), .forwardR2(ID_Forward[3:2]),
    .MEM_W_num(Mem_WriteReg_num), .MEM_MemToReg(Mem_MemToReg));
  Multiplexer #(.select(2), .width(32), .enable("false")) multiplexer_2 (
    .in0(adder_1_out), .in1(adder_2_out), .in2(multiplexer_1_out), .out(multiplexer_2_out),
    .sel({\id_ex_1_控制信号输出 [8], \条件分支 }));  // open: in3
  Hex_Digit_Display hex_digit_display_7 (.value(LedData[3:0]));  // open: dp
  Hex_Digit_Display hex_digit_display_8 (.value(LedData[7:4]));  // open: dp
  Clock clock_1 (.out(CLK));
  // Probe on Forward1
  Multiplexer #(.select(2), .width(32), .enable("false")) multiplexer_3 (
    .in0(EX_R1), .in1(WB_Mem), .in2(WB_AluR), .in3(MEM_AluR), .out(Redir_A), .sel(Forward1));
  // Probe on Forward2
  Multiplexer #(.select(2), .width(32), .enable("false")) multiplexer_4 (
    .in0(EX_R2), .in1(WB_Mem), .in2(WB_AluR), .in3(MEM_AluR), .out(Redir_B), .sel(Forward2));
  Multiplexer #(.width(32), .enable("false")) multiplexer_5 (
    .in0(multiplexer_2_out), .in1(\中断程序地址 ), .out(multiplexer_5_out), .sel(\CPU中断Sig ));
  Multiplexer #(.width(32), .enable("false")) multiplexer_6 (
    .in0(multiplexer_5_out), .in1(EPc_t), .out(multiplexer_6_out), .sel(ERET));
  Register #(.width(32)) PC (.D(multiplexer_6_out), .en(and_1_out), .Q(IF_PC), .clk(CLK), .clr(RST));
  and and_1 (and_1_out, Halt, not_1_out);
  not not_1 (not_1_out, \LoadUse相关 );
  // Probe on \总周期数 
  // Probe on \无条件分支数 
  // Probe on \条件分支成功数 
  // Probe on \插入气泡数 
  // Probe on \LoadUse次数 
  Adder #(.width(32)) adder_1 (.a(32'h1), .b(IF_PC), .out(adder_1_out));  // open: cin, cout
  // MIPS_Probe mips_probe_1: pin names not known; wires that end beside it: mips_probe_1_p1
  // Probe on IF_PC[11:0]
  or or_1 (or_1_out, RST, \条件分支 , ERET, \id_ex_1_控制信号输出 [8], \CPU中断Sig );
  IF_ID if_id_1 (
    .IR(mips_probe_1_p1), .\IR输出 (\if_id_1_ir输出 ), .PC(IF_PC), .\PC输出 (ID_PC), .\传输状态In_表明当前传输数据有效 (1'b1),
    .\传输状态Out_表明当前传输数据有效 (\if_id_1_传输状态out_表明当前传输数据有效 ), .CLK(CLK), .\同步清零_气泡_高电平有效 (or_1_out),
    .\使能端_低电平有效_stall_高电平有效 (\LoadUse相关 ), .PcNext(adder_1_out), .\PcNext输出 (\if_id_1_pcnext输出 ));  // open: Hit, Hit输出
  ROM #(.addrWidth(10), .dataWidth(32)) rom_1 (.addr(IF_PC[9:0]), .data(mips_probe_1_p1));  // open: sel
  // Probe on ID_PC[11:0]
  // Probe on EX_PC[11:0]
  // Probe on MEM_PC[11:0]
  \指令译码  \u_指令译码_1  (
    .Op(Op), .Imm16(\指令译码_1_imm16 ), .Func(Func), .Rs(\指令译码_1_rs ), .Instruction(\if_id_1_ir输出 ),
    .Rt(\指令译码_1_rt ), .Imm26(\指令译码_1_imm26 ), .Rd(\指令译码_1_rd ), .shamt(\指令译码_1_shamt ));
  ImmExt immext_1 (
    .Imm16(\指令译码_1_imm16 ), .Imm26(\指令译码_1_imm26 ), .Imm16Out(immext_1_imm16out),
    .Imm26Out(immext_1_imm26out), .SignedExt(\硬布线控制器_封装_1_controlsig [10]));
  // Probe on WB_PC[11:0]
  \硬布线控制器_封装  \u_硬布线控制器_封装_1  (
    .OP(Op), .Func(Func),
    .ControlSig({\硬布线控制器_封装_1_controlsig [15:8], \硬布线控制器_封装_1_controlsig_2 [0], \硬布线控制器_封装_1_controlsig_2 [1], \硬布线控制器_封装_1_controlsig [5:0]}));
  // MIPS_Probe mips_probe_2: pin names not known; wires that end beside it: \if_id_1_ir输出 
  Multiplexer #(.select(2), .width(5), .enable("false")) multiplexer_7 (
    .in0(\指令译码_1_rt ), .in1(\指令译码_1_rd ), .in2({5{1'b1}}), .in3({5{1'b1}}), .out(multiplexer_7_out),
    .sel(\硬布线控制器_封装_1_controlsig_2 ));
  \拓展指令信号  \u_拓展指令信号_1  (
    .OP0(Op[0]), .OP1(Op[1]), .OP2(Op[2]), .OP3(Op[3]), .OP4(Op[4]), .OP5(Op[5]), .F0(Func[0]), .F1(Func[1]),
    .F2(Func[2]), .F3(Func[3]), .F4(Func[4]), .F5(Func[5]), .LUI(\拓展指令信号_1_lui [0]), .LH(\拓展指令信号_1_lui [1]),
    .BLTZ(\拓展指令信号_1_lui [2]));
  SelReg selreg_1 (
    .in_1(\硬布线控制器_封装_1_controlsig [11]), .Rs(\指令译码_1_rs ), .Rt(\指令译码_1_rt ), .R1_num(ID_R1_num),
    .R2_num(ID_R2_num));
  or or_2 (or_2_out, RST, ERET, \CPU中断Sig );
  MIPS_Regifile mips_regifile_1 (
    .Din(\lui指令_1_dout ), .Clk(CLK), .R1(mips_regifile_1_r1), .R2(mips_regifile_1_r2),
    .WE(\mem_wb_1_控制信号输出 [5]), .W_num(\mem_wb_1_w_输出 ), .R1_num(ID_R1_num), .R2_num(ID_R2_num));
  Counter #(.width(16), .max('hffff)) counter_1 (
    .count(and_2_out), .Q(\条件分支成功数 ), .clk(CLK), .clr(RST));  // open: load, D, carry
  and and_2 (and_2_out, Halt, \条件分支 );
  Counter #(.width(16), .max('hffff)) counter_2 (
    .count(and_3_out), .Q(\无条件分支数 ), .clk(CLK), .clr(RST));  // open: load, D, carry
  and and_3 (and_3_out, Halt, \无条件分支 );
  or or_3 (or_3_out, or_2_out, \条件分支 , \id_ex_1_控制信号输出 [8], \LoadUse相关 );
  ID_EX id_ex_1 (
    .PC(ID_PC), .\PC输出 (EX_PC), .\传输状态In_表明当前传输数据有效 (\if_id_1_传输状态out_表明当前传输数据有效 ),
    .\传输状态Out_表明当前传输数据有效 (\id_ex_1_传输状态out_表明当前传输数据有效 ), .CLK(CLK), .\同步清零_气泡_高电平有效 (or_3_out),
    .\使能端_低电平有效_stall_高电平有效 (not_2_out), .IR(\if_id_1_ir输出 ), .\IR输出 (\id_ex_1_ir输出 ),
    .\控制信号 ({\硬布线控制器_封装_1_controlsig [15:8], \硬布线控制器_封装_1_controlsig_2 [0], \硬布线控制器_封装_1_controlsig_2 [1], \硬布线控制器_封装_1_controlsig [5:0]}),
    .\控制信号输出 ({\id_ex_1_控制信号输出 [15:12], Syscall, \id_ex_1_控制信号输出 [10], JR, \id_ex_1_控制信号输出 [8:6], Ex_RegWrite, AluSrcB, \id_ex_1_控制信号输出 [3], Ex_MemToReg, \id_ex_1_控制信号输出 [1:0]}),
    .Imm16(immext_1_imm16out), .\Imm16输出 (\id_ex_1_imm16输出 ), .R1(mips_regifile_1_r1), .\R1输出 (EX_R1),
    .\R2输出 (EX_R2), .R2(mips_regifile_1_r2), .shamt(\指令译码_1_shamt ), .\shamt输出 (\id_ex_1_shamt输出 ),
    .W_num(multiplexer_7_out), .\W_输出 (Ex_WriteReg_num), .PcNext(\if_id_1_pcnext输出 ),
    .\PcNext输出_2 (\id_ex_1_pcnext输出_2 ), .Imm26(immext_1_imm26out), .\PcNext输出 (\id_ex_1_pcnext输出 ),
    .Forward(ID_Forward), .\Forward输出 ({Forward2, Forward1}), .ExtIns(\拓展指令信号_1_lui ),
    .\ExtIns输出 (\id_ex_1_extins输出 ));  // open: Hit, Hit输出
  not not_2 (not_2_out, Halt);
  Adder #(.width(32)) adder_2 (.a(\id_ex_1_imm16输出 ), .b(\id_ex_1_pcnext输出_2 ), .out(adder_2_out));  // open: cin, cout
  // MIPS_Probe mips_probe_3: pin names not known; wires that end beside it: \id_ex_1_ir输出 , Redir_A, mips_probe_3_p3
  Multiplexer #(.width(32), .enable("false")) multiplexer_8 (
    .in0(Redir_B), .in1(\id_ex_1_imm16输出 ), .out(multiplexer_8_out), .sel(AluSrcB));
  // Probe on \lui指令_1_dout 
  not not_3 (not_3_out, mips_alu_1_equal);
  MIPS_ALU mips_alu_1 (
    .X(Redir_A), .Y(multiplexer_8_out), .AluOP(\id_ex_1_控制信号输出 [15:12]), .Equal(mips_alu_1_equal),
    .Result(mips_probe_3_p3), .shamt(\id_ex_1_shamt输出 ));  // open: Result_2
  Multiplexer #(.width(32), .enable("false")) multiplexer_9 (
    .in0(mips_probe_3_p3), .in1({\id_ex_1_imm16输出 [15:0], {16{1'b0}}}), .out(multiplexer_9_out),
    .sel(\id_ex_1_extins输出 [0]));
  Comparator #(.width(32), .mode("unsigned")) comparator_1 (.a(Redir_A), .b(32'h22), .eq(EQ));  // open: gt, lt
  Register #(.width(32)) register_1 (.D(Redir_B), .en(and_4_out), .Q(LedData), .clk(CLK));  // open: clr
  and and_4 (and_4_out, EQ, Syscall);
  and and_5 (and_5_out, mips_alu_1_equal, \id_ex_1_控制信号输出 [0]);
  or or_4 (or_4_out, and_5_out, and_6_out);
  and and_6 (and_6_out, not_3_out, \id_ex_1_控制信号输出 [1]);
  and and_7 (and_7_out, \id_ex_1_extins输出 [2], multiplexer_9_out[0]);
  or or_5 (or_5_out, RST, ERET, \CPU中断Sig );
  EX_MEM ex_mem_1 (
    .\控制信号 ({\id_ex_1_控制信号输出 [15:12], Syscall, \id_ex_1_控制信号输出 [10], JR, \id_ex_1_控制信号输出 [8:6], Ex_RegWrite, AluSrcB, \id_ex_1_控制信号输出 [3], Ex_MemToReg, \id_ex_1_控制信号输出 [1:0]}),
    .\控制信号输出 ({\ex_mem_1_控制信号输出 [15:6], Mem_RegWrite, \ex_mem_1_控制信号输出 [4:3], Mem_MemToReg, \ex_mem_1_控制信号输出 [1:0]}),
    .AluR(multiplexer_9_out), .\AluR输出 (MEM_AluR), .IR(\id_ex_1_ir输出 ), .\IR输出 (\ex_mem_1_ir输出 ), .PC(EX_PC),
    .\PC输出 (MEM_PC), .\传输状态In_表明当前传输数据有效 (\id_ex_1_传输状态out_表明当前传输数据有效 ),
    .\传输状态Out_表明当前传输数据有效 (\ex_mem_1_传输状态out_表明当前传输数据有效 ), .CLK(CLK), .\同步清零_气泡_高电平有效 (or_5_out),
    .\使能端_低电平有效_stall_高电平有效 (not_4_out), .MemDin(Redir_B), .\MemDin输出 (\ex_mem_1_memdin输出 ),
    .W_num(Ex_WriteReg_num), .\W_输出 (Mem_WriteReg_num), .PcNext(\id_ex_1_pcnext输出_2 ),
    .\PcNext输出 (\ex_mem_1_pcnext输出 ), .EQ(EQ), .\EQ输出 (\ex_mem_1_eq输出 ), .ExtIns(\id_ex_1_extins输出 ),
    .\ExtIns输出 (\ex_mem_1_extins输出 ));
  not not_4 (not_4_out, Halt);
  not not_5 (not_5_out, EQHalt);
  and and_8 (and_8_out, not_5_out, SyscallHalt);
  or or_6 (\条件分支 , or_4_out, and_7_out);
  // MIPS_Probe mips_probe_4: pin names not known; wires that end beside it: \ex_mem_1_ir输出 
  and and_9 (and_9_out, Halt, \LoadUse相关 );
  Counter #(.width(16), .max('hffff)) counter_3 (
    .count(Halt), .Q(\总周期数 ), .clk(CLK), .clr(RST));  // open: load, D, carry
  Counter #(.width(16), .max('hffff)) counter_4 (
    .count(and_9_out), .Q(\LoadUse次数 ), .clk(CLK), .clr(RST));  // open: load, D, carry
  not not_6 (Halt, d_ff_1_q);
  D_Flip_Flop #(.trigger("high")) d_ff_1 (
    .clk(CLK), .D(and_8_out), .Q(d_ff_1_q), .en(SyscallHalt), .reset(Go));  // open: Qn, preset
  RAM #(.addrWidth(10), .dataWidth(32), .bus("separate")) ram_1 (
    .addr(MEM_AluR[11:2]), .din(\ex_mem_1_memdin输出 ), .data(ram_1_data), .str(\ex_mem_1_控制信号输出 [3]),
    .clk(CLK), .clr(RST));  // open: sel, ld
  MEM_WB mem_wb_1 (
    .\控制信号 ({\ex_mem_1_控制信号输出 [15:6], Mem_RegWrite, \ex_mem_1_控制信号输出 [4:3], Mem_MemToReg, \ex_mem_1_控制信号输出 [1:0]}),
    .\控制信号输出 ({\mem_wb_1_控制信号输出 [15:12], SyscallHalt, \mem_wb_1_控制信号输出 [10:9], \无条件分支 , \mem_wb_1_控制信号输出 [7], WB_JAL, \mem_wb_1_控制信号输出 [5:0]}),
    .Mem(ram_1_data), .\Mem输出 (\mem_wb_1_mem输出 ), .Alu(MEM_AluR), .\Alu输出 (WB_AluR), .IR(\ex_mem_1_ir输出 ),
    .\IR输出 (\mem_wb_1_ir输出 ), .PC(MEM_PC), .\PC输出 (WB_PC),
    .\传输状态In_表明当前传输数据有效 (\ex_mem_1_传输状态out_表明当前传输数据有效 ), .CLK(CLK), .\同步清零_气泡_高电平有效 (RST),
    .\使能端_低电平有效_stall_高电平有效 (not_7_out), .W_num(Mem_WriteReg_num), .\W_输出 (\mem_wb_1_w_输出 ),
    .PcNext(\ex_mem_1_pcnext输出 ), .\PcNext输出 (WB_PcNext), .EQ(\ex_mem_1_eq输出 ), .EQ_2(EQHalt),
    .ExtIns(\ex_mem_1_extins输出 ), .\ExtIns输出 ({\mem_wb_1_extins输出 [2], LH, LUI}));  // open: 传输状态Out_表明当前传输数据有效, v0, v0输出
  not not_7 (not_7_out, Halt);
  Multiplexer #(.width(32), .enable("false")) multiplexer_10 (
    .in0(\mem_wb_1_mem输出 ), .in1(\lh指令_1_dout ), .out(WB_Mem), .sel(LH));
  Priority_Encoder #(.select(2)) priority_encoder_1 (
    .in0(IR1Sig), .in1(IR2Sig), .in2(IR3Sig), .in3(1'b0), .out(\中断号 ), .gs(\解码信号 ), .en_in(1'b1));  // open: en_out
  // MIPS_Probe mips_probe_5: pin names not known; wires that end beside it: \mem_wb_1_ir输出 
  Multiplexer #(.width(32), .enable("false")) multiplexer_11 (
    .in0(WB_AluR), .in1(\mem_wb_1_mem输出 ), .out(multiplexer_11_out), .sel(\mem_wb_1_控制信号输出 [2]));
  and and_10 (\CPU中断Sig , \解码信号 , IE);
  \LH指令  \lh指令_1  (.Dout(\lh指令_1_dout ), .Din(multiplexer_11_out), .LH(LH), .SEL(WB_AluR[1]));
  \LUI指令  \lui指令_1  (
    .Imm16(\mem_wb_1_ir输出 [15:0]), .Dout(\lui指令_1_dout ), .Din(\lh指令_1_dout ), .PcNext(WB_PcNext),
    .JAL(WB_JAL), .LUI(LUI));
  Register #(.width(2)) INTNUM (.D(\中断号 ), .en(\CPU中断Sig ), .Q(\正在执行的中断程序 ), .clk(CLK));  // open: clr
  Register #(.width(1)) INT (.D(\CPU中断Sig ), .en(\CPU中断Sig ), .Q(INT_q), .clk(CLK), .clr(ERET));
  D_Flip_Flop u_IE (.clk(CLK), .D(1'b1), .Q(IE), .reset(INT_q));  // open: Qn, preset, en
  Register #(.width(32)) u_EPC (.D(WB_PC), .en(\CPU中断Sig ), .Q(EPC), .clk(CLK), .clr(RST));
  \中断按键采样电路  \u_中断按键采样电路_1  (.CLK(CLK), .\中断信号 (IR1), .\和中断屏蔽位与 (IR1Sig), .\同步清零信号 (\中断Rst1 ), .\中断等待指示灯 (W1));
  \中断按键采样电路  \u_中断按键采样电路_2  (.CLK(CLK), .\中断信号 (IR2), .\和中断屏蔽位与 (IR2Sig), .\同步清零信号 (\中断Rst2 ), .\中断等待指示灯 (W2));
  \中断按键采样电路  \u_中断按键采样电路_3  (.CLK(CLK), .\中断信号 (IR3), .\和中断屏蔽位与 (IR3Sig), .\同步清零信号 (\中断Rst3 ), .\中断等待指示灯 (W3));
  Comparator #(.width(32)) comparator_2 (.a(\mem_wb_1_ir输出 ), .b(32'h42000018), .eq(ERET));  // open: gt, lt
  Multiplexer #(.select(2), .width(32), .enable("false")) multiplexer_12 (
    .in0(32'h9), .in1(32'h34), .in2(32'h5f), .out(\中断程序地址 ), .sel(\中断号 ));  // open: in3
  Demultiplexer #(.select(2), .enable("false")) demultiplexer_1 (
    .out0(\中断Rst1 ), .out1(\中断Rst2 ), .out2(\中断Rst3 ), .in(ERET), .sel(multiplexer_13_out));  // open: out3
  Multiplexer #(.width(2), .enable("false")) multiplexer_13 (
    .in0(2'b11), .in1(\正在执行的中断程序 ), .out(multiplexer_13_out), .sel(\解码信号 ));
  Comparator #(.width(32)) comparator_3 (.a(EPC), .b({32{1'b0}}), .eq(comparator_3_eq));  // open: gt, lt
  Multiplexer #(.width(32), .enable("false")) multiplexer_14 (
    .in0(EPC), .in1(32'h5), .out(EPc_t), .sel(comparator_3_eq));

  // Other names for the same wires on the sheet: v0[31:0] = Redir_B

  // Notes on the sheet:
  //   中断源
  //   0:Beq
  //   1:Bne
  //   2:MemToReg
  //   3:MemWrite
  //   4:AluSrcB
  //   5:RegWrite
  //   6:JAL
  //   7:RegDst
  //   8:JMP
  //   9:JR
  //   10:SignedExt
  //   11:Syscall
  //   12-15:AluOp
  //   中断等待指示
  //   数码管输出
  //   指令存储器
  //   contents of rom_1 (hex, n*v repeats v):
  //   20110001 8100005 20110001 20120002 20130003 8100009 20110001 20120002 20130003 810000d 20110001
  //   20120002 20130003 8100011 20110001 20120002 20130003 c1000fc 20100001 20110001 118fc0 112020
  //   20020022 c 118882 12200001 8100015 112020 20020022 c 20110001 118880 112020 20020022 c 12200001
  //   810001f 20110001 118fc0 112020 20020022 c 1188c3 112020 20020022 c 118903 112020 20020022 c 118903
  //   112020 20020022 c 118903 112020 20020022 c 118903 112020 20020022 c 118903 112020 20020022 c 118903
  //   112020 20020022 c 118903 112020 20020022 c 20100001 109fc0 139fc3 8021 2012000c 24160003 26100001
  //   3210000f 20080008 20090001 139900 2709825 132020 20020022 c 1094022 1500fff9 22100001 2018000f
  //   2188024 108700 20080008 20090001 139902 2709825 132021 20020022 c 1094022 1500fff9 108702 2c9b022
  //   12c00001 8100050 4020 1084027 84400 3508ffff 82021 20020022 c 2010ffff 20110000 ae300000 22100001
  //   22310004 ae300000 22100001 22310004 ae300000 22100001 22310004 ae300000 22100001 22310004 ae300000
  //   22100001 22310004 ae300000 22100001 22310004 ae300000 22100001 22310004 ae300000 22100001 22310004
  //   ae300000 22100001 22310004 ae300000 22100001 22310004 ae300000 22100001 22310004 ae300000 22100001
  //   22310004 ae300000 22100001 22310004 ae300000 22100001 22310004 ae300000 22100001 22310004 ae300000
  //   22100001 22310004 22100001 8020 2011003c 8e130000 8e340000 274402a 11000002 ae330000 ae140000
  //   2231fffc 1611fff8 102020 20020022 c 22100004 2011003c 1611fff2 20020032 c 2008ffff 20117777 112020
  //   20020022 c 200b0010 2288826 112020 20020022 c 216bffff 1560fffa 2002000a c 200b0008 3c11fedc
  //   3631ffff 112020 20020022 c 3c11ba98 112020 c 3c117654 112020 c 3c113210 112020 c 216bffff 1560fff0
  //   2002000a c 0 0 0 20090000 200b0010 34118483 20120404 118c00 129400 36318281 22520404 ad310000
  //   2328820 21290004 216bffff 1560fffb 200b0020 20090000 85310000 112020 20020022 c 21290002 216bffff
  //   1560fff9 2002000a c 2011fff1 112020 20020022 c 22310001 620fffb 2002000a c 20100000 22100001 102020
  //   20020022 c 22100002 102020 20020022 c 22100003 102020 20020022 c 22100004 102020 20020022 c 22100005
  //   102020 20020022 c 22100006 102020 20020022 c 22100007 102020 20020022 c 22100008 102020 20020022
  //   20020022 c 3e00008
  //   流水调试日志用
  //   SignedExt
  //   JAL
  //   RegDst
  //   Syscall
  //   RegWrite
  //   无条件分支
  //   JAL
  //   AlcSrcB
  //   BNE+BEQ
  //   BLTZ
  //   MemWrite
endmodule

module \_28条多级中断  (
);

  wire and_1_out, and_2_out, and_3_out, and_4_out, and_5_out, and_6_out, and_7_out, and_8_out, and_10_out,
       BLTZ, CLK, comparator_5_lt, \CPU中断Sig , d_ff_1_q, decoder_1_out0, decoder_1_out1, decoder_1_out2, EQ,
       ERET, Go, Halt, IE, INT_q, IR1, IR1Sig, IR2, IR2Sig, IR3, IR3Sig, JAL, LH, LUI, MFC0,
       mips_alu_1_equal, MTC0, not_1_out, not_2_out, or_2_out, or_3_out, or_4_out, or_5_out, or_6_out,
       or_7_out, RST, SignedExt, Syscall, undriven, W1, W2, W3, \中断Rst1 , \中断Rst2 , \中断Rst3 ,
       \中断按键采样电路_4_和中断屏蔽位与 , \无条件分支 , \条件分支 , \硬布线控制器_1_alu_src , \硬布线控制器_1_beq , \硬布线控制器_1_bne ,
       \硬布线控制器_1_jr , \硬布线控制器_1_memtoreg , \硬布线控制器_1_memwrite , \硬布线控制器_1_regdst , \硬布线控制器_1_regwrite ,
       \解码信号 ;
  wire [1:0] multiplexer_15_out, multiplexer_16_out, multiplexer_18_out, priority_encoder_2_out, \中断号 ,
       \正在执行的中断程序 ;
  wire [3:0] \硬布线控制器_1_alu_op ;
  wire [4:0] multiplexer_5_out, multiplexer_8_out, multiplexer_9_out, multiplexer_10_out;
  wire [15:0] \总周期数 , \无条件分支数 , \条件分支成功数 ;
  wire [31:0] adder_1_out, adder_2_out, bit_extender_1_out, bit_extender_2_out, bit_extender_3_out,
       bit_extender_4_out, EPC, Instruction, LedData, mips_alu_1_result, mips_regifile_1_r1,
       multiplexer_1_out, multiplexer_2_out, multiplexer_3_out, multiplexer_4_out, multiplexer_6_out,
       multiplexer_7_out, multiplexer_11_out, multiplexer_12_out, multiplexer_13_out, multiplexer_14_out, PC,
       R2, ram_1_data, \中断程序地址 ;

  Multiplexer #(.width(32), .enable("false")) multiplexer_1 (
    .in0(bit_extender_1_out), .in1(mips_regifile_1_r1), .out(multiplexer_1_out), .sel(\硬布线控制器_1_jr ));
  or or_1 (\条件分支 , and_7_out, and_8_out, and_6_out);
  Button \u_总复位  (.out(RST));
  Button \u_继续运行  (.out(Go));
  Clock clock_1 (.out(CLK));
  Multiplexer #(.select(2), .width(32), .enable("false")) multiplexer_2 (
    .in0(adder_1_out), .in1(adder_2_out), .in2(multiplexer_1_out), .out(multiplexer_2_out),
    .sel({\无条件分支 , \条件分支 }));  // open: in3
  Multiplexer #(.width(32), .enable("false")) multiplexer_3 (
    .in0(multiplexer_2_out), .in1(\中断程序地址 ), .out(multiplexer_3_out), .sel(\CPU中断Sig ));
  Hex_Digit_Display hex_digit_display_1 (.value(LedData[31:28]));  // open: dp
  Hex_Digit_Display hex_digit_display_2 (.value(LedData[27:24]));  // open: dp
  Multiplexer #(.width(32), .enable("false")) multiplexer_4 (
    .in0(multiplexer_3_out), .in1(EPC), .out(multiplexer_4_out), .sel(ERET));
  Hex_Digit_Display hex_digit_display_3 (.value(LedData[19:16]));  // open: dp
  Hex_Digit_Display hex_digit_display_4 (.value(LedData[23:20]));  // open: dp
  and and_1 (and_1_out, Halt, \无条件分支 );
  Register #(.width(32)) u_PC (.D(multiplexer_4_out), .en(Halt), .Q(PC), .clk(CLK), .clr(RST));
  Hex_Digit_Display hex_digit_display_5 (.value(LedData[15:12]));  // open: dp
  Hex_Digit_Display hex_digit_display_6 (.value(LedData[11:8]));  // open: dp
  Counter #(.width(16), .max('hffff)) counter_1 (
    .count(Halt), .Q(\总周期数 ), .clk(CLK), .clr(RST));  // open: load, D, carry
  Counter #(.width(16), .max('hffff)) counter_2 (
    .count(and_1_out), .Q(\无条件分支数 ), .clk(CLK), .clr(RST));  // open: load, D, carry
  Adder #(.width(32)) adder_1 (.a(PC), .b(32'h1), .out(adder_1_out));  // open: cin, cout
  Hex_Digit_Display hex_digit_display_7 (.value(LedData[3:0]));  // open: dp
  Hex_Digit_Display hex_digit_display_8 (.value(LedData[7:4]));  // open: dp
  ROM #(.addrWidth(10), .dataWidth(32)) rom_1 (.addr(PC[9:0]), .data(Instruction));  // open: sel
  assign bit_extender_1_out = {{6{Instruction[25]}}, Instruction[25:0]};  // Bit_Extender bit_extender_1
  // Probe on bit_extender_1_out
  Counter #(.width(16), .max('hffff)) counter_3 (
    .count(and_2_out), .Q(\条件分支成功数 ), .clk(CLK), .clr(RST));  // open: load, D, carry
  and and_2 (and_2_out, Halt, \条件分支 );
  and and_3 (and_3_out, Instruction[15], SignedExt);
  \cpu28__硬布线控制器  \u_硬布线控制器_1  (
    .Func(Instruction[5:0]), .OP(Instruction[31:26]), .ALU_OP(\硬布线控制器_1_alu_op ),
    .MemToReg(\硬布线控制器_1_memtoreg ), .MemWrite(\硬布线控制器_1_memwrite ), .ALU_SRC(\硬布线控制器_1_alu_src ),
    .RegWrite(\硬布线控制器_1_regwrite ), .SysCALL(Syscall), .SignedExt(SignedExt), .RegDst(\硬布线控制器_1_regdst ),
    .JR(\硬布线控制器_1_jr ), .JMP(\无条件分支 ), .Beq(\硬布线控制器_1_beq ), .JAL(JAL), .Bne(\硬布线控制器_1_bne ), .LUI(LUI),
    .LH(LH), .BLTZ(BLTZ));
  Multiplexer #(.width(5), .enable("false")) multiplexer_5 (
    .in0(Instruction[20:16]), .in1(Instruction[15:11]), .out(multiplexer_5_out), .sel(\硬布线控制器_1_regdst ));
  Multiplexer #(.select(2), .width(32), .enable("false")) multiplexer_6 (
    .in0(multiplexer_7_out), .in1(adder_1_out), .in2({Instruction[15:0], {16{1'b0}}}),
    .out(multiplexer_6_out), .sel({LUI, JAL}));  // open: in3
  assign bit_extender_2_out = {{16{and_3_out}}, Instruction[15:0]};  // Bit_Extender bit_extender_2
  Multiplexer #(.width(32), .enable("false")) multiplexer_7 (
    .in0(multiplexer_12_out), .in1(EPC), .out(multiplexer_7_out), .sel(MFC0));
  // Probe on \总周期数 
  // Probe on \无条件分支数 
  // Probe on \条件分支成功数 
  Register #(.width(32)) register_1 (.D(R2), .en(and_4_out), .Q(LedData), .clk(CLK));  // open: clr
  and and_4 (and_4_out, EQ, Syscall);
  Multiplexer #(.width(5), .enable("false")) multiplexer_8 (
    .in0(Instruction[25:21]), .in1(5'b00010), .out(multiplexer_8_out), .sel(Syscall));
  Multiplexer #(.width(5), .enable("false")) multiplexer_9 (
    .in0(Instruction[20:16]), .in1(5'b00100), .out(multiplexer_9_out), .sel(Syscall));
  Multiplexer #(.width(5), .enable("false")) multiplexer_10 (
    .in0(multiplexer_5_out), .in1({5{1'b1}}), .out(multiplexer_10_out), .sel(JAL));
  Button _1 (.out(IR1));
  Button _2 (.out(IR2));
  Button _3 (.out(IR3));
  or or_2 (or_2_out, \硬布线控制器_1_regwrite , MFC0);
  LED led_1 (.in(W1));
  LED led_2 (.in(W2));
  LED led_3 (.in(W3));
  MIPS_Regifile mips_regifile_1 (
    .Din(multiplexer_6_out), .Clk(CLK), .R1(mips_regifile_1_r1), .R2(R2), .WE(or_2_out),
    .W_num(multiplexer_10_out), .R1_num(multiplexer_8_out), .R2_num(multiplexer_9_out));
  not not_1 (not_1_out, EQ);
  Comparator #(.width(32), .mode("unsigned")) comparator_1 (
    .a(32'h22), .b(mips_regifile_1_r1), .eq(EQ));  // open: gt, lt
  Multiplexer #(.width(32), .enable("false")) multiplexer_11 (
    .in0(R2), .in1(bit_extender_2_out), .out(multiplexer_11_out), .sel(\硬布线控制器_1_alu_src ));
  and and_5 (and_5_out, not_1_out, Syscall);
  MIPS_ALU mips_alu_1 (
    .X(mips_regifile_1_r1), .Y(multiplexer_11_out), .AluOP(\硬布线控制器_1_alu_op ), .Equal(mips_alu_1_equal),
    .Result(mips_alu_1_result), .shamt(Instruction[10:6]));  // open: Result_2
  Adder #(.width(32)) adder_2 (.a(bit_extender_2_out), .b(adder_1_out), .out(adder_2_out));  // open: cin, cout
  D_Flip_Flop #(.trigger("high")) d_ff_1 (
    .clk(CLK), .D(and_5_out), .Q(d_ff_1_q), .en(Syscall), .reset(Go));  // open: Qn, preset
  and and_6 (and_6_out, mips_alu_1_equal, \硬布线控制器_1_beq );
  not not_2 (not_2_out, mips_alu_1_equal);
  and and_7 (and_7_out, not_2_out, \硬布线控制器_1_bne );
  Priority_Encoder #(.select(2)) priority_encoder_1 (
    .in0(IR1Sig), .in1(IR2Sig), .in2(IR3Sig), .in3(1'b0), .out(\中断号 ), .gs(\解码信号 ), .en_in(1'b1));  // open: en_out
  not not_3 (Halt, d_ff_1_q);
  and and_8 (and_8_out, BLTZ, mips_alu_1_result[0]);
  Multiplexer #(.select(2), .width(32), .enable("false")) multiplexer_12 (
    .in0(multiplexer_14_out), .in1(multiplexer_14_out), .in2(bit_extender_3_out), .in3(bit_extender_4_out),
    .out(multiplexer_12_out), .sel({LH, mips_alu_1_result[1]}));
  and and_9 (\CPU中断Sig , \解码信号 , IE);
  Multiplexer #(.width(32), .enable("false")) multiplexer_13 (.in0(PC), .in1(R2), .out(multiplexer_13_out), .sel(MTC0));
  RAM #(.addrWidth(10), .dataWidth(32), .bus("separate")) ram_1 (
    .addr(mips_alu_1_result[11:2]), .din(R2), .data(ram_1_data), .str(\硬布线控制器_1_memwrite ), .clk(CLK),
    .ld(\硬布线控制器_1_memtoreg ), .clr(RST));  // open: sel
  or or_3 (or_3_out, \CPU中断Sig , MTC0);
  Multiplexer #(.width(32), .enable("false")) multiplexer_14 (
    .in0(mips_alu_1_result), .in1(ram_1_data), .out(multiplexer_14_out), .sel(\硬布线控制器_1_memtoreg ));
  Register #(.width(2)) INTNUM (.D(\中断号 ), .en(\CPU中断Sig ), .Q(\正在执行的中断程序 ), .clk(CLK));  // open: clr
  Register #(.width(1)) INT (.D(\CPU中断Sig ), .en(\CPU中断Sig ), .Q(INT_q), .clk(CLK), .clr(or_4_out));
  D_Flip_Flop u_IE (.clk(CLK), .D(1'b1), .Q(IE), .reset(INT_q));  // open: Qn, preset, en
  Register #(.width(32)) u_EPC (.D(multiplexer_13_out), .en(or_3_out), .Q(EPC), .clk(CLK), .clr(RST));
  \中断按键采样电路  \u_中断按键采样电路_1  (.CLK(CLK), .\中断信号 (IR1), .\同步清零信号 (\中断Rst1 ), .\中断等待指示灯 (W1));  // open: 和中断屏蔽位与
  \中断按键采样电路  \u_中断按键采样电路_2  (.CLK(CLK), .\中断信号 (IR2), .\同步清零信号 (\中断Rst2 ), .\中断等待指示灯 (W2));  // open: 和中断屏蔽位与
  \中断按键采样电路  \u_中断按键采样电路_3  (.CLK(CLK), .\中断信号 (IR3), .\同步清零信号 (\中断Rst3 ), .\中断等待指示灯 (W3));  // open: 和中断屏蔽位与
  or or_4 (or_4_out, ERET, and_10_out);
  assign bit_extender_3_out = {{16{multiplexer_14_out[15]}}, multiplexer_14_out[15:0]};  // Bit_Extender bit_extender_3
  assign bit_extender_4_out = {{16{multiplexer_14_out[31]}}, multiplexer_14_out[31:16]};  // Bit_Extender bit_extender_4
  Demultiplexer #(.select(2), .enable("false")) demultiplexer_1 (
    .out1(\中断Rst1 ), .out2(\中断Rst2 ), .out3(\中断Rst3 ), .in(ERET), .sel(multiplexer_15_out));  // open: out0
  Multiplexer #(.width(2), .enable("false")) multiplexer_15 (
    .in0(priority_encoder_2_out), .in1(2'b00), .out(multiplexer_15_out), .sel(undriven));
  Priority_Encoder #(.select(2)) priority_encoder_2 (
    .in1(W1), .in2(W2), .in3(W3), .out(priority_encoder_2_out));  // open: in0
  and and_10 (and_10_out, comparator_5_lt, ~IE);  // AND_Gate
  Comparator #(.width(32)) comparator_2 (.a(Instruction), .b(32'h42000018), .eq(ERET));  // open: gt, lt
  Comparator #(.width(11)) comparator_3 (.a(Instruction[31:21]), .b(11'h200), .eq(MFC0));  // open: gt, lt
  Comparator #(.width(11)) comparator_4 (.a(Instruction[31:21]), .b(11'h204), .eq(MTC0));  // open: gt, lt
  Multiplexer #(.width(2), .enable("false")) multiplexer_16 (
    .in0(2'b00), .in1(\中断号 ), .out(multiplexer_16_out), .sel(\解码信号 ));
  Multiplexer #(.select(2), .width(32), .enable("false")) multiplexer_17 (
    .in0(32'hc), .in1(32'h3d), .in2(32'h6e), .out(\中断程序地址 ), .sel(\中断号 ));  // open: in3
  Comparator #(.width(2), .mode("unsigned")) comparator_5 (
    .a(\正在执行的中断程序 ), .b(multiplexer_16_out), .lt(comparator_5_lt));  // open: gt, eq
  \中断按键采样电路  \u_中断按键采样电路_4  (
    .CLK(CLK), .\中断信号 (IR1), .\和中断屏蔽位与 (\中断按键采样电路_4_和中断屏蔽位与 ), .\同步清零信号 (or_5_out));  // open: 中断等待指示灯
  or or_5 (or_5_out, decoder_1_out0, \中断Rst1 );
  \中断按键采样电路  \u_中断按键采样电路_5  (.CLK(CLK), .\中断信号 (IR2), .\和中断屏蔽位与 (IR2Sig), .\同步清零信号 (or_6_out));  // open: 中断等待指示灯
  or or_6 (or_6_out, decoder_1_out1, \中断Rst2 );
  \中断按键采样电路  \u_中断按键采样电路_6  (.CLK(CLK), .\中断信号 (IR3), .\和中断屏蔽位与 (IR3Sig), .\同步清零信号 (or_7_out));  // open: 中断等待指示灯
  and and_11 (IR1Sig, ~W2, ~W3, \中断按键采样电路_4_和中断屏蔽位与 );  // AND_Gate
  or or_7 (or_7_out, decoder_1_out2, \中断Rst3 );
  Decoder #(.select(2), .enable("false")) decoder_1 (
    .out0(decoder_1_out0), .out1(decoder_1_out1), .out2(decoder_1_out2), .sel(multiplexer_18_out));  // open: out3
  Multiplexer #(.width(2), .enable("false")) multiplexer_18 (
    .in0(2'b11), .in1(\正在执行的中断程序 ), .out(multiplexer_18_out), .sel(\解码信号 ));

  // Other names for the same wires on the sheet: v0[31:0] = R2

  // Notes on the sheet:
  //   数码管输出应该用寄存器锁存，否则显示数据只能一闪而过
  //   可以通过项目增加Logisim库的方式将前几次实验完成的电路作为子电路引入到本电路中使用
  //   数码管输出
  //   指令存储器
  //   contents of rom_1 (hex, n*v repeats v):
  //   20110001 8100005 20110001 20120002 20130003 8100009 20110001 20120002 20130003 810000d 20110001
  //   20120002 20130003 8100011 20110001 20120002 20130003 c1000fc 20100001 20110001 118fc0 112020
  //   20020022 c 118882 12200001 8100015 112020 20020022 c 20110001 118880 112020 20020022 c 12200001
  //   810001f 20110001 118fc0 112020 20020022 c 1188c3 112020 20020022 c 118903 112020 20020022 c 118903
  //   112020 20020022 c 118903 112020 20020022 c 118903 112020 20020022 c 118903 112020 20020022 c 118903
  //   112020 20020022 c 118903 112020 20020022 c 20100001 109fc0 139fc3 8021 2012000c 24160003 26100001
  //   3210000f 20080008 20090001 139900 2709825 132020 20020022 c 1094022 1500fff9 22100001 2018000f
  //   2188024 108700 20080008 20090001 139902 2709825 132021 20020022 c 1094022 1500fff9 108702 2c9b022
  //   12c00001 8100050 4020 1084027 84400 3508ffff 82021 20020022 c 2010ffff 20110000 ae300000 22100001
  //   22310004 ae300000 22100001 22310004 ae300000 22100001 22310004 ae300000 22100001 22310004 ae300000
  //   22100001 22310004 ae300000 22100001 22310004 ae300000 22100001 22310004 ae300000 22100001 22310004
  //   ae300000 22100001 22310004 ae300000 22100001 22310004 ae300000 22100001 22310004 ae300000 22100001
  //   22310004 ae300000 22100001 22310004 ae300000 22100001 22310004 ae300000 22100001 22310004 ae300000
  //   22100001 22310004 22100001 8020 2011003c 8e130000 8e340000 274402a 11000002 ae330000 ae140000
  //   2231fffc 1611fff8 102020 20020022 c 22100004 2011003c 1611fff2 20020032 c 2008ffff 20117777 112020
  //   20020022 c 200b0010 2288826 112020 20020022 c 216bffff 1560fffa 2002000a c 200b0008 3c11fedc
  //   3631ffff 112020 20020022 c 3c11ba98 112020 c 3c117654 112020 c 3c113210 112020 c 216bffff 1560fff0
  //   2002000a c 0 0 0 20090000 200b0010 34118483 20120404 118c00 129400 36318281 22520404 ad310000
  //   2328820 21290004 216bffff 1560fffb 200b0020 20090000 85310000 112020 20020022 c 21290002 216bffff
  //   1560fff9 2002000a c 2011fff1 112020 20020022 c 22310001 620fffb 2002000a c 20100000 22100001 102020
  //   20020022 c 22100002 102020 20020022 c 22100003 102020 20020022 c 22100004 102020 20020022 c 22100005
  //   102020 20020022 c 22100006 102020 20020022 c 22100007 102020 20020022 c 22100008 102020 20020022
  //   20020022 c 3e00008
  //   JMP
  //   JR
  //   Op
  //   Func
  //   总复位信号应将除ROM以外所有存储组件全部清零
  //   Beq
  //   JAL
  //   rs
  //   rt
  //   rd
  //   Bne
  //   MemToReg
  //   MemWrite
  //   AluOP
  //   AluSrcB
  //   RegWrite
  //   RegDst
  //   v0
  //   a0
  //   中断源
  //   中断等待指示
endmodule
